// Logisim project 8Bit_ALU.circ as structural Verilog: 3 circuits, main circuit main
module main (
  input  A8,
  input  A4,
  input  A2,
  input  A1,
  input  B8,
  input  B4,
  input  B2,
  input  B1,
  input  in_9,
  input  in_10,
  input  A128,
  input  A64,
  input  A32,
  input  A16,
  input  B128,
  input  B64,
  input  B32,
  input  B16,
  input  in_19,
  output O8,
  output O4,
  output O2,
  output O1,
  output O128,
  output O64,
  output O32,
  output O16,
  output O256
);

  wire asu_sub_1_c16;

  ASU_SUB asu_sub_1 (
    .A8(A8), .A4(A4), .A2(A2), .A1(A1), .B8(B8), .B4(B4), .B2(B2), .B1(B1), .C_in(in_9), .MODE(in_10),
    .O8(O8), .O4(O4), .O2(O2), .O1(O1), .C16(asu_sub_1_c16));
  ASU_SUB asu_sub_2 (
    .A8(A128), .A4(A64), .A2(A32), .A1(A16), .B8(B128), .B4(B64), .B2(B32), .B1(B16), .C_in(asu_sub_1_c16),
    .MODE(in_19), .O8(O128), .O4(O64), .O2(O32), .O1(O16), .C16(O256));
endmodule

module ASU_SUB (
  input  A8,
  input  A4,
  input  A2,
  input  A1,
  input  B8,
  input  B4,
  input  B2,
  input  B1,
  input  C_in,
  input  MODE,
  output O8,
  output O4,
  output O2,
  output O1,
  output C16
);

  wire fulladder_sub_1_carry, fulladder_sub_2_carry, fulladder_sub_3_carry, or_1_out, xor_1_out, xor_2_out,
       xor_3_out, xor_4_out;

  or or_1 (or_1_out, C_in, MODE);
  xor xor_1 (xor_1_out, B1, MODE);
  xor xor_2 (xor_2_out, B2, MODE);
  xor xor_3 (xor_3_out, B4, MODE);
  xor xor_4 (xor_4_out, B8, MODE);
  FullAdder_SUB fulladder_sub_1 (.A1(A1), .B1(xor_1_out), .C_in(or_1_out), .SUM(O1), .CARRY(fulladder_sub_1_carry));
  FullAdder_SUB fulladder_sub_2 (
    .A1(A2), .B1(xor_2_out), .C_in(fulladder_sub_1_carry), .SUM(O2), .CARRY(fulladder_sub_2_carry));
  FullAdder_SUB fulladder_sub_3 (
    .A1(A4), .B1(xor_3_out), .C_in(fulladder_sub_2_carry), .SUM(O4), .CARRY(fulladder_sub_3_carry));
  FullAdder_SUB fulladder_sub_4 (.A1(A8), .B1(xor_4_out), .C_in(fulladder_sub_3_carry), .SUM(O8), .CARRY(C16));

  // Notes on the sheet:
  //   A
  //   B
  //   0=Addition (A+B)
  //   1=Subtraction(A-B)
  //   2's Complement Step 2 Logic
  //   2's Complement Step 1 Logic
  //   4 BIT ADDITION SUBTRACTION UNIT
  //   ADDITION CASE=OVERFLOW(16)
  //   SUBTRACTION CASE= LED GLOW=ANSWER IS IN ITS TRUE FORM
  //   = LED DON'T GLOW= ANSWER IS IN 2'S COMPLEMENT FORM
  //   In case of Subtraction It also works as carry flag if LED glows then A>=B and if not A<B
endmodule

module FullAdder_SUB (
  input  A1,
  input  B1,
  input  C_in,
  output SUM,
  output CARRY
);

  wire and_1_out, and_2_out, and_3_out, or_1_out, xor_1_out;

  xor xor_1 (xor_1_out, A1, B1);
  xor xor_2 (SUM, xor_1_out, C_in);
  and and_1 (and_1_out, A1, C_in);
  and and_2 (and_2_out, A1, B1);
  and and_3 (and_3_out, B1, C_in);
  or or_1 (or_1_out, and_1_out, and_2_out);
  or or_2 (CARRY, or_1_out, and_3_out);

  // Notes on the sheet:
  //   FULL ADDER
endmodule
