// Logisim project 8Bit_ALU_GI.circ as structural Verilog: 5 circuits, main circuit main
module main (
  input  B128,
  input  B64,
  input  B32,
  input  B16,
  input  B8,
  input  B4,
  input  B2,
  input  B1,
  input  in_9,
  input  A128,
  input  A64,
  input  A32,
  input  A16,
  input  A8,
  input  A4,
  input  A2,
  input  A1,
  input  SUB_ENABLE,
  input  OUT_ENABLE,
  output O8,
  output O4,
  output O2,
  output O1,
  output O128,
  output O64,
  output O32,
  output O16,
  output O256
);

  wire asu_sub_1_c16, asu_sub_1_o1, asu_sub_1_o2, asu_sub_1_o4, asu_sub_1_o8, asu_sub_2_c16, asu_sub_2_o1,
       asu_sub_2_o2, asu_sub_2_o4, asu_sub_2_o8, binary2bcd_1_o1_1, binary2bcd_1_o1_2, binary2bcd_1_o1_4,
       binary2bcd_1_o1_8, binary2bcd_1_o2_1, binary2bcd_1_o2_2, binary2bcd_1_o2_4, binary2bcd_1_o2_8,
       binary2bcd_1_o3_1, binary2bcd_1_o3_2, binary2bcd_1_o3_4, binary2bcd_1_o3_8, segment_display_1_a,
       segment_display_1_b, segment_display_1_c, segment_display_1_d, segment_display_1_e,
       segment_display_1_f, segment_display_1_g, segment_display_2_a, segment_display_2_b,
       segment_display_2_c, segment_display_2_d, segment_display_2_e, segment_display_2_f,
       segment_display_2_g, segment_display_3_a, segment_display_3_b, segment_display_3_c,
       segment_display_3_d, segment_display_3_e, segment_display_3_f, segment_display_3_g;

  assign O8 = OUT_ENABLE ? asu_sub_1_o8 : 1'bz;  // Controlled_Buffer controlled_buffer_1
  ASU_SUB asu_sub_1 (
    .A8(A8), .A4(A4), .A2(A2), .A1(A1), .B8(B8), .B4(B4), .B2(B2), .B1(B1), .C_in(in_9), .MODE(SUB_ENABLE),
    .O8(asu_sub_1_o8), .O4(asu_sub_1_o4), .O2(asu_sub_1_o2), .O1(asu_sub_1_o1), .C16(asu_sub_1_c16));
  assign O4 = OUT_ENABLE ? asu_sub_1_o4 : 1'bz;  // Controlled_Buffer controlled_buffer_2
  assign O2 = OUT_ENABLE ? asu_sub_1_o2 : 1'bz;  // Controlled_Buffer controlled_buffer_3
  assign O1 = OUT_ENABLE ? asu_sub_1_o1 : 1'bz;  // Controlled_Buffer controlled_buffer_4
  assign O128 = OUT_ENABLE ? asu_sub_2_o8 : 1'bz;  // Controlled_Buffer controlled_buffer_5
  ASU_SUB asu_sub_2 (
    .A8(A128), .A4(A64), .A2(A32), .A1(A16), .B8(B128), .B4(B64), .B2(B32), .B1(B16), .C_in(asu_sub_1_c16),
    .MODE(SUB_ENABLE), .O8(asu_sub_2_o8), .O4(asu_sub_2_o4), .O2(asu_sub_2_o2), .O1(asu_sub_2_o1),
    .C16(asu_sub_2_c16));
  assign O64 = OUT_ENABLE ? asu_sub_2_o4 : 1'bz;  // Controlled_Buffer controlled_buffer_6
  assign O32 = OUT_ENABLE ? asu_sub_2_o2 : 1'bz;  // Controlled_Buffer controlled_buffer_7
  assign O16 = OUT_ENABLE ? asu_sub_2_o1 : 1'bz;  // Controlled_Buffer controlled_buffer_8
  assign O256 = OUT_ENABLE ? asu_sub_2_c16 : 1'bz;  // Controlled_Buffer controlled_buffer_9
  Binary2BCD binary2bcd_1 (
    .I128(O128), .I64(O64), .I32(O32), .I16(O16), .I8(O8), .I4(O4), .I2(O2), .I1(O1),
    .O1_8(binary2bcd_1_o1_8), .O1_4(binary2bcd_1_o1_4), .O1_2(binary2bcd_1_o1_2), .O1_1(binary2bcd_1_o1_1),
    .O2_8(binary2bcd_1_o2_8), .O2_4(binary2bcd_1_o2_4), .O2_2(binary2bcd_1_o2_2), .O2_1(binary2bcd_1_o2_1),
    .O3_8(binary2bcd_1_o3_8), .O3_4(binary2bcd_1_o3_4), .O3_2(binary2bcd_1_o3_2), .O3_1(binary2bcd_1_o3_1));
  Segment_Display segment_display_1 (
    .O8(binary2bcd_1_o1_8), .O4(binary2bcd_1_o1_4), .O2(binary2bcd_1_o1_2), .O1(binary2bcd_1_o1_1),
    .B(segment_display_1_b), .A(segment_display_1_a), .G(segment_display_1_g), .F(segment_display_1_f),
    .E(segment_display_1_e), .C(segment_display_1_c), .D(segment_display_1_d));
  Segment_Display segment_display_2 (
    .O8(binary2bcd_1_o2_8), .O4(binary2bcd_1_o2_4), .O2(binary2bcd_1_o2_2), .O1(binary2bcd_1_o2_1),
    .B(segment_display_2_b), .A(segment_display_2_a), .G(segment_display_2_g), .F(segment_display_2_f),
    .E(segment_display_2_e), .C(segment_display_2_c), .D(segment_display_2_d));
  Segment_Display segment_display_3 (
    .O8(binary2bcd_1_o3_8), .O4(binary2bcd_1_o3_4), .O2(binary2bcd_1_o3_2), .O1(binary2bcd_1_o3_1),
    .B(segment_display_3_b), .A(segment_display_3_a), .G(segment_display_3_g), .F(segment_display_3_f),
    .E(segment_display_3_e), .C(segment_display_3_c), .D(segment_display_3_d));
  _7_Segment_Display u_7_segment_display_1 (
    .g(segment_display_1_g), .f(segment_display_1_f), .a(segment_display_1_a), .b(segment_display_1_b),
    .e(segment_display_1_e), .d(segment_display_1_d), .c(segment_display_1_c));  // open: dp
  _7_Segment_Display u_7_segment_display_2 (
    .g(segment_display_2_g), .f(segment_display_2_f), .a(segment_display_2_a), .b(segment_display_2_b),
    .e(segment_display_2_e), .d(segment_display_2_d), .c(segment_display_2_c));  // open: dp
  _7_Segment_Display u_7_segment_display_3 (
    .g(segment_display_3_g), .f(segment_display_3_f), .a(segment_display_3_a), .b(segment_display_3_b),
    .e(segment_display_3_e), .d(segment_display_3_d), .c(segment_display_3_c));  // open: dp
endmodule

module ASU_SUB (
  input  A8,
  input  A4,
  input  A2,
  input  A1,
  input  B8,
  input  B4,
  input  B2,
  input  B1,
  input  C_in,
  input  MODE,
  output O8,
  output O4,
  output O2,
  output O1,
  output C16
);

  wire fulladder_sub_1_carry, fulladder_sub_2_carry, fulladder_sub_3_carry, or_1_out, xor_1_out, xor_2_out,
       xor_3_out, xor_4_out;

  or or_1 (or_1_out, C_in, MODE);
  xor xor_1 (xor_1_out, B1, MODE);
  xor xor_2 (xor_2_out, B2, MODE);
  xor xor_3 (xor_3_out, B4, MODE);
  xor xor_4 (xor_4_out, B8, MODE);
  FullAdder_SUB fulladder_sub_1 (.A1(A1), .B1(xor_1_out), .C_in(or_1_out), .SUM(O1), .CARRY(fulladder_sub_1_carry));
  FullAdder_SUB fulladder_sub_2 (
    .A1(A2), .B1(xor_2_out), .C_in(fulladder_sub_1_carry), .SUM(O2), .CARRY(fulladder_sub_2_carry));
  FullAdder_SUB fulladder_sub_3 (
    .A1(A4), .B1(xor_3_out), .C_in(fulladder_sub_2_carry), .SUM(O4), .CARRY(fulladder_sub_3_carry));
  FullAdder_SUB fulladder_sub_4 (.A1(A8), .B1(xor_4_out), .C_in(fulladder_sub_3_carry), .SUM(O8), .CARRY(C16));

  // Notes on the sheet:
  //   A
  //   B
  //   0=Addition (A+B)
  //   1=Subtraction(A-B)
  //   2's Complement Step 2 Logic
  //   2's Complement Step 1 Logic
  //   4 BIT ADDITION SUBTRACTION UNIT
  //   ADDITION CASE=OVERFLOW(16)
  //   SUBTRACTION CASE= LED GLOW=ANSWER IS IN ITS TRUE FORM
  //   = LED DON'T GLOW= ANSWER IS IN 2'S COMPLEMENT FORM
  //   In case of Subtraction It also works as carry flag if LED glows then A>=B and if not A<B
endmodule

module FullAdder_SUB (
  input  A1,
  input  B1,
  input  C_in,
  output SUM,
  output CARRY
);

  wire and_1_out, and_2_out, and_3_out, or_1_out, xor_1_out;

  xor xor_1 (xor_1_out, A1, B1);
  xor xor_2 (SUM, xor_1_out, C_in);
  and and_1 (and_1_out, A1, C_in);
  and and_2 (and_2_out, A1, B1);
  and and_3 (and_3_out, B1, C_in);
  or or_1 (or_1_out, and_1_out, and_2_out);
  or or_2 (CARRY, or_1_out, and_3_out);

  // Notes on the sheet:
  //   FULL ADDER
endmodule

module Binary2BCD (
  input  I128,
  input  I64,
  input  I32,
  input  I16,
  input  I8,
  input  I4,
  input  I2,
  input  I1,
  output O1_8,
  output O1_4,
  output O1_2,
  output O1_1,
  output O2_8,
  output O2_4,
  output O2_2,
  output O2_1,
  output O3_8,
  output O3_4,
  output O3_2,
  output O3_1
);

  wire and_1_out, and_2_out, and_3_out, and_4_out, and_5_out, and_6_out, and_7_out, nand_1_out, nand_2_out,
       nand_3_out, nand_4_out, nand_5_out, nand_6_out, nand_7_out, nand_8_out, nand_9_out, nand_10_out,
       nand_11_out, nand_12_out, nand_13_out, nand_14_out, nand_15_out, nand_19_out, nand_20_out,
       nand_21_out, nand_22_out, nand_23_out, nand_24_out, nand_25_out, nand_26_out, nand_27_out,
       nand_28_out, nand_29_out, nand_31_out, nand_32_out, nand_33_out, nand_34_out, nand_35_out,
       nand_36_out, nand_37_out, nand_38_out, nand_39_out, nand_40_out, nand_41_out, nand_42_out,
       nand_43_out, nand_44_out, nand_45_out, nand_46_out, nand_47_out, nand_48_out, nand_49_out,
       nand_51_out, nand_52_out, nand_53_out, nand_54_out, nand_55_out, nand_56_out, nand_57_out,
       nand_58_out, nand_59_out, nand_60_out, nand_61_out, nand_62_out, nand_63_out, nand_67_out,
       nand_68_out, nand_69_out, nor_1_out, nor_2_out, nor_3_out, nor_4_out, nor_5_out, nor_6_out, nor_7_out,
       nor_8_out, nor_9_out, nor_10_out, nor_11_out, nor_12_out, nor_13_out, nor_14_out, not_1_out,
       not_2_out, not_3_out, not_4_out, not_5_out, not_6_out, not_7_out, not_8_out, not_9_out, not_10_out,
       not_11_out, not_12_out, not_13_out, not_14_out, or_1_out, or_2_out, or_3_out, or_4_out, or_5_out,
       or_6_out, or_7_out, or_8_out, or_9_out, or_10_out, or_11_out, or_12_out, or_13_out, or_14_out,
       or_15_out, or_16_out, or_17_out, or_18_out, or_19_out, or_20_out, or_21_out, or_22_out, or_23_out,
       or_24_out, or_25_out, or_26_out, or_27_out, or_28_out;

  nand nand_1 (nand_1_out, 1'b0, I32);
  nor nor_1 (nor_1_out, I128, 1'b0);
  and and_1 (and_1_out, I64, I128);
  not not_1 (not_1_out, I32);
  not not_2 (not_2_out, I128);
  nand nand_2 (nand_2_out, nand_62_out, I4);
  nor nor_2 (nor_2_out, nand_61_out, nand_62_out);
  and and_2 (and_2_out, nand_60_out, nand_61_out);
  not not_3 (not_3_out, I4);
  not not_4 (not_4_out, nand_61_out);
  nand nand_3 (nand_3_out, nand_24_out, I2);
  nor nor_3 (nor_3_out, nand_23_out, nand_24_out);
  and and_3 (and_3_out, nand_22_out, nand_23_out);
  not not_5 (not_5_out, I2);
  not not_6 (not_6_out, nand_23_out);
  nand nand_4 (nand_4_out, I128, not_1_out);
  nand nand_5 (nand_5_out, I32, nor_1_out);
  nor nor_4 (nor_4_out, 1'b0, and_1_out);
  nand nand_6 (nand_6_out, not_1_out, 1'b0);
  or or_1 (or_1_out, I64, not_2_out);
  nand nand_7 (nand_7_out, nand_61_out, not_3_out);
  nand nand_8 (nand_8_out, I4, nor_2_out);
  nor nor_5 (nor_5_out, nand_62_out, and_2_out);
  nand nand_9 (nand_9_out, not_3_out, nand_62_out);
  or or_2 (or_2_out, nand_60_out, not_4_out);
  nand nand_10 (nand_10_out, nand_23_out, not_5_out);
  nand nand_11 (nand_11_out, I2, nor_3_out);
  nor nor_6 (nor_6_out, nand_24_out, and_3_out);
  nand nand_12 (nand_12_out, not_5_out, nand_24_out);
  or or_3 (or_3_out, nand_22_out, not_6_out);
  nand nand_13 (nand_13_out, nand_4_out, I64);
  or or_4 (or_4_out, nor_4_out, I32);
  or or_5 (or_5_out, or_1_out, I32);
  nand nand_14 (nand_14_out, nand_7_out, nand_60_out);
  or or_6 (or_6_out, nor_5_out, I4);
  or or_7 (or_7_out, or_2_out, I4);
  nand nand_15 (nand_15_out, nand_10_out, nand_22_out);
  or or_8 (or_8_out, nor_6_out, I2);
  or or_9 (or_9_out, or_3_out, I2);
  nand nand_16 (O3_2, nand_11_out, or_8_out);
  nand nand_17 (O3_4, nand_15_out, nand_12_out);
  nand nand_18 (O3_8, nand_3_out, or_9_out);
  nand nand_19 (nand_19_out, nand_5_out, or_4_out);
  nand nand_20 (nand_20_out, nand_13_out, nand_6_out);
  nand nand_21 (nand_21_out, nand_1_out, or_5_out);
  nand nand_22 (nand_22_out, nand_8_out, or_6_out);
  nand nand_23 (nand_23_out, nand_14_out, nand_9_out);
  nand nand_24 (nand_24_out, nand_2_out, or_7_out);
  or or_10 (or_10_out, nand_19_out, not_1_out);
  nand nand_25 (nand_25_out, nand_19_out, not_1_out);
  or or_11 (or_11_out, nand_22_out, not_3_out);
  nand nand_26 (nand_26_out, nand_22_out, not_3_out);
  or or_12 (or_12_out, O3_2, not_5_out);
  nand nand_27 (nand_27_out, O3_2, not_5_out);
  nand nand_28 (nand_28_out, or_10_out, nand_25_out);
  nand nand_29 (nand_29_out, or_11_out, nand_26_out);
  nand nand_30 (O2_1, or_12_out, nand_27_out);
  nand nand_31 (nand_31_out, nand_21_out, I16);
  nor nor_7 (nor_7_out, nand_20_out, nand_21_out);
  and and_4 (and_4_out, nand_19_out, nand_20_out);
  not not_7 (not_7_out, I16);
  not not_8 (not_8_out, nand_20_out);
  nand nand_32 (nand_32_out, 1'b0, nand_68_out);
  nor nor_8 (nor_8_out, nand_28_out, 1'b0);
  and and_5 (and_5_out, nand_48_out, nand_28_out);
  not not_9 (not_9_out, nand_68_out);
  not not_10 (not_10_out, nand_28_out);
  nand nand_33 (nand_33_out, nand_20_out, not_7_out);
  nand nand_34 (nand_34_out, I16, nor_7_out);
  nor nor_9 (nor_9_out, nand_21_out, and_4_out);
  nand nand_35 (nand_35_out, not_7_out, nand_21_out);
  or or_13 (or_13_out, nand_19_out, not_8_out);
  nand nand_36 (nand_36_out, nand_28_out, not_9_out);
  nand nand_37 (nand_37_out, nand_68_out, nor_8_out);
  nor nor_10 (nor_10_out, 1'b0, and_5_out);
  nand nand_38 (nand_38_out, not_9_out, 1'b0);
  or or_14 (or_14_out, nand_48_out, not_10_out);
  nand nand_39 (nand_39_out, nand_33_out, nand_19_out);
  or or_15 (or_15_out, nor_9_out, I16);
  or or_16 (or_16_out, or_13_out, I16);
  nand nand_40 (nand_40_out, nand_36_out, nand_48_out);
  or or_17 (or_17_out, nor_10_out, nand_68_out);
  or or_18 (or_18_out, or_14_out, nand_68_out);
  nand nand_41 (nand_41_out, nand_34_out, or_15_out);
  nand nand_42 (nand_42_out, nand_39_out, nand_35_out);
  nand nand_43 (nand_43_out, nand_31_out, or_16_out);
  nand nand_44 (nand_44_out, nand_37_out, or_17_out);
  nand nand_45 (nand_45_out, nand_40_out, nand_38_out);
  nand nand_46 (nand_46_out, nand_32_out, or_18_out);
  or or_19 (or_19_out, nand_41_out, not_7_out);
  nand nand_47 (nand_47_out, nand_41_out, not_7_out);
  nand nand_48 (nand_48_out, or_19_out, nand_47_out);
  or or_20 (or_20_out, nand_44_out, not_9_out);
  nand nand_49 (nand_49_out, nand_44_out, not_9_out);
  nand nand_50 (O1_2, or_20_out, nand_49_out);
  nand nand_51 (nand_51_out, nand_43_out, I8);
  nor nor_11 (nor_11_out, nand_42_out, nand_43_out);
  and and_6 (and_6_out, nand_41_out, nand_42_out);
  not not_11 (not_11_out, I8);
  not not_12 (not_12_out, nand_42_out);
  nand nand_52 (nand_52_out, nand_46_out, nand_29_out);
  nor nor_12 (nor_12_out, nand_45_out, nand_46_out);
  and and_7 (and_7_out, nand_44_out, nand_45_out);
  not not_13 (not_13_out, nand_29_out);
  not not_14 (not_14_out, nand_45_out);
  nand nand_53 (nand_53_out, nand_42_out, not_11_out);
  nand nand_54 (nand_54_out, I8, nor_11_out);
  nor nor_13 (nor_13_out, nand_43_out, and_6_out);
  nand nand_55 (nand_55_out, not_11_out, nand_43_out);
  or or_21 (or_21_out, nand_41_out, not_12_out);
  nand nand_56 (nand_56_out, nand_45_out, not_13_out);
  nand nand_57 (nand_57_out, nand_29_out, nor_12_out);
  nor nor_14 (nor_14_out, nand_46_out, and_7_out);
  nand nand_58 (nand_58_out, not_13_out, nand_46_out);
  or or_22 (or_22_out, nand_44_out, not_14_out);
  nand nand_59 (nand_59_out, nand_53_out, nand_41_out);
  or or_23 (or_23_out, nor_13_out, I8);
  or or_24 (or_24_out, or_21_out, I8);
  or or_25 (or_25_out, nor_14_out, nand_29_out);
  or or_26 (or_26_out, or_22_out, nand_29_out);
  nand nand_60 (nand_60_out, nand_54_out, or_23_out);
  nand nand_61 (nand_61_out, nand_59_out, nand_55_out);
  nand nand_62 (nand_62_out, nand_51_out, or_24_out);
  nand nand_63 (nand_63_out, nand_56_out, nand_44_out);
  nand nand_64 (O2_2, nand_57_out, or_25_out);
  nand nand_65 (O2_4, nand_63_out, nand_58_out);
  nand nand_66 (O2_8, nand_52_out, or_26_out);
  or or_27 (or_27_out, nand_60_out, not_11_out);
  nand nand_67 (nand_67_out, nand_60_out, not_11_out);
  or or_28 (or_28_out, O2_2, not_13_out);
  nand nand_68 (nand_68_out, or_27_out, nand_67_out);
  nand nand_69 (nand_69_out, O2_2, not_13_out);
  nand nand_70 (O1_1, or_28_out, nand_69_out);

  assign O3_1 = I1;

  // Notes on the sheet:
  //   DABBLER T
  //   DABBLER D
  //   DABBLER N
  //   D2
  //   T3
  //   T2
  //   T1
  //   T0
  //   D3
  //   D1
  //   D0
  //   N3
  //   N2
  //   N1
  //   N0
  //   DABBLER W
  //   DABBLER K
  //   W2
  //   W1
  //   W3
  //   W0
  //   K3
  //   K2
  //   K1
  //   K0
  //   DABBLER Z
  //   DABBLER M
  //   M1
  //   M0
  //   Z3
  //   Z2
  //   Z1
  //   Z0
  //   M3
  //   M2
endmodule

module Segment_Display (
  input  O8,
  input  O4,
  input  O2,
  input  O1,
  output B,
  output A,
  output G,
  output F,
  output E,
  output C,
  output D
);

  wire and_1_out, and_2_out, and_3_out, nand_1_out, nand_2_out, nand_3_out, nand_5_out, nor_1_out, nor_2_out,
       nor_3_out, not_1_out, not_3_out, or_1_out, or_2_out, or_5_out, or_6_out;

  nor nor_1 (nor_1_out, O8, O2);
  not not_1 (not_1_out, O2);
  nand nand_1 (nand_1_out, O1, O2);
  nor nor_2 (nor_2_out, O1, O2);
  or or_1 (or_1_out, O1, nor_1_out);
  and and_1 (and_1_out, O4, nand_1_out);
  or or_2 (or_2_out, not_1_out, O4);
  nand nand_2 (nand_2_out, not_1_out, O4);
  not not_2 (E, or_1_out);
  or or_3 (F, O8, and_1_out);
  nor nor_3 (nor_3_out, nand_2_out, O1);
  and and_2 (and_2_out, O1, nand_2_out);
  not not_3 (not_3_out, F);
  nand nand_3 (nand_3_out, O1, F);
  or or_4 (C, F, and_2_out);
  or or_5 (or_5_out, F, nor_2_out);
  and and_3 (and_3_out, nand_3_out, or_2_out);
  nand nand_4 (D, and_3_out, or_1_out);
  or or_6 (or_6_out, not_3_out, D);
  or or_7 (A, O2, D);
  or or_8 (G, D, nor_3_out);
  nand nand_5 (nand_5_out, or_6_out, or_5_out);
  or or_9 (B, O8, nand_5_out);
endmodule
