// Logisim project Address_Decode_Logic.circ as structural Verilog: 1 circuit, main circuit main
module main (
  input  A0,
  input  A1,
  input  A2,
  input  A3,
  output CELL_0,
  output CELL_1,
  output CELL_2,
  output CELL_3,
  output CELL_4,
  output CELL_5,
  output CELL_6,
  output CELL_7,
  output CELL_8,
  output CELL_9,
  output CELL_10,
  output CELL_11,
  output CELL_12,
  output CELL_13,
  output CELL_14,
  output CELL_15
);

  wire not_1_out, not_2_out, not_3_out, not_4_out;

  not not_1 (not_1_out, A0);
  not not_2 (not_2_out, A1);
  not not_3 (not_3_out, A2);
  not not_4 (not_4_out, A3);
  and and_1 (CELL_0, not_1_out, not_2_out, not_3_out, not_4_out);
  and and_2 (CELL_1, A0, not_2_out, not_3_out, not_4_out);
  and and_3 (CELL_2, not_1_out, A1, not_3_out, not_4_out);
  and and_4 (CELL_3, A0, A1, not_3_out, not_4_out);
  and and_5 (CELL_4, not_1_out, not_2_out, A2, not_4_out);
  and and_6 (CELL_5, A0, not_2_out, A2, not_4_out);
  and and_7 (CELL_6, not_1_out, A1, A2, not_4_out);
  and and_8 (CELL_7, A0, A1, A2, not_4_out);
  and and_9 (CELL_8, not_1_out, not_2_out, not_3_out, A3);
  and and_10 (CELL_9, A0, not_2_out, not_3_out, A3);
  and and_11 (CELL_10, not_1_out, A1, not_3_out, A3);
  and and_12 (CELL_11, A0, A1, not_3_out, A3);
  and and_13 (CELL_12, not_1_out, not_2_out, A2, A3);
  and and_14 (CELL_13, A0, not_2_out, A2, A3);
  and and_15 (CELL_14, not_1_out, A1, A2, A3);
  and and_16 (CELL_15, A0, A1, A2, A3);
endmodule
