// Logisim project Manually_Programmable_RAM.circ as structural Verilog: 3 circuits, main circuit main
module main (
  input  in_1,
  input  in_2,
  input  in_3,
  input  in_4,
  input  in_5,
  input  in_6,
  input  in_7,
  input  in_8,
  input  in_9,
  input  in_10,
  input  in_11,
  input  in_12,
  input  in_13,
  input  in_14,
  input  in_15,
  input  in_16,
  input  in_17,
  input  in_18,
  input  in_19,
  input  in_20,
  input  in_21,
  input  in_22,
  input  in_23,
  input  in_24
);

  wire address_decode_logic_1_cell_0_e, address_decode_logic_1_cell_0_w, address_decode_logic_1_cell_1_e,
       address_decode_logic_1_cell_1_w, address_decode_logic_1_cell_2_e, address_decode_logic_1_cell_2_w,
       address_decode_logic_1_cell_3_e, address_decode_logic_1_cell_3_w, address_decode_logic_1_cell_4_e,
       address_decode_logic_1_cell_4_w, address_decode_logic_1_cell_5_e, address_decode_logic_1_cell_5_w,
       address_decode_logic_1_cell_6_e, address_decode_logic_1_cell_6_w, address_decode_logic_1_cell_7_e,
       address_decode_logic_1_cell_8_e, address_decode_logic_1_cell_8_w, address_decode_logic_1_cell_9_e,
       address_decode_logic_1_cell_9_w, address_decode_logic_1_cell_10_e, address_decode_logic_1_cell_10_w,
       address_decode_logic_1_cell_11_e, address_decode_logic_1_cell_11_w, address_decode_logic_1_cell_12_e,
       address_decode_logic_1_cell_12_w, address_decode_logic_1_cell_13_e, address_decode_logic_1_cell_13_w,
       address_decode_logic_1_cell_14_e, address_decode_logic_1_cell_14_w, address_decode_logic_1_cell_15_e,
       address_decode_logic_1_cell_15_w, C0_clk, C0_v1, C0_v2, C0_v3, C0_v4, C0_v5, C0_v6, C0_v7, C0_v8,
       C1_clk, C1_v1, C1_v2, C1_v3, C1_v4, C1_v5, C1_v6, C1_v7, C1_v8, C2_clk, C2_v1, C2_v2, C2_v3, C2_v4,
       C2_v5, C2_v6, C2_v7, C2_v8, C3_clk, C3_v1, C3_v2, C3_v3, C3_v4, C3_v5, C3_v6, C3_v7, C3_v8, C4_clk,
       C4_v1, C4_v2, C4_v3, C4_v4, C4_v5, C4_v6, C4_v7, C4_v8, C5_clk, C5_v1, C5_v2, C5_v3, C5_v4, C5_v5,
       C5_v6, C5_v7, C5_v8, C6_clk, C6_o7, C6_v1, C6_v2, C6_v3, C6_v4, C6_v5, C6_v6, C6_v7, C6_v8, C7_clk,
       C7_v1, C7_v2, C7_v3, C7_v4, C7_v5, C7_v6, C7_v7, C7_v8, C8_clk, C8_v1, C8_v2, C8_v3, C8_v4, C8_v5,
       C8_v6, C8_v7, C8_v8, C9_clk, C9_v1, C9_v2, C9_v3, C9_v4, C9_v5, C9_v6, C9_v7, C9_v8, C10_clk, C10_v1,
       C10_v2, C10_v3, C10_v4, C10_v5, C10_v6, C10_v7, C10_v8, C11_clk, C11_v1, C11_v2, C11_v3, C11_v4,
       C11_v5, C11_v6, C11_v7, C11_v8, C12_clk, C12_v1, C12_v2, C12_v3, C12_v4, C12_v5, C12_v6, C12_v7,
       C12_v8, C13_clk, C13_v1, C13_v2, C13_v3, C13_v4, C13_v5, C13_v6, C13_v7, C13_v8, C14_clk, C14_v1,
       C14_v2, C14_v3, C14_v4, C14_v5, C14_v6, C14_v7, C14_v8, C15_clk, C15_v1, C15_v2, C15_v3, C15_v4,
       C15_v5, C15_v6, C15_v7, C15_v8, controlled_buffer_1_out, controlled_buffer_2_out,
       controlled_buffer_3_out, controlled_buffer_4_out, controlled_buffer_5_out, controlled_buffer_6_out,
       controlled_buffer_7_out, controlled_buffer_8_out;

  Address_Decode_Logic address_decode_logic_1 (
    .A0(in_19), .A1(in_20), .A2(in_21), .A3(in_22), .OUT_CONTROL(in_23), .E0W1(in_24),
    .CELL_0_E(address_decode_logic_1_cell_0_e), .CELL_0_W(address_decode_logic_1_cell_0_w),
    .CELL_1_E(address_decode_logic_1_cell_1_e), .CELL_1_W(address_decode_logic_1_cell_1_w),
    .CELL_2_E(address_decode_logic_1_cell_2_e), .CELL_2_W(address_decode_logic_1_cell_2_w),
    .CELL_3_E(address_decode_logic_1_cell_3_e), .CELL_3_W(address_decode_logic_1_cell_3_w),
    .CELL_4_E(address_decode_logic_1_cell_4_e), .CELL_4_W(address_decode_logic_1_cell_4_w),
    .CELL_5_E(address_decode_logic_1_cell_5_e), .CELL_5_W(address_decode_logic_1_cell_5_w),
    .CELL_6_E(address_decode_logic_1_cell_6_e), .CELL_6_W(address_decode_logic_1_cell_6_w),
    .CELL_7_E(address_decode_logic_1_cell_7_e), .CELL_7_W(address_decode_logic_1_cell_7_e),
    .CELL_8_E(address_decode_logic_1_cell_8_e), .CELL_8_W(address_decode_logic_1_cell_8_w),
    .CELL_9_E(address_decode_logic_1_cell_9_e), .CELL_9_W(address_decode_logic_1_cell_9_w),
    .CELL_10_E(address_decode_logic_1_cell_10_e), .CELL_10_W(address_decode_logic_1_cell_10_w),
    .CELL_11_E(address_decode_logic_1_cell_11_e), .CELL_11_W(address_decode_logic_1_cell_11_w),
    .CELL_12_E(address_decode_logic_1_cell_12_e), .CELL_12_W(address_decode_logic_1_cell_12_w),
    .CELL_13_E(address_decode_logic_1_cell_13_e), .CELL_13_W(address_decode_logic_1_cell_13_w),
    .CELL_14_E(address_decode_logic_1_cell_14_e), .CELL_14_W(address_decode_logic_1_cell_14_w),
    .CELL_15_E(address_decode_logic_1_cell_15_e), .CELL_15_W(address_decode_logic_1_cell_15_w));
  assign controlled_buffer_1_out = in_9 ? in_1 : 1'bz;  // Controlled_Buffer controlled_buffer_1
  assign controlled_buffer_2_out = in_9 ? in_2 : 1'bz;  // Controlled_Buffer controlled_buffer_2
  assign controlled_buffer_3_out = in_9 ? in_3 : 1'bz;  // Controlled_Buffer controlled_buffer_3
  assign controlled_buffer_4_out = in_9 ? in_4 : 1'bz;  // Controlled_Buffer controlled_buffer_4
  assign controlled_buffer_5_out = in_9 ? in_5 : 1'bz;  // Controlled_Buffer controlled_buffer_5
  assign controlled_buffer_6_out = in_9 ? in_6 : 1'bz;  // Controlled_Buffer controlled_buffer_6
  assign controlled_buffer_7_out = in_9 ? in_7 : 1'bz;  // Controlled_Buffer controlled_buffer_7
  assign controlled_buffer_8_out = in_9 ? in_8 : 1'bz;  // Controlled_Buffer controlled_buffer_8
  assign controlled_buffer_1_out = in_18 ? in_10 : 1'bz;  // Controlled_Buffer controlled_buffer_9
  assign controlled_buffer_2_out = in_18 ? in_11 : 1'bz;  // Controlled_Buffer controlled_buffer_10
  assign controlled_buffer_3_out = in_18 ? in_12 : 1'bz;  // Controlled_Buffer controlled_buffer_11
  assign controlled_buffer_4_out = in_18 ? in_13 : 1'bz;  // Controlled_Buffer controlled_buffer_12
  assign controlled_buffer_5_out = in_18 ? in_14 : 1'bz;  // Controlled_Buffer controlled_buffer_13
  assign controlled_buffer_6_out = in_18 ? in_15 : 1'bz;  // Controlled_Buffer controlled_buffer_14
  assign controlled_buffer_7_out = in_18 ? in_16 : 1'bz;  // Controlled_Buffer controlled_buffer_15
  assign controlled_buffer_8_out = in_18 ? in_17 : 1'bz;  // Controlled_Buffer controlled_buffer_16
  LED led_1 (.in(C0_v1));
  Byte_Memory_Module C0 (
    .D1(controlled_buffer_1_out), .D2(controlled_buffer_2_out), .D3(controlled_buffer_3_out),
    .D4(controlled_buffer_4_out), .D5(controlled_buffer_5_out), .D6(controlled_buffer_6_out),
    .D7(controlled_buffer_7_out), .D8(controlled_buffer_8_out), .WR(address_decode_logic_1_cell_0_w),
    .EN(address_decode_logic_1_cell_0_e), .V1(C0_v1), .V2(C0_v2), .V3(C0_v3), .V4(C0_v4), .V5(C0_v5),
    .V6(C0_v6), .V7(C0_v7), .V8(C0_v8), .CLK(C0_clk), .O8(controlled_buffer_8_out),
    .O1(controlled_buffer_1_out), .O2(controlled_buffer_2_out), .O3(controlled_buffer_3_out),
    .O4(controlled_buffer_4_out), .O5(controlled_buffer_5_out), .O6(controlled_buffer_6_out),
    .O7(controlled_buffer_7_out));  // open: RESET
  LED led_2 (.in(C0_v2));
  LED led_3 (.in(C0_v3));
  LED led_4 (.in(C0_v4));
  LED led_5 (.in(C0_v5));
  LED led_6 (.in(C0_v6));
  LED led_7 (.in(C0_v7));
  LED led_8 (.in(C0_v8));
  LED led_9 (.in(C0_clk));
  LED led_10 (.in(C4_v1));
  Byte_Memory_Module C4 (
    .D1(controlled_buffer_1_out), .D2(controlled_buffer_2_out), .D3(controlled_buffer_3_out),
    .D4(controlled_buffer_4_out), .D5(controlled_buffer_5_out), .D6(controlled_buffer_6_out),
    .D7(controlled_buffer_7_out), .D8(controlled_buffer_8_out), .WR(address_decode_logic_1_cell_4_w),
    .EN(address_decode_logic_1_cell_4_e), .V1(C4_v1), .V2(C4_v2), .V3(C4_v3), .V4(C4_v4), .V5(C4_v5),
    .V6(C4_v6), .V7(C4_v7), .V8(C4_v8), .CLK(C4_clk), .O8(controlled_buffer_8_out),
    .O1(controlled_buffer_1_out), .O2(controlled_buffer_2_out), .O3(controlled_buffer_3_out),
    .O4(controlled_buffer_4_out), .O5(controlled_buffer_5_out), .O6(controlled_buffer_6_out),
    .O7(controlled_buffer_7_out));  // open: RESET
  LED led_11 (.in(C4_v2));
  LED led_12 (.in(C4_v3));
  LED led_13 (.in(C4_v4));
  LED led_14 (.in(C4_v5));
  LED led_15 (.in(C4_v6));
  LED led_16 (.in(C4_v7));
  LED led_17 (.in(C4_v8));
  LED led_18 (.in(C4_clk));
  LED led_19 (.in(C8_v1));
  Byte_Memory_Module C8 (
    .D1(controlled_buffer_1_out), .D2(controlled_buffer_2_out), .D3(controlled_buffer_3_out),
    .D4(controlled_buffer_4_out), .D5(controlled_buffer_5_out), .D6(controlled_buffer_6_out),
    .D7(controlled_buffer_7_out), .D8(controlled_buffer_8_out), .WR(address_decode_logic_1_cell_8_w),
    .EN(address_decode_logic_1_cell_8_e), .V1(C8_v1), .V2(C8_v2), .V3(C8_v3), .V4(C8_v4), .V5(C8_v5),
    .V6(C8_v6), .V7(C8_v7), .V8(C8_v8), .CLK(C8_clk), .O8(controlled_buffer_8_out),
    .O1(controlled_buffer_1_out), .O2(controlled_buffer_2_out), .O3(controlled_buffer_3_out),
    .O4(controlled_buffer_4_out), .O5(controlled_buffer_5_out), .O6(controlled_buffer_6_out),
    .O7(controlled_buffer_7_out));  // open: RESET
  LED led_20 (.in(C8_v2));
  LED led_21 (.in(C8_v3));
  LED led_22 (.in(C8_v4));
  LED led_23 (.in(C8_v5));
  LED led_24 (.in(C8_v6));
  LED led_25 (.in(C8_v7));
  LED led_26 (.in(C8_v8));
  LED led_27 (.in(C8_clk));
  LED led_28 (.in(C12_v1));
  Byte_Memory_Module C12 (
    .D1(controlled_buffer_1_out), .D2(controlled_buffer_2_out), .D3(controlled_buffer_3_out),
    .D4(controlled_buffer_4_out), .D5(controlled_buffer_5_out), .D6(controlled_buffer_6_out),
    .D7(controlled_buffer_7_out), .D8(controlled_buffer_8_out), .WR(address_decode_logic_1_cell_12_w),
    .EN(address_decode_logic_1_cell_12_e), .V1(C12_v1), .V2(C12_v2), .V3(C12_v3), .V4(C12_v4), .V5(C12_v5),
    .V6(C12_v6), .V7(C12_v7), .V8(C12_v8), .CLK(C12_clk), .O8(controlled_buffer_8_out),
    .O1(controlled_buffer_1_out), .O2(controlled_buffer_2_out), .O3(controlled_buffer_3_out),
    .O4(controlled_buffer_4_out), .O5(controlled_buffer_5_out), .O6(controlled_buffer_6_out),
    .O7(controlled_buffer_7_out));  // open: RESET
  LED led_29 (.in(C12_v2));
  LED led_30 (.in(C12_v3));
  LED led_31 (.in(C12_v4));
  LED led_32 (.in(C12_v5));
  LED led_33 (.in(C12_v6));
  LED led_34 (.in(C12_v7));
  LED led_35 (.in(C12_v8));
  LED led_36 (.in(C12_clk));
  LED led_37 (.in(C1_v1));
  Byte_Memory_Module C1 (
    .D1(controlled_buffer_1_out), .D2(controlled_buffer_2_out), .D3(controlled_buffer_3_out),
    .D4(controlled_buffer_4_out), .D5(controlled_buffer_5_out), .D6(controlled_buffer_6_out),
    .D7(controlled_buffer_7_out), .D8(controlled_buffer_8_out), .WR(address_decode_logic_1_cell_1_w),
    .EN(address_decode_logic_1_cell_1_e), .V1(C1_v1), .V2(C1_v2), .V3(C1_v3), .V4(C1_v4), .V5(C1_v5),
    .V6(C1_v6), .V7(C1_v7), .V8(C1_v8), .CLK(C1_clk), .O8(controlled_buffer_8_out),
    .O1(controlled_buffer_1_out), .O2(controlled_buffer_2_out), .O3(controlled_buffer_3_out),
    .O4(controlled_buffer_4_out), .O5(controlled_buffer_5_out), .O6(controlled_buffer_6_out),
    .O7(controlled_buffer_7_out));  // open: RESET
  LED led_38 (.in(C1_v2));
  LED led_39 (.in(C1_v3));
  LED led_40 (.in(C1_v4));
  LED led_41 (.in(C1_v5));
  LED led_42 (.in(C1_v6));
  LED led_43 (.in(C1_v7));
  LED led_44 (.in(C1_v8));
  LED led_45 (.in(C1_clk));
  LED led_46 (.in(C5_v1));
  Byte_Memory_Module C5 (
    .D1(controlled_buffer_1_out), .D2(controlled_buffer_2_out), .D3(controlled_buffer_3_out),
    .D4(controlled_buffer_4_out), .D5(controlled_buffer_5_out), .D6(controlled_buffer_6_out),
    .D7(controlled_buffer_7_out), .D8(controlled_buffer_8_out), .WR(address_decode_logic_1_cell_5_w),
    .EN(address_decode_logic_1_cell_5_e), .V1(C5_v1), .V2(C5_v2), .V3(C5_v3), .V4(C5_v4), .V5(C5_v5),
    .V6(C5_v6), .V7(C5_v7), .V8(C5_v8), .CLK(C5_clk), .O8(controlled_buffer_8_out),
    .O1(controlled_buffer_1_out), .O2(controlled_buffer_2_out), .O3(controlled_buffer_3_out),
    .O4(controlled_buffer_4_out), .O5(controlled_buffer_5_out), .O6(controlled_buffer_6_out),
    .O7(controlled_buffer_7_out));  // open: RESET
  LED led_47 (.in(C5_v2));
  LED led_48 (.in(C5_v3));
  LED led_49 (.in(C5_v4));
  LED led_50 (.in(C5_v5));
  LED led_51 (.in(C5_v6));
  LED led_52 (.in(C5_v7));
  LED led_53 (.in(C5_v8));
  LED led_54 (.in(C5_clk));
  LED led_55 (.in(C9_v1));
  Byte_Memory_Module C9 (
    .D1(controlled_buffer_1_out), .D2(controlled_buffer_2_out), .D3(controlled_buffer_3_out),
    .D4(controlled_buffer_4_out), .D5(controlled_buffer_5_out), .D6(controlled_buffer_6_out),
    .D7(controlled_buffer_7_out), .D8(controlled_buffer_8_out), .WR(address_decode_logic_1_cell_9_w),
    .EN(address_decode_logic_1_cell_9_e), .V1(C9_v1), .V2(C9_v2), .V3(C9_v3), .V4(C9_v4), .V5(C9_v5),
    .V6(C9_v6), .V7(C9_v7), .V8(C9_v8), .CLK(C9_clk), .O8(controlled_buffer_8_out),
    .O1(controlled_buffer_1_out), .O2(controlled_buffer_2_out), .O3(controlled_buffer_3_out),
    .O4(controlled_buffer_4_out), .O5(controlled_buffer_5_out), .O6(controlled_buffer_6_out),
    .O7(controlled_buffer_7_out));  // open: RESET
  LED led_56 (.in(C9_v2));
  LED led_57 (.in(C9_v3));
  LED led_58 (.in(C9_v4));
  LED led_59 (.in(C9_v5));
  LED led_60 (.in(C9_v6));
  LED led_61 (.in(C9_v7));
  LED led_62 (.in(C9_v8));
  LED led_63 (.in(C9_clk));
  LED led_64 (.in(C13_v1));
  Byte_Memory_Module C13 (
    .D1(controlled_buffer_1_out), .D2(controlled_buffer_2_out), .D3(controlled_buffer_3_out),
    .D4(controlled_buffer_4_out), .D5(controlled_buffer_5_out), .D6(controlled_buffer_6_out),
    .D7(controlled_buffer_7_out), .D8(controlled_buffer_8_out), .WR(address_decode_logic_1_cell_13_w),
    .EN(address_decode_logic_1_cell_13_e), .V1(C13_v1), .V2(C13_v2), .V3(C13_v3), .V4(C13_v4), .V5(C13_v5),
    .V6(C13_v6), .V7(C13_v7), .V8(C13_v8), .CLK(C13_clk), .O8(controlled_buffer_8_out),
    .O1(controlled_buffer_1_out), .O2(controlled_buffer_2_out), .O3(controlled_buffer_3_out),
    .O4(controlled_buffer_4_out), .O5(controlled_buffer_5_out), .O6(controlled_buffer_6_out),
    .O7(controlled_buffer_7_out));  // open: RESET
  LED led_65 (.in(C13_v2));
  LED led_66 (.in(C13_v3));
  LED led_67 (.in(C13_v4));
  LED led_68 (.in(C13_v5));
  LED led_69 (.in(C13_v6));
  LED led_70 (.in(C13_v7));
  LED led_71 (.in(C13_v8));
  LED led_72 (.in(C13_clk));
  LED led_73 (.in(C2_v1));
  Byte_Memory_Module C2 (
    .D1(controlled_buffer_1_out), .D2(controlled_buffer_2_out), .D3(controlled_buffer_3_out),
    .D4(controlled_buffer_4_out), .D5(controlled_buffer_5_out), .D6(controlled_buffer_6_out),
    .D7(controlled_buffer_7_out), .D8(controlled_buffer_8_out), .WR(address_decode_logic_1_cell_2_w),
    .EN(address_decode_logic_1_cell_2_e), .V1(C2_v1), .V2(C2_v2), .V3(C2_v3), .V4(C2_v4), .V5(C2_v5),
    .V6(C2_v6), .V7(C2_v7), .V8(C2_v8), .CLK(C2_clk), .O8(controlled_buffer_8_out),
    .O1(controlled_buffer_1_out), .O2(controlled_buffer_2_out), .O3(controlled_buffer_3_out),
    .O4(controlled_buffer_4_out), .O5(controlled_buffer_5_out), .O6(controlled_buffer_6_out),
    .O7(controlled_buffer_7_out));  // open: RESET
  LED led_74 (.in(C2_v2));
  LED led_75 (.in(C2_v3));
  LED led_76 (.in(C2_v4));
  LED led_77 (.in(C2_v5));
  LED led_78 (.in(C2_v6));
  LED led_79 (.in(C2_v7));
  LED led_80 (.in(C2_v8));
  LED led_81 (.in(C2_clk));
  LED led_82 (.in(C6_v1));
  Byte_Memory_Module C6 (
    .D1(controlled_buffer_1_out), .D2(controlled_buffer_2_out), .D3(controlled_buffer_3_out),
    .D4(controlled_buffer_4_out), .D5(controlled_buffer_5_out), .D6(controlled_buffer_6_out),
    .D7(controlled_buffer_7_out), .D8(controlled_buffer_8_out), .WR(address_decode_logic_1_cell_6_w),
    .EN(address_decode_logic_1_cell_6_e), .V1(C6_v1), .V2(C6_v2), .V3(C6_v3), .V4(C6_v4), .V5(C6_v5),
    .V6(C6_v6), .V7(C6_v7), .V8(C6_v8), .CLK(C6_clk), .O8(controlled_buffer_8_out),
    .O1(controlled_buffer_1_out), .O2(controlled_buffer_2_out), .O3(controlled_buffer_3_out),
    .O4(controlled_buffer_4_out), .O5(controlled_buffer_5_out), .O6(controlled_buffer_6_out), .O7(C6_o7));  // open: RESET
  LED led_83 (.in(C6_v2));
  LED led_84 (.in(C6_v3));
  LED led_85 (.in(C6_v4));
  LED led_86 (.in(C6_v5));
  LED led_87 (.in(C6_v6));
  LED led_88 (.in(C6_v7));
  LED led_89 (.in(C6_v8));
  LED led_90 (.in(C6_clk));
  LED led_91 (.in(C10_v1));
  Byte_Memory_Module C10 (
    .D1(controlled_buffer_1_out), .D2(controlled_buffer_2_out), .D3(controlled_buffer_3_out),
    .D4(controlled_buffer_4_out), .D5(controlled_buffer_5_out), .D6(controlled_buffer_6_out),
    .D7(controlled_buffer_7_out), .D8(controlled_buffer_8_out), .WR(address_decode_logic_1_cell_10_w),
    .EN(address_decode_logic_1_cell_10_e), .V1(C10_v1), .V2(C10_v2), .V3(C10_v3), .V4(C10_v4), .V5(C10_v5),
    .V6(C10_v6), .V7(C10_v7), .V8(C10_v8), .CLK(C10_clk), .O8(controlled_buffer_8_out),
    .O1(controlled_buffer_1_out), .O2(controlled_buffer_2_out), .O3(controlled_buffer_3_out),
    .O4(controlled_buffer_4_out), .O5(controlled_buffer_5_out), .O6(controlled_buffer_6_out),
    .O7(controlled_buffer_7_out));  // open: RESET
  LED led_92 (.in(C10_v2));
  LED led_93 (.in(C10_v3));
  LED led_94 (.in(C10_v4));
  LED led_95 (.in(C10_v5));
  LED led_96 (.in(C10_v6));
  LED led_97 (.in(C10_v7));
  LED led_98 (.in(C10_v8));
  LED led_99 (.in(C10_clk));
  LED led_100 (.in(C14_v1));
  Byte_Memory_Module C14 (
    .D1(controlled_buffer_1_out), .D2(controlled_buffer_2_out), .D3(controlled_buffer_3_out),
    .D4(controlled_buffer_4_out), .D5(controlled_buffer_5_out), .D6(controlled_buffer_6_out),
    .D7(controlled_buffer_7_out), .D8(controlled_buffer_8_out), .WR(address_decode_logic_1_cell_14_w),
    .EN(address_decode_logic_1_cell_14_e), .V1(C14_v1), .V2(C14_v2), .V3(C14_v3), .V4(C14_v4), .V5(C14_v5),
    .V6(C14_v6), .V7(C14_v7), .V8(C14_v8), .CLK(C14_clk), .O8(controlled_buffer_8_out),
    .O1(controlled_buffer_1_out), .O2(controlled_buffer_2_out), .O3(controlled_buffer_3_out),
    .O4(controlled_buffer_4_out), .O5(controlled_buffer_5_out), .O6(controlled_buffer_6_out),
    .O7(controlled_buffer_7_out));  // open: RESET
  LED led_101 (.in(C14_v2));
  LED led_102 (.in(C14_v3));
  LED led_103 (.in(C14_v4));
  LED led_104 (.in(C14_v5));
  LED led_105 (.in(C14_v6));
  LED led_106 (.in(C14_v7));
  LED led_107 (.in(C14_v8));
  LED led_108 (.in(C14_clk));
  LED led_109 (.in(C3_v1));
  Byte_Memory_Module C3 (
    .D1(controlled_buffer_1_out), .D2(controlled_buffer_2_out), .D3(controlled_buffer_3_out),
    .D4(controlled_buffer_4_out), .D5(controlled_buffer_5_out), .D6(controlled_buffer_6_out),
    .D7(controlled_buffer_7_out), .D8(controlled_buffer_8_out), .WR(address_decode_logic_1_cell_3_w),
    .EN(address_decode_logic_1_cell_3_e), .V1(C3_v1), .V2(C3_v2), .V3(C3_v3), .V4(C3_v4), .V5(C3_v5),
    .V6(C3_v6), .V7(C3_v7), .V8(C3_v8), .CLK(C3_clk), .O8(controlled_buffer_8_out),
    .O1(controlled_buffer_1_out), .O2(controlled_buffer_2_out), .O3(controlled_buffer_3_out),
    .O4(controlled_buffer_4_out), .O5(controlled_buffer_5_out), .O6(controlled_buffer_6_out),
    .O7(controlled_buffer_7_out));  // open: RESET
  LED led_110 (.in(C3_v2));
  LED led_111 (.in(C3_v3));
  LED led_112 (.in(C3_v4));
  LED led_113 (.in(C3_v5));
  LED led_114 (.in(C3_v6));
  LED led_115 (.in(C3_v7));
  LED led_116 (.in(C3_v8));
  LED led_117 (.in(C3_clk));
  LED led_118 (.in(C7_v1));
  Byte_Memory_Module C7 (
    .D1(controlled_buffer_1_out), .D2(controlled_buffer_2_out), .D3(controlled_buffer_3_out),
    .D4(controlled_buffer_4_out), .D5(controlled_buffer_5_out), .D6(controlled_buffer_6_out), .D7(C6_o7),
    .D8(controlled_buffer_8_out), .WR(address_decode_logic_1_cell_7_e), .EN(address_decode_logic_1_cell_7_e),
    .V1(C7_v1), .V2(C7_v2), .V3(C7_v3), .V4(C7_v4), .V5(C7_v5), .V6(C7_v6), .V7(C7_v7), .V8(C7_v8),
    .CLK(C7_clk), .O8(controlled_buffer_8_out), .O1(controlled_buffer_1_out), .O2(controlled_buffer_2_out),
    .O3(controlled_buffer_3_out), .O4(controlled_buffer_4_out), .O5(controlled_buffer_5_out),
    .O6(controlled_buffer_6_out), .O7(C6_o7));  // open: RESET
  LED led_119 (.in(C7_v2));
  LED led_120 (.in(C7_v3));
  LED led_121 (.in(C7_v4));
  LED led_122 (.in(C7_v5));
  LED led_123 (.in(C7_v6));
  LED led_124 (.in(C7_v7));
  LED led_125 (.in(C7_v8));
  LED led_126 (.in(C7_clk));
  LED led_127 (.in(C11_v1));
  Byte_Memory_Module C11 (
    .D1(controlled_buffer_1_out), .D2(controlled_buffer_2_out), .D3(controlled_buffer_3_out),
    .D4(controlled_buffer_4_out), .D5(controlled_buffer_5_out), .D6(controlled_buffer_6_out),
    .D7(controlled_buffer_7_out), .D8(controlled_buffer_8_out), .WR(address_decode_logic_1_cell_11_w),
    .EN(address_decode_logic_1_cell_11_e), .V1(C11_v1), .V2(C11_v2), .V3(C11_v3), .V4(C11_v4), .V5(C11_v5),
    .V6(C11_v6), .V7(C11_v7), .V8(C11_v8), .CLK(C11_clk), .O8(controlled_buffer_8_out),
    .O1(controlled_buffer_1_out), .O2(controlled_buffer_2_out), .O3(controlled_buffer_3_out),
    .O4(controlled_buffer_4_out), .O5(controlled_buffer_5_out), .O6(controlled_buffer_6_out),
    .O7(controlled_buffer_7_out));  // open: RESET
  LED led_128 (.in(C11_v2));
  LED led_129 (.in(C11_v3));
  LED led_130 (.in(C11_v4));
  LED led_131 (.in(C11_v5));
  LED led_132 (.in(C11_v6));
  LED led_133 (.in(C11_v7));
  LED led_134 (.in(C11_v8));
  LED led_135 (.in(C11_clk));
  LED led_136 (.in(C15_v1));
  Byte_Memory_Module C15 (
    .D1(controlled_buffer_1_out), .D2(controlled_buffer_2_out), .D3(controlled_buffer_3_out),
    .D4(controlled_buffer_4_out), .D5(controlled_buffer_5_out), .D6(controlled_buffer_6_out),
    .D7(controlled_buffer_7_out), .D8(controlled_buffer_8_out), .WR(address_decode_logic_1_cell_15_w),
    .EN(address_decode_logic_1_cell_15_e), .V1(C15_v1), .V2(C15_v2), .V3(C15_v3), .V4(C15_v4), .V5(C15_v5),
    .V6(C15_v6), .V7(C15_v7), .V8(C15_v8), .CLK(C15_clk), .O8(controlled_buffer_8_out),
    .O1(controlled_buffer_1_out), .O2(controlled_buffer_2_out), .O3(controlled_buffer_3_out),
    .O4(controlled_buffer_4_out), .O5(controlled_buffer_5_out), .O6(controlled_buffer_6_out),
    .O7(controlled_buffer_7_out));  // open: RESET
  LED led_137 (.in(C15_v2));
  LED led_138 (.in(C15_v3));
  LED led_139 (.in(C15_v4));
  LED led_140 (.in(C15_v5));
  LED led_141 (.in(C15_v6));
  LED led_142 (.in(C15_v7));
  LED led_143 (.in(C15_v8));
  LED led_144 (.in(C15_clk));

  // Notes on the sheet:
  //   BUS INTERFACE
  //   MANUAL PROGRAMMING PINS
endmodule

module Byte_Memory_Module (
  input  D1,
  input  D2,
  input  D3,
  input  D4,
  input  D5,
  input  D6,
  input  D7,
  input  D8,
  input  WR,
  input  RESET,
  input  EN,
  output V1,
  output V2,
  output V3,
  output V4,
  output V5,
  output V6,
  output V7,
  output V8,
  output CLK,
  output O8,
  output O1,
  output O2,
  output O3,
  output O4,
  output O5,
  output O6,
  output O7
);

  wire controlled_buffer_1_out, controlled_buffer_2_out, controlled_buffer_3_out, controlled_buffer_4_out,
       controlled_buffer_5_out, controlled_buffer_6_out, controlled_buffer_7_out, controlled_buffer_8_out,
       d_ff_1_qn, d_ff_2_qn, d_ff_3_qn, d_ff_4_qn, d_ff_5_qn, d_ff_6_qn, d_ff_7_qn, d_ff_8_qn;

  assign controlled_buffer_1_out = WR ? D1 : 1'bz;  // Controlled_Buffer controlled_buffer_1
  assign controlled_buffer_2_out = WR ? D2 : 1'bz;  // Controlled_Buffer controlled_buffer_2
  D_Flip_Flop d_ff_1 (.D(controlled_buffer_1_out), .clk(CLK), .Q(V1), .Qn(d_ff_1_qn), .reset(RESET));  // open: preset
  Clock clock_1 (.out(CLK));
  assign controlled_buffer_3_out = WR ? D3 : 1'bz;  // Controlled_Buffer controlled_buffer_3
  D_Flip_Flop d_ff_2 (.D(controlled_buffer_2_out), .clk(CLK), .Q(V2), .Qn(d_ff_2_qn), .reset(RESET));  // open: preset
  assign O1 = EN ? ~d_ff_1_qn : 1'bz;  // Controlled_Inverter controlled_inverter_1
  assign controlled_buffer_4_out = WR ? D4 : 1'bz;  // Controlled_Buffer controlled_buffer_4
  D_Flip_Flop d_ff_3 (.D(controlled_buffer_3_out), .clk(CLK), .Q(V3), .Qn(d_ff_3_qn), .reset(RESET));  // open: preset
  D_Flip_Flop d_ff_4 (.D(controlled_buffer_4_out), .clk(CLK), .Q(V4), .Qn(d_ff_4_qn), .reset(RESET));  // open: preset
  assign O2 = EN ? ~d_ff_2_qn : 1'bz;  // Controlled_Inverter controlled_inverter_2
  assign controlled_buffer_5_out = WR ? D5 : 1'bz;  // Controlled_Buffer controlled_buffer_5
  D_Flip_Flop d_ff_5 (.D(controlled_buffer_5_out), .clk(CLK), .Q(V5), .Qn(d_ff_5_qn), .reset(RESET));  // open: preset
  assign O3 = EN ? ~d_ff_3_qn : 1'bz;  // Controlled_Inverter controlled_inverter_3
  assign controlled_buffer_6_out = WR ? D6 : 1'bz;  // Controlled_Buffer controlled_buffer_6
  D_Flip_Flop d_ff_6 (.D(controlled_buffer_6_out), .clk(CLK), .Q(V6), .Qn(d_ff_6_qn), .reset(RESET));  // open: preset
  assign O4 = EN ? ~d_ff_4_qn : 1'bz;  // Controlled_Inverter controlled_inverter_4
  assign O5 = EN ? ~d_ff_5_qn : 1'bz;  // Controlled_Inverter controlled_inverter_5
  assign controlled_buffer_7_out = WR ? D7 : 1'bz;  // Controlled_Buffer controlled_buffer_7
  D_Flip_Flop d_ff_7 (.D(controlled_buffer_7_out), .clk(CLK), .Q(V7), .Qn(d_ff_7_qn), .reset(RESET));  // open: preset
  assign O6 = EN ? ~d_ff_6_qn : 1'bz;  // Controlled_Inverter controlled_inverter_6
  assign controlled_buffer_8_out = WR ? D8 : 1'bz;  // Controlled_Buffer controlled_buffer_8
  D_Flip_Flop d_ff_8 (.D(controlled_buffer_8_out), .clk(CLK), .Q(V8), .Qn(d_ff_8_qn), .reset(RESET));  // open: preset
  assign O7 = EN ? ~d_ff_7_qn : 1'bz;  // Controlled_Inverter controlled_inverter_7
  assign O8 = EN ? ~d_ff_8_qn : 1'bz;  // Controlled_Inverter controlled_inverter_8
endmodule

module Address_Decode_Logic (
  input  A0,
  input  A1,
  input  A2,
  input  A3,
  input  OUT_CONTROL,
  input  E0W1,
  output CELL_0_E,
  output CELL_0_W,
  output CELL_1_E,
  output CELL_1_W,
  output CELL_2_E,
  output CELL_2_W,
  output CELL_3_E,
  output CELL_3_W,
  output CELL_4_E,
  output CELL_4_W,
  output CELL_5_E,
  output CELL_5_W,
  output CELL_6_E,
  output CELL_6_W,
  output CELL_7_E,
  output CELL_7_W,
  output CELL_8_E,
  output CELL_8_W,
  output CELL_9_E,
  output CELL_9_W,
  output CELL_10_E,
  output CELL_10_W,
  output CELL_11_E,
  output CELL_11_W,
  output CELL_12_E,
  output CELL_12_W,
  output CELL_13_E,
  output CELL_13_W,
  output CELL_14_E,
  output CELL_14_W,
  output CELL_15_E,
  output CELL_15_W
);

  wire and_1_out, and_2_out, and_3_out, and_4_out, and_5_out, and_6_out, and_7_out, and_8_out, and_9_out,
       and_10_out, and_11_out, and_12_out, and_13_out, and_14_out, and_15_out, and_16_out, and_17_out,
       and_18_out, and_19_out, and_20_out, and_21_out, and_22_out, and_23_out, and_24_out, and_25_out,
       and_26_out, and_27_out, and_28_out, and_29_out, and_30_out, and_31_out, and_32_out, not_1_out,
       not_2_out, not_3_out, not_4_out;

  not not_1 (not_1_out, A0);
  not not_2 (not_2_out, A1);
  not not_3 (not_3_out, A2);
  not not_4 (not_4_out, A3);
  and and_1 (and_1_out, not_1_out, not_2_out, not_3_out, not_4_out);
  and and_2 (and_2_out, A0, not_2_out, not_3_out, not_4_out);
  and and_3 (and_3_out, not_1_out, A1, not_3_out, not_4_out);
  and and_4 (and_4_out, A0, A1, not_3_out, not_4_out);
  and and_5 (and_5_out, not_1_out, not_2_out, A2, not_4_out);
  and and_6 (and_6_out, A0, not_2_out, A2, not_4_out);
  and and_7 (and_7_out, not_1_out, A1, A2, not_4_out);
  and and_8 (and_8_out, A0, A1, A2, not_4_out);
  and and_9 (and_9_out, not_1_out, not_2_out, not_3_out, A3);
  and and_10 (and_10_out, A0, not_2_out, not_3_out, A3);
  and and_11 (and_11_out, not_1_out, A1, not_3_out, A3);
  and and_12 (and_12_out, A0, A1, not_3_out, A3);
  and and_13 (and_13_out, not_1_out, not_2_out, A2, A3);
  and and_14 (and_14_out, A0, not_2_out, A2, A3);
  and and_15 (and_15_out, not_1_out, A1, A2, A3);
  and and_16 (and_16_out, A0, A1, A2, A3);
  and and_17 (and_17_out, and_1_out, OUT_CONTROL);
  Demultiplexer demultiplexer_1 (.out0(CELL_0_E), .out1(CELL_0_W), .in(and_17_out), .sel(E0W1));
  and and_18 (and_18_out, and_2_out, OUT_CONTROL);
  Demultiplexer demultiplexer_2 (.out0(CELL_1_E), .out1(CELL_1_W), .in(and_18_out), .sel(E0W1));
  and and_19 (and_19_out, and_3_out, OUT_CONTROL);
  Demultiplexer demultiplexer_3 (.out0(CELL_2_E), .out1(CELL_2_W), .in(and_19_out), .sel(E0W1));
  and and_20 (and_20_out, and_4_out, OUT_CONTROL);
  Demultiplexer demultiplexer_4 (.out0(CELL_3_E), .out1(CELL_3_W), .in(and_20_out), .sel(E0W1));
  and and_21 (and_21_out, and_5_out, OUT_CONTROL);
  Demultiplexer demultiplexer_5 (.out0(CELL_4_E), .out1(CELL_4_W), .in(and_21_out), .sel(E0W1));
  and and_22 (and_22_out, and_6_out, OUT_CONTROL);
  Demultiplexer demultiplexer_6 (.out0(CELL_5_E), .out1(CELL_5_W), .in(and_22_out), .sel(E0W1));
  and and_23 (and_23_out, and_7_out, OUT_CONTROL);
  Demultiplexer demultiplexer_7 (.out0(CELL_6_E), .out1(CELL_6_W), .in(and_23_out), .sel(E0W1));
  and and_24 (and_24_out, and_8_out, OUT_CONTROL);
  Demultiplexer demultiplexer_8 (.out0(CELL_7_E), .out1(CELL_7_W), .in(and_24_out), .sel(E0W1));
  and and_25 (and_25_out, and_9_out, OUT_CONTROL);
  Demultiplexer demultiplexer_9 (.out0(CELL_8_E), .out1(CELL_8_W), .in(and_25_out), .sel(E0W1));
  and and_26 (and_26_out, and_10_out, OUT_CONTROL);
  Demultiplexer demultiplexer_10 (.out0(CELL_9_E), .out1(CELL_9_W), .in(and_26_out), .sel(E0W1));
  and and_27 (and_27_out, and_11_out, OUT_CONTROL);
  Demultiplexer demultiplexer_11 (.out0(CELL_10_E), .out1(CELL_10_W), .in(and_27_out), .sel(E0W1));
  and and_28 (and_28_out, and_12_out, OUT_CONTROL);
  Demultiplexer demultiplexer_12 (.out0(CELL_11_E), .out1(CELL_11_W), .in(and_28_out), .sel(E0W1));
  and and_29 (and_29_out, and_13_out, OUT_CONTROL);
  Demultiplexer demultiplexer_13 (.out0(CELL_12_E), .out1(CELL_12_W), .in(and_29_out), .sel(E0W1));
  and and_30 (and_30_out, and_14_out, OUT_CONTROL);
  Demultiplexer demultiplexer_14 (.out0(CELL_13_E), .out1(CELL_13_W), .in(and_30_out), .sel(E0W1));
  and and_31 (and_31_out, and_15_out, OUT_CONTROL);
  Demultiplexer demultiplexer_15 (.out0(CELL_14_E), .out1(CELL_14_W), .in(and_31_out), .sel(E0W1));
  and and_32 (and_32_out, and_16_out, OUT_CONTROL);
  Demultiplexer demultiplexer_16 (.out0(CELL_15_E), .out1(CELL_15_W), .in(and_32_out), .sel(E0W1));
endmodule
