// Logisim project PROM_CHIP -8Bit_Decimal _Display.circ as structural Verilog: 5 circuits, main circuit Byte_Memory_Module
module main (
  input  in_1,
  input  DATA,
  input  in_3,
  input  in_4,
  input  in_5,
  input  in_6,
  input  in_7,
  input  in_8,
  input  in_9,
  input  in_10,
  input  ADDRESS,
  input  PINS,
  input  in_13,
  input  in_14,
  input  in_15,
  input  in_16,
  input  in_17,
  input  in_18,
  input  in_19,
  input  DATA_BUS,
  input  in_21,
  input  in_22,
  input  in_23,
  input  in_24,
  input  in_25,
  input  in_26,
  input  in_27,
  input  in_28,
  input  in_29,
  input  in_30,
  input  in_31
);

  wire binary2bcd_1_o1_1, binary2bcd_1_o1_2, binary2bcd_1_o2_1, binary2bcd_1_o2_2, binary2bcd_1_o2_4,
       binary2bcd_1_o2_8, binary2bcd_1_o3_1, binary2bcd_1_o3_2, binary2bcd_1_o3_4, binary2bcd_1_o3_8,
       or_1_out, or_2_out, or_3_out, or_4_out, or_5_out, or_6_out, or_7_out, or_8_out, or_9_out, or_10_out,
       prom_chip_1_clk, prom_chip_1_disp_a, prom_chip_1_disp_b, prom_chip_1_disp_c, prom_chip_1_disp_d,
       prom_chip_1_disp_e, prom_chip_1_disp_f, prom_chip_1_disp_g, prom_chip_2_clk, prom_chip_2_disp_a,
       prom_chip_2_disp_b, prom_chip_2_disp_c, prom_chip_2_disp_d, prom_chip_2_disp_e, prom_chip_2_disp_f,
       prom_chip_2_disp_g, prom_chip_3_clk, prom_chip_3_disp_a, prom_chip_3_disp_b, prom_chip_3_disp_c,
       prom_chip_3_disp_d, prom_chip_3_disp_e, prom_chip_3_disp_f, prom_chip_3_disp_g;

  Binary2BCD binary2bcd_1 (
    .I128(in_16), .I64(in_17), .I32(in_18), .I16(in_19), .I8(DATA_BUS), .I4(in_21), .I2(in_22), .I1(in_24),
    .O1_2(binary2bcd_1_o1_2), .O1_1(binary2bcd_1_o1_1), .O2_8(binary2bcd_1_o2_8), .O2_4(binary2bcd_1_o2_4),
    .O2_2(binary2bcd_1_o2_2), .O2_1(binary2bcd_1_o2_1), .O3_8(binary2bcd_1_o3_8), .O3_4(binary2bcd_1_o3_4),
    .O3_2(binary2bcd_1_o3_2), .O3_1(binary2bcd_1_o3_1));  // open: O1_8, O1_4
  or or_1 (or_1_out, in_10, binary2bcd_1_o1_1);
  or or_2 (or_2_out, ADDRESS, binary2bcd_1_o1_2);
  or or_3 (or_3_out, in_10, binary2bcd_1_o2_1);
  or or_4 (or_4_out, binary2bcd_1_o2_2, ADDRESS);
  or or_5 (or_5_out, in_10, binary2bcd_1_o3_1);
  or or_6 (or_6_out, binary2bcd_1_o3_2, ADDRESS);
  or or_7 (or_7_out, binary2bcd_1_o2_4, PINS);
  or or_8 (or_8_out, binary2bcd_1_o3_4, PINS);
  or or_9 (or_9_out, in_13, binary2bcd_1_o2_8);
  or or_10 (or_10_out, binary2bcd_1_o3_8, in_13);
  PROM_CHIP prom_chip_1 (
    .a(in_1), .b(DATA), .c(in_3), .d(in_4), .e(in_5), .f(in_6), .g(in_7), .DATA_ENABLE(in_8), .RESET(in_9),
    .AO(or_1_out), .A1(or_2_out), .A2(PINS), .A3(in_13), .CHIP_ENABLE(in_14), .E0W1(in_15),
    .disp_a(prom_chip_1_disp_a), .disp_b(prom_chip_1_disp_b), .disp_c(prom_chip_1_disp_c),
    .disp_d(prom_chip_1_disp_d), .disp_e(prom_chip_1_disp_e), .disp_f(prom_chip_1_disp_f),
    .disp_g(prom_chip_1_disp_g), .CLK(prom_chip_1_clk));
  LED led_1 (.in(prom_chip_1_clk));
  PROM_CHIP prom_chip_2 (
    .a(in_1), .b(DATA), .c(in_3), .d(in_4), .e(in_5), .f(in_6), .g(in_7), .DATA_ENABLE(in_23), .RESET(in_25),
    .AO(or_3_out), .A1(or_4_out), .A2(or_7_out), .A3(or_9_out), .CHIP_ENABLE(in_26), .E0W1(in_27),
    .disp_a(prom_chip_2_disp_a), .disp_b(prom_chip_2_disp_b), .disp_c(prom_chip_2_disp_c),
    .disp_d(prom_chip_2_disp_d), .disp_e(prom_chip_2_disp_e), .disp_f(prom_chip_2_disp_f),
    .disp_g(prom_chip_2_disp_g), .CLK(prom_chip_2_clk));
  LED led_2 (.in(prom_chip_2_clk));
  PROM_CHIP prom_chip_3 (
    .a(in_1), .b(DATA), .c(in_3), .d(in_4), .e(in_5), .f(in_6), .g(in_7), .DATA_ENABLE(in_28), .RESET(in_29),
    .AO(or_5_out), .A1(or_6_out), .A2(or_8_out), .A3(or_10_out), .CHIP_ENABLE(in_30), .E0W1(in_31),
    .disp_a(prom_chip_3_disp_a), .disp_b(prom_chip_3_disp_b), .disp_c(prom_chip_3_disp_c),
    .disp_d(prom_chip_3_disp_d), .disp_e(prom_chip_3_disp_e), .disp_f(prom_chip_3_disp_f),
    .disp_g(prom_chip_3_disp_g), .CLK(prom_chip_3_clk));
  LED led_3 (.in(prom_chip_3_clk));
  _7_Segment_Display u_7_segment_display_1 (
    .g(prom_chip_1_disp_g), .f(prom_chip_1_disp_f), .a(prom_chip_1_disp_a), .b(prom_chip_1_disp_b),
    .e(prom_chip_1_disp_e), .d(prom_chip_1_disp_d), .c(prom_chip_1_disp_c));  // open: dp
  _7_Segment_Display u_7_segment_display_2 (
    .g(prom_chip_2_disp_g), .f(prom_chip_2_disp_f), .a(prom_chip_2_disp_a), .b(prom_chip_2_disp_b),
    .e(prom_chip_2_disp_e), .d(prom_chip_2_disp_d), .c(prom_chip_2_disp_c));  // open: dp
  _7_Segment_Display u_7_segment_display_3 (
    .g(prom_chip_3_disp_g), .f(prom_chip_3_disp_f), .a(prom_chip_3_disp_a), .b(prom_chip_3_disp_b),
    .e(prom_chip_3_disp_e), .d(prom_chip_3_disp_d), .c(prom_chip_3_disp_c));  // open: dp

  // Notes on the sheet:
  //   PROGRAMMING
  //   PINS
endmodule

module Byte_Memory_Module (
  input  D1,
  input  D2,
  input  D3,
  input  D4,
  input  D5,
  input  D6,
  input  D7,
  input  D8,
  input  WR,
  input  RESET,
  input  EN,
  output V1,
  output V2,
  output V3,
  output V4,
  output V5,
  output V6,
  output V7,
  output V8,
  output CLK,
  output O8,
  output O1,
  output O2,
  output O3,
  output O4,
  output O5,
  output O6,
  output O7
);

  wire controlled_buffer_1_out, controlled_buffer_2_out, controlled_buffer_3_out, controlled_buffer_4_out,
       controlled_buffer_5_out, controlled_buffer_6_out, controlled_buffer_7_out, controlled_buffer_8_out,
       d_ff_1_qn, d_ff_2_qn, d_ff_3_qn, d_ff_4_qn, d_ff_5_qn, d_ff_6_qn, d_ff_7_qn, d_ff_8_qn;

  assign controlled_buffer_1_out = WR ? D1 : 1'bz;  // Controlled_Buffer controlled_buffer_1
  assign controlled_buffer_2_out = WR ? D2 : 1'bz;  // Controlled_Buffer controlled_buffer_2
  D_Flip_Flop d_ff_1 (.D(controlled_buffer_1_out), .clk(CLK), .Q(V1), .Qn(d_ff_1_qn), .reset(RESET));  // open: preset
  Clock clock_1 (.out(CLK));
  assign controlled_buffer_3_out = WR ? D3 : 1'bz;  // Controlled_Buffer controlled_buffer_3
  D_Flip_Flop d_ff_2 (.D(controlled_buffer_2_out), .clk(CLK), .Q(V2), .Qn(d_ff_2_qn), .reset(RESET));  // open: preset
  assign O1 = EN ? ~d_ff_1_qn : 1'bz;  // Controlled_Inverter controlled_inverter_1
  assign controlled_buffer_4_out = WR ? D4 : 1'bz;  // Controlled_Buffer controlled_buffer_4
  D_Flip_Flop d_ff_3 (.D(controlled_buffer_3_out), .clk(CLK), .Q(V3), .Qn(d_ff_3_qn), .reset(RESET));  // open: preset
  D_Flip_Flop d_ff_4 (.D(controlled_buffer_4_out), .clk(CLK), .Q(V4), .Qn(d_ff_4_qn), .reset(RESET));  // open: preset
  assign O2 = EN ? ~d_ff_2_qn : 1'bz;  // Controlled_Inverter controlled_inverter_2
  assign controlled_buffer_5_out = WR ? D5 : 1'bz;  // Controlled_Buffer controlled_buffer_5
  D_Flip_Flop d_ff_5 (.D(controlled_buffer_5_out), .clk(CLK), .Q(V5), .Qn(d_ff_5_qn), .reset(RESET));  // open: preset
  assign O3 = EN ? ~d_ff_3_qn : 1'bz;  // Controlled_Inverter controlled_inverter_3
  assign controlled_buffer_6_out = WR ? D6 : 1'bz;  // Controlled_Buffer controlled_buffer_6
  D_Flip_Flop d_ff_6 (.D(controlled_buffer_6_out), .clk(CLK), .Q(V6), .Qn(d_ff_6_qn), .reset(RESET));  // open: preset
  assign O4 = EN ? ~d_ff_4_qn : 1'bz;  // Controlled_Inverter controlled_inverter_4
  assign O5 = EN ? ~d_ff_5_qn : 1'bz;  // Controlled_Inverter controlled_inverter_5
  assign controlled_buffer_7_out = WR ? D7 : 1'bz;  // Controlled_Buffer controlled_buffer_7
  D_Flip_Flop d_ff_7 (.D(controlled_buffer_7_out), .clk(CLK), .Q(V7), .Qn(d_ff_7_qn), .reset(RESET));  // open: preset
  assign O6 = EN ? ~d_ff_6_qn : 1'bz;  // Controlled_Inverter controlled_inverter_6
  assign controlled_buffer_8_out = WR ? D8 : 1'bz;  // Controlled_Buffer controlled_buffer_8
  D_Flip_Flop d_ff_8 (.D(controlled_buffer_8_out), .clk(CLK), .Q(V8), .Qn(d_ff_8_qn), .reset(RESET));  // open: preset
  assign O7 = EN ? ~d_ff_7_qn : 1'bz;  // Controlled_Inverter controlled_inverter_7
  assign O8 = EN ? ~d_ff_8_qn : 1'bz;  // Controlled_Inverter controlled_inverter_8
endmodule

module Address_Decode_Logic (
  input  A0,
  input  A1,
  input  A2,
  input  A3,
  input  OUT_CONTROL,
  input  E0W1,
  output CELL_0_E,
  output CELL_0_W,
  output CELL_1_E,
  output CELL_1_W,
  output CELL_2_E,
  output CELL_2_W,
  output CELL_3_E,
  output CELL_3_W,
  output CELL_4_E,
  output CELL_4_W,
  output CELL_5_E,
  output CELL_5_W,
  output CELL_6_E,
  output CELL_6_W,
  output CELL_7_E,
  output CELL_7_W,
  output CELL_8_E,
  output CELL_8_W,
  output CELL_9_E,
  output CELL_9_W,
  output CELL_10_E,
  output CELL_10_W,
  output CELL_11_E,
  output CELL_11_W,
  output CELL_12_E,
  output CELL_12_W,
  output CELL_13_E,
  output CELL_13_W,
  output CELL_14_E,
  output CELL_14_W,
  output CELL_15_E,
  output CELL_15_W
);

  wire and_1_out, and_2_out, and_3_out, and_4_out, and_5_out, and_6_out, and_7_out, and_8_out, and_9_out,
       and_10_out, and_11_out, and_12_out, and_13_out, and_14_out, and_15_out, and_16_out, and_17_out,
       and_18_out, and_19_out, and_20_out, and_21_out, and_22_out, and_23_out, and_24_out, and_25_out,
       and_26_out, and_27_out, and_28_out, and_29_out, and_30_out, and_31_out, and_32_out, not_1_out,
       not_2_out, not_3_out, not_4_out;

  not not_1 (not_1_out, A0);
  not not_2 (not_2_out, A1);
  not not_3 (not_3_out, A2);
  not not_4 (not_4_out, A3);
  and and_1 (and_1_out, not_1_out, not_2_out, not_3_out, not_4_out);
  and and_2 (and_2_out, A0, not_2_out, not_3_out, not_4_out);
  and and_3 (and_3_out, not_1_out, A1, not_3_out, not_4_out);
  and and_4 (and_4_out, A0, A1, not_3_out, not_4_out);
  and and_5 (and_5_out, not_1_out, not_2_out, A2, not_4_out);
  and and_6 (and_6_out, A0, not_2_out, A2, not_4_out);
  and and_7 (and_7_out, not_1_out, A1, A2, not_4_out);
  and and_8 (and_8_out, A0, A1, A2, not_4_out);
  and and_9 (and_9_out, not_1_out, not_2_out, not_3_out, A3);
  and and_10 (and_10_out, A0, not_2_out, not_3_out, A3);
  and and_11 (and_11_out, not_1_out, A1, not_3_out, A3);
  and and_12 (and_12_out, A0, A1, not_3_out, A3);
  and and_13 (and_13_out, not_1_out, not_2_out, A2, A3);
  and and_14 (and_14_out, A0, not_2_out, A2, A3);
  and and_15 (and_15_out, not_1_out, A1, A2, A3);
  and and_16 (and_16_out, A0, A1, A2, A3);
  and and_17 (and_17_out, and_1_out, OUT_CONTROL);
  Demultiplexer demultiplexer_1 (.out0(CELL_0_E), .out1(CELL_0_W), .in(and_17_out), .sel(E0W1));
  and and_18 (and_18_out, and_2_out, OUT_CONTROL);
  Demultiplexer demultiplexer_2 (.out0(CELL_1_E), .out1(CELL_1_W), .in(and_18_out), .sel(E0W1));
  and and_19 (and_19_out, and_3_out, OUT_CONTROL);
  Demultiplexer demultiplexer_3 (.out0(CELL_2_E), .out1(CELL_2_W), .in(and_19_out), .sel(E0W1));
  and and_20 (and_20_out, and_4_out, OUT_CONTROL);
  Demultiplexer demultiplexer_4 (.out0(CELL_3_E), .out1(CELL_3_W), .in(and_20_out), .sel(E0W1));
  and and_21 (and_21_out, and_5_out, OUT_CONTROL);
  Demultiplexer demultiplexer_5 (.out0(CELL_4_E), .out1(CELL_4_W), .in(and_21_out), .sel(E0W1));
  and and_22 (and_22_out, and_6_out, OUT_CONTROL);
  Demultiplexer demultiplexer_6 (.out0(CELL_5_E), .out1(CELL_5_W), .in(and_22_out), .sel(E0W1));
  and and_23 (and_23_out, and_7_out, OUT_CONTROL);
  Demultiplexer demultiplexer_7 (.out0(CELL_6_E), .out1(CELL_6_W), .in(and_23_out), .sel(E0W1));
  and and_24 (and_24_out, and_8_out, OUT_CONTROL);
  Demultiplexer demultiplexer_8 (.out0(CELL_7_E), .out1(CELL_7_W), .in(and_24_out), .sel(E0W1));
  and and_25 (and_25_out, and_9_out, OUT_CONTROL);
  Demultiplexer demultiplexer_9 (.out0(CELL_8_E), .out1(CELL_8_W), .in(and_25_out), .sel(E0W1));
  and and_26 (and_26_out, and_10_out, OUT_CONTROL);
  Demultiplexer demultiplexer_10 (.out0(CELL_9_E), .out1(CELL_9_W), .in(and_26_out), .sel(E0W1));
  and and_27 (and_27_out, and_11_out, OUT_CONTROL);
  Demultiplexer demultiplexer_11 (.out0(CELL_10_E), .out1(CELL_10_W), .in(and_27_out), .sel(E0W1));
  and and_28 (and_28_out, and_12_out, OUT_CONTROL);
  Demultiplexer demultiplexer_12 (.out0(CELL_11_E), .out1(CELL_11_W), .in(and_28_out), .sel(E0W1));
  and and_29 (and_29_out, and_13_out, OUT_CONTROL);
  Demultiplexer demultiplexer_13 (.out0(CELL_12_E), .out1(CELL_12_W), .in(and_29_out), .sel(E0W1));
  and and_30 (and_30_out, and_14_out, OUT_CONTROL);
  Demultiplexer demultiplexer_14 (.out0(CELL_13_E), .out1(CELL_13_W), .in(and_30_out), .sel(E0W1));
  and and_31 (and_31_out, and_15_out, OUT_CONTROL);
  Demultiplexer demultiplexer_15 (.out0(CELL_14_E), .out1(CELL_14_W), .in(and_31_out), .sel(E0W1));
  and and_32 (and_32_out, and_16_out, OUT_CONTROL);
  Demultiplexer demultiplexer_16 (.out0(CELL_15_E), .out1(CELL_15_W), .in(and_32_out), .sel(E0W1));
endmodule

module PROM_CHIP (
  input  a,
  input  b,
  input  c,
  input  d,
  input  e,
  input  f,
  input  g,
  input  DATA_ENABLE,
  input  RESET,
  input  AO,
  input  A1,
  input  A2,
  input  A3,
  input  CHIP_ENABLE,
  input  E0W1,
  output disp_a,
  output disp_b,
  output disp_c,
  output disp_d,
  output disp_e,
  output disp_f,
  output disp_g,
  output CLK
);

  wire address_decode_logic_1_cell_0_e, address_decode_logic_1_cell_0_w, address_decode_logic_1_cell_1_e,
       address_decode_logic_1_cell_1_w, address_decode_logic_1_cell_2_e, address_decode_logic_1_cell_2_w,
       address_decode_logic_1_cell_3_e, address_decode_logic_1_cell_3_w, address_decode_logic_1_cell_4_e,
       address_decode_logic_1_cell_4_w, address_decode_logic_1_cell_5_e, address_decode_logic_1_cell_5_w,
       address_decode_logic_1_cell_6_e, address_decode_logic_1_cell_6_w, address_decode_logic_1_cell_7_e,
       address_decode_logic_1_cell_7_w, address_decode_logic_1_cell_8_e, address_decode_logic_1_cell_8_w,
       address_decode_logic_1_cell_9_e, address_decode_logic_1_cell_9_w, address_decode_logic_1_cell_10_e,
       address_decode_logic_1_cell_10_w, address_decode_logic_1_cell_11_e, address_decode_logic_1_cell_11_w,
       address_decode_logic_1_cell_12_e, address_decode_logic_1_cell_12_w, address_decode_logic_1_cell_13_e,
       address_decode_logic_1_cell_13_w, address_decode_logic_1_cell_14_e, address_decode_logic_1_cell_14_w,
       address_decode_logic_1_cell_15_e, address_decode_logic_1_cell_15_w, C0_clk, C0_v1, C0_v2, C0_v3,
       C0_v4, C0_v5, C0_v6, C0_v7, C0_v8, C1_clk, C1_v1, C1_v2, C1_v3, C1_v4, C1_v5, C1_v6, C1_v7, C1_v8,
       C2_clk, C2_v1, C2_v2, C2_v3, C2_v4, C2_v5, C2_v6, C2_v7, C2_v8, C3_clk, C3_v1, C3_v2, C3_v3, C3_v4,
       C3_v5, C3_v6, C3_v7, C3_v8, C4_v1, C4_v2, C4_v3, C4_v4, C4_v5, C4_v6, C4_v7, C4_v8, C5_clk, C5_v1,
       C5_v2, C5_v3, C5_v4, C5_v5, C5_v6, C5_v7, C5_v8, C6_clk, C6_v1, C6_v2, C6_v3, C6_v4, C6_v5, C6_v6,
       C6_v7, C6_v8, C7_clk, C7_v1, C7_v2, C7_v3, C7_v4, C7_v5, C7_v6, C7_v7, C7_v8, C8_clk, C8_v1, C8_v2,
       C8_v3, C8_v4, C8_v5, C8_v6, C8_v7, C8_v8, C9_clk, C9_v1, C9_v2, C9_v3, C9_v4, C9_v5, C9_v6, C9_v7,
       C9_v8, C10_clk, C10_v1, C10_v2, C10_v3, C10_v4, C10_v5, C10_v6, C10_v7, C10_v8, C11_clk, C11_v1,
       C11_v2, C11_v3, C11_v4, C11_v5, C11_v6, C11_v7, C11_v8, C12_clk, C12_v1, C12_v2, C12_v3, C12_v4,
       C12_v5, C12_v6, C12_v7, C12_v8, C13_clk, C13_v1, C13_v2, C13_v3, C13_v4, C13_v5, C13_v6, C13_v7,
       C13_v8, C14_clk, C14_v1, C14_v2, C14_v3, C14_v4, C14_v5, C14_v6, C14_v7, C14_v8, C15_clk, C15_v1,
       C15_v2, C15_v3, C15_v4, C15_v5, C15_v6, C15_v7, C15_v8, controlled_buffer_8_out, undriven;

  Address_Decode_Logic address_decode_logic_1 (
    .A0(AO), .A1(A1), .A2(A2), .A3(A3), .OUT_CONTROL(CHIP_ENABLE), .E0W1(E0W1),
    .CELL_0_E(address_decode_logic_1_cell_0_e), .CELL_0_W(address_decode_logic_1_cell_0_w),
    .CELL_1_E(address_decode_logic_1_cell_1_e), .CELL_1_W(address_decode_logic_1_cell_1_w),
    .CELL_2_E(address_decode_logic_1_cell_2_e), .CELL_2_W(address_decode_logic_1_cell_2_w),
    .CELL_3_E(address_decode_logic_1_cell_3_e), .CELL_3_W(address_decode_logic_1_cell_3_w),
    .CELL_4_E(address_decode_logic_1_cell_4_e), .CELL_4_W(address_decode_logic_1_cell_4_w),
    .CELL_5_E(address_decode_logic_1_cell_5_e), .CELL_5_W(address_decode_logic_1_cell_5_w),
    .CELL_6_E(address_decode_logic_1_cell_6_e), .CELL_6_W(address_decode_logic_1_cell_6_w),
    .CELL_7_E(address_decode_logic_1_cell_7_e), .CELL_7_W(address_decode_logic_1_cell_7_w),
    .CELL_8_E(address_decode_logic_1_cell_8_e), .CELL_8_W(address_decode_logic_1_cell_8_w),
    .CELL_9_E(address_decode_logic_1_cell_9_e), .CELL_9_W(address_decode_logic_1_cell_9_w),
    .CELL_10_E(address_decode_logic_1_cell_10_e), .CELL_10_W(address_decode_logic_1_cell_10_w),
    .CELL_11_E(address_decode_logic_1_cell_11_e), .CELL_11_W(address_decode_logic_1_cell_11_w),
    .CELL_12_E(address_decode_logic_1_cell_12_e), .CELL_12_W(address_decode_logic_1_cell_12_w),
    .CELL_13_E(address_decode_logic_1_cell_13_e), .CELL_13_W(address_decode_logic_1_cell_13_w),
    .CELL_14_E(address_decode_logic_1_cell_14_e), .CELL_14_W(address_decode_logic_1_cell_14_w),
    .CELL_15_E(address_decode_logic_1_cell_15_e), .CELL_15_W(address_decode_logic_1_cell_15_w));
  assign disp_a = DATA_ENABLE ? a : 1'bz;  // Controlled_Buffer controlled_buffer_1
  assign disp_b = DATA_ENABLE ? b : 1'bz;  // Controlled_Buffer controlled_buffer_2
  assign disp_c = DATA_ENABLE ? c : 1'bz;  // Controlled_Buffer controlled_buffer_3
  assign disp_d = DATA_ENABLE ? d : 1'bz;  // Controlled_Buffer controlled_buffer_4
  assign disp_e = DATA_ENABLE ? e : 1'bz;  // Controlled_Buffer controlled_buffer_5
  assign disp_f = DATA_ENABLE ? f : 1'bz;  // Controlled_Buffer controlled_buffer_6
  assign disp_g = DATA_ENABLE ? g : 1'bz;  // Controlled_Buffer controlled_buffer_7
  assign controlled_buffer_8_out = DATA_ENABLE ? undriven : 1'bz;  // Controlled_Buffer controlled_buffer_8
  LED led_1 (.in(C0_v1));
  Byte_Memory_Module C0 (
    .D1(disp_a), .D2(disp_b), .D3(disp_c), .D4(disp_d), .D5(disp_e), .D6(disp_f), .D7(disp_g),
    .D8(controlled_buffer_8_out), .WR(address_decode_logic_1_cell_0_w), .RESET(RESET),
    .EN(address_decode_logic_1_cell_0_e), .V1(C0_v1), .V2(C0_v2), .V3(C0_v3), .V4(C0_v4), .V5(C0_v5),
    .V6(C0_v6), .V7(C0_v7), .V8(C0_v8), .CLK(C0_clk), .O8(controlled_buffer_8_out), .O1(disp_a), .O2(disp_b),
    .O3(disp_c), .O4(disp_d), .O5(disp_e), .O6(disp_f), .O7(disp_g));
  LED led_2 (.in(C0_v2));
  LED led_3 (.in(C0_v3));
  LED led_4 (.in(C0_v4));
  LED led_5 (.in(C0_v5));
  LED led_6 (.in(C0_v6));
  LED led_7 (.in(C0_v7));
  LED led_8 (.in(C0_v8));
  LED led_9 (.in(C0_clk));
  LED led_10 (.in(C4_v1));
  Byte_Memory_Module C4 (
    .D1(disp_a), .D2(disp_b), .D3(disp_c), .D4(disp_d), .D5(disp_e), .D6(disp_f), .D7(disp_g),
    .D8(controlled_buffer_8_out), .WR(address_decode_logic_1_cell_4_w), .RESET(RESET),
    .EN(address_decode_logic_1_cell_4_e), .V1(C4_v1), .V2(C4_v2), .V3(C4_v3), .V4(C4_v4), .V5(C4_v5),
    .V6(C4_v6), .V7(C4_v7), .V8(C4_v8), .CLK(CLK), .O8(controlled_buffer_8_out), .O1(disp_a), .O2(disp_b),
    .O3(disp_c), .O4(disp_d), .O5(disp_e), .O6(disp_f), .O7(disp_g));
  LED led_11 (.in(C4_v2));
  LED led_12 (.in(C4_v3));
  LED led_13 (.in(C4_v4));
  LED led_14 (.in(C4_v5));
  LED led_15 (.in(C4_v6));
  LED led_16 (.in(C4_v7));
  LED led_17 (.in(C4_v8));
  LED led_18 (.in(C8_v1));
  Byte_Memory_Module C8 (
    .D1(disp_a), .D2(disp_b), .D3(disp_c), .D4(disp_d), .D5(disp_e), .D6(disp_f), .D7(disp_g),
    .D8(controlled_buffer_8_out), .WR(address_decode_logic_1_cell_8_w), .RESET(RESET),
    .EN(address_decode_logic_1_cell_8_e), .V1(C8_v1), .V2(C8_v2), .V3(C8_v3), .V4(C8_v4), .V5(C8_v5),
    .V6(C8_v6), .V7(C8_v7), .V8(C8_v8), .CLK(C8_clk), .O8(controlled_buffer_8_out), .O1(disp_a), .O2(disp_b),
    .O3(disp_c), .O4(disp_d), .O5(disp_e), .O6(disp_f), .O7(disp_g));
  LED led_19 (.in(C8_v2));
  LED led_20 (.in(C8_v3));
  LED led_21 (.in(C8_v4));
  LED led_22 (.in(C8_v5));
  LED led_23 (.in(C8_v6));
  LED led_24 (.in(C8_v7));
  LED led_25 (.in(C8_v8));
  LED led_26 (.in(C8_clk));
  LED led_27 (.in(C12_v1));
  Byte_Memory_Module C12 (
    .D1(disp_a), .D2(disp_b), .D3(disp_c), .D4(disp_d), .D5(disp_e), .D6(disp_f), .D7(disp_g),
    .D8(controlled_buffer_8_out), .WR(address_decode_logic_1_cell_12_w), .RESET(RESET),
    .EN(address_decode_logic_1_cell_12_e), .V1(C12_v1), .V2(C12_v2), .V3(C12_v3), .V4(C12_v4), .V5(C12_v5),
    .V6(C12_v6), .V7(C12_v7), .V8(C12_v8), .CLK(C12_clk), .O8(controlled_buffer_8_out), .O1(disp_a),
    .O2(disp_b), .O3(disp_c), .O4(disp_d), .O5(disp_e), .O6(disp_f), .O7(disp_g));
  LED led_28 (.in(C12_v2));
  LED led_29 (.in(C12_v3));
  LED led_30 (.in(C12_v4));
  LED led_31 (.in(C12_v5));
  LED led_32 (.in(C12_v6));
  LED led_33 (.in(C12_v7));
  LED led_34 (.in(C12_v8));
  LED led_35 (.in(C12_clk));
  LED led_36 (.in(C1_v1));
  Byte_Memory_Module C1 (
    .D1(disp_a), .D2(disp_b), .D3(disp_c), .D4(disp_d), .D5(disp_e), .D6(disp_f), .D7(disp_g),
    .D8(controlled_buffer_8_out), .WR(address_decode_logic_1_cell_1_w), .RESET(RESET),
    .EN(address_decode_logic_1_cell_1_e), .V1(C1_v1), .V2(C1_v2), .V3(C1_v3), .V4(C1_v4), .V5(C1_v5),
    .V6(C1_v6), .V7(C1_v7), .V8(C1_v8), .CLK(C1_clk), .O8(controlled_buffer_8_out), .O1(disp_a), .O2(disp_b),
    .O3(disp_c), .O4(disp_d), .O5(disp_e), .O6(disp_f), .O7(disp_g));
  LED led_37 (.in(C1_v2));
  LED led_38 (.in(C1_v3));
  LED led_39 (.in(C1_v4));
  LED led_40 (.in(C1_v5));
  LED led_41 (.in(C1_v6));
  LED led_42 (.in(C1_v7));
  LED led_43 (.in(C1_v8));
  LED led_44 (.in(C1_clk));
  LED led_45 (.in(C5_v1));
  Byte_Memory_Module C5 (
    .D1(disp_a), .D2(disp_b), .D3(disp_c), .D4(disp_d), .D5(disp_e), .D6(disp_f), .D7(disp_g),
    .D8(controlled_buffer_8_out), .WR(address_decode_logic_1_cell_5_w), .RESET(RESET),
    .EN(address_decode_logic_1_cell_5_e), .V1(C5_v1), .V2(C5_v2), .V3(C5_v3), .V4(C5_v4), .V5(C5_v5),
    .V6(C5_v6), .V7(C5_v7), .V8(C5_v8), .CLK(C5_clk), .O8(controlled_buffer_8_out), .O1(disp_a), .O2(disp_b),
    .O3(disp_c), .O4(disp_d), .O5(disp_e), .O6(disp_f), .O7(disp_g));
  LED led_46 (.in(C5_v2));
  LED led_47 (.in(C5_v3));
  LED led_48 (.in(C5_v4));
  LED led_49 (.in(C5_v5));
  LED led_50 (.in(C5_v6));
  LED led_51 (.in(C5_v7));
  LED led_52 (.in(C5_v8));
  LED led_53 (.in(C5_clk));
  LED led_54 (.in(C9_v1));
  Byte_Memory_Module C9 (
    .D1(disp_a), .D2(disp_b), .D3(disp_c), .D4(disp_d), .D5(disp_e), .D6(disp_f), .D7(disp_g),
    .D8(controlled_buffer_8_out), .WR(address_decode_logic_1_cell_9_w), .RESET(RESET),
    .EN(address_decode_logic_1_cell_9_e), .V1(C9_v1), .V2(C9_v2), .V3(C9_v3), .V4(C9_v4), .V5(C9_v5),
    .V6(C9_v6), .V7(C9_v7), .V8(C9_v8), .CLK(C9_clk), .O8(controlled_buffer_8_out), .O1(disp_a), .O2(disp_b),
    .O3(disp_c), .O4(disp_d), .O5(disp_e), .O6(disp_f), .O7(disp_g));
  LED led_55 (.in(C9_v2));
  LED led_56 (.in(C9_v3));
  LED led_57 (.in(C9_v4));
  LED led_58 (.in(C9_v5));
  LED led_59 (.in(C9_v6));
  LED led_60 (.in(C9_v7));
  LED led_61 (.in(C9_v8));
  LED led_62 (.in(C9_clk));
  LED led_63 (.in(C13_v1));
  Byte_Memory_Module C13 (
    .D1(disp_a), .D2(disp_b), .D3(disp_c), .D4(disp_d), .D5(disp_e), .D6(disp_f), .D7(disp_g),
    .D8(controlled_buffer_8_out), .WR(address_decode_logic_1_cell_13_w), .RESET(RESET),
    .EN(address_decode_logic_1_cell_13_e), .V1(C13_v1), .V2(C13_v2), .V3(C13_v3), .V4(C13_v4), .V5(C13_v5),
    .V6(C13_v6), .V7(C13_v7), .V8(C13_v8), .CLK(C13_clk), .O8(controlled_buffer_8_out), .O1(disp_a),
    .O2(disp_b), .O3(disp_c), .O4(disp_d), .O5(disp_e), .O6(disp_f), .O7(disp_g));
  LED led_64 (.in(C13_v2));
  LED led_65 (.in(C13_v3));
  LED led_66 (.in(C13_v4));
  LED led_67 (.in(C13_v5));
  LED led_68 (.in(C13_v6));
  LED led_69 (.in(C13_v7));
  LED led_70 (.in(C13_v8));
  LED led_71 (.in(C13_clk));
  LED led_72 (.in(C2_v1));
  Byte_Memory_Module C2 (
    .D1(disp_a), .D2(disp_b), .D3(disp_c), .D4(disp_d), .D5(disp_e), .D6(disp_f), .D7(disp_g),
    .D8(controlled_buffer_8_out), .WR(address_decode_logic_1_cell_2_w), .RESET(RESET),
    .EN(address_decode_logic_1_cell_2_e), .V1(C2_v1), .V2(C2_v2), .V3(C2_v3), .V4(C2_v4), .V5(C2_v5),
    .V6(C2_v6), .V7(C2_v7), .V8(C2_v8), .CLK(C2_clk), .O8(controlled_buffer_8_out), .O1(disp_a), .O2(disp_b),
    .O3(disp_c), .O4(disp_d), .O5(disp_e), .O6(disp_f), .O7(disp_g));
  LED led_73 (.in(C2_v2));
  LED led_74 (.in(C2_v3));
  LED led_75 (.in(C2_v4));
  LED led_76 (.in(C2_v5));
  LED led_77 (.in(C2_v6));
  LED led_78 (.in(C2_v7));
  LED led_79 (.in(C2_v8));
  LED led_80 (.in(C2_clk));
  LED led_81 (.in(C6_v1));
  Byte_Memory_Module C6 (
    .D1(disp_a), .D2(disp_b), .D3(disp_c), .D4(disp_d), .D5(disp_e), .D6(disp_f), .D7(disp_g),
    .D8(controlled_buffer_8_out), .WR(address_decode_logic_1_cell_6_w), .RESET(RESET),
    .EN(address_decode_logic_1_cell_6_e), .V1(C6_v1), .V2(C6_v2), .V3(C6_v3), .V4(C6_v4), .V5(C6_v5),
    .V6(C6_v6), .V7(C6_v7), .V8(C6_v8), .CLK(C6_clk), .O8(controlled_buffer_8_out), .O1(disp_a), .O2(disp_b),
    .O3(disp_c), .O4(disp_d), .O5(disp_e), .O6(disp_f), .O7(disp_g));
  LED led_82 (.in(C6_v2));
  LED led_83 (.in(C6_v3));
  LED led_84 (.in(C6_v4));
  LED led_85 (.in(C6_v5));
  LED led_86 (.in(C6_v6));
  LED led_87 (.in(C6_v7));
  LED led_88 (.in(C6_v8));
  LED led_89 (.in(C6_clk));
  LED led_90 (.in(C10_v1));
  Byte_Memory_Module C10 (
    .D1(disp_a), .D2(disp_b), .D3(disp_c), .D4(disp_d), .D5(disp_e), .D6(disp_f), .D7(disp_g),
    .D8(controlled_buffer_8_out), .WR(address_decode_logic_1_cell_10_w), .RESET(RESET),
    .EN(address_decode_logic_1_cell_10_e), .V1(C10_v1), .V2(C10_v2), .V3(C10_v3), .V4(C10_v4), .V5(C10_v5),
    .V6(C10_v6), .V7(C10_v7), .V8(C10_v8), .CLK(C10_clk), .O8(controlled_buffer_8_out), .O1(disp_a),
    .O2(disp_b), .O3(disp_c), .O4(disp_d), .O5(disp_e), .O6(disp_f), .O7(disp_g));
  LED led_91 (.in(C10_v2));
  LED led_92 (.in(C10_v3));
  LED led_93 (.in(C10_v4));
  LED led_94 (.in(C10_v5));
  LED led_95 (.in(C10_v6));
  LED led_96 (.in(C10_v7));
  LED led_97 (.in(C10_v8));
  LED led_98 (.in(C10_clk));
  LED led_99 (.in(C14_v1));
  Byte_Memory_Module C14 (
    .D1(disp_a), .D2(disp_b), .D3(disp_c), .D4(disp_d), .D5(disp_e), .D6(disp_f), .D7(disp_g),
    .D8(controlled_buffer_8_out), .WR(address_decode_logic_1_cell_14_w), .RESET(RESET),
    .EN(address_decode_logic_1_cell_14_e), .V1(C14_v1), .V2(C14_v2), .V3(C14_v3), .V4(C14_v4), .V5(C14_v5),
    .V6(C14_v6), .V7(C14_v7), .V8(C14_v8), .CLK(C14_clk), .O8(controlled_buffer_8_out), .O1(disp_a),
    .O2(disp_b), .O3(disp_c), .O4(disp_d), .O5(disp_e), .O6(disp_f), .O7(disp_g));
  LED led_100 (.in(C14_v2));
  LED led_101 (.in(C14_v3));
  LED led_102 (.in(C14_v4));
  LED led_103 (.in(C14_v5));
  LED led_104 (.in(C14_v6));
  LED led_105 (.in(C14_v7));
  LED led_106 (.in(C14_v8));
  LED led_107 (.in(C14_clk));
  LED led_108 (.in(C3_v1));
  Byte_Memory_Module C3 (
    .D1(disp_a), .D2(disp_b), .D3(disp_c), .D4(disp_d), .D5(disp_e), .D6(disp_f), .D7(disp_g),
    .D8(controlled_buffer_8_out), .WR(address_decode_logic_1_cell_3_w), .RESET(RESET),
    .EN(address_decode_logic_1_cell_3_e), .V1(C3_v1), .V2(C3_v2), .V3(C3_v3), .V4(C3_v4), .V5(C3_v5),
    .V6(C3_v6), .V7(C3_v7), .V8(C3_v8), .CLK(C3_clk), .O8(controlled_buffer_8_out), .O1(disp_a), .O2(disp_b),
    .O3(disp_c), .O4(disp_d), .O5(disp_e), .O6(disp_f), .O7(disp_g));
  LED led_109 (.in(C3_v2));
  LED led_110 (.in(C3_v3));
  LED led_111 (.in(C3_v4));
  LED led_112 (.in(C3_v5));
  LED led_113 (.in(C3_v6));
  LED led_114 (.in(C3_v7));
  LED led_115 (.in(C3_v8));
  LED led_116 (.in(C3_clk));
  LED led_117 (.in(C7_v1));
  Byte_Memory_Module C7 (
    .D1(disp_a), .D2(disp_b), .D3(disp_c), .D4(disp_d), .D5(disp_e), .D6(disp_f), .D7(disp_g),
    .D8(controlled_buffer_8_out), .WR(address_decode_logic_1_cell_7_w), .RESET(RESET),
    .EN(address_decode_logic_1_cell_7_e), .V1(C7_v1), .V2(C7_v2), .V3(C7_v3), .V4(C7_v4), .V5(C7_v5),
    .V6(C7_v6), .V7(C7_v7), .V8(C7_v8), .CLK(C7_clk), .O8(controlled_buffer_8_out), .O1(disp_a), .O2(disp_b),
    .O3(disp_c), .O4(disp_d), .O5(disp_e), .O6(disp_f), .O7(disp_g));
  LED led_118 (.in(C7_v2));
  LED led_119 (.in(C7_v3));
  LED led_120 (.in(C7_v4));
  LED led_121 (.in(C7_v5));
  LED led_122 (.in(C7_v6));
  LED led_123 (.in(C7_v7));
  LED led_124 (.in(C7_v8));
  LED led_125 (.in(C7_clk));
  LED led_126 (.in(C11_v1));
  Byte_Memory_Module C11 (
    .D1(disp_a), .D2(disp_b), .D3(disp_c), .D4(disp_d), .D5(disp_e), .D6(disp_f), .D7(disp_g),
    .D8(controlled_buffer_8_out), .WR(address_decode_logic_1_cell_11_w), .RESET(RESET),
    .EN(address_decode_logic_1_cell_11_e), .V1(C11_v1), .V2(C11_v2), .V3(C11_v3), .V4(C11_v4), .V5(C11_v5),
    .V6(C11_v6), .V7(C11_v7), .V8(C11_v8), .CLK(C11_clk), .O8(controlled_buffer_8_out), .O1(disp_a),
    .O2(disp_b), .O3(disp_c), .O4(disp_d), .O5(disp_e), .O6(disp_f), .O7(disp_g));
  LED led_127 (.in(C11_v2));
  LED led_128 (.in(C11_v3));
  LED led_129 (.in(C11_v4));
  LED led_130 (.in(C11_v5));
  LED led_131 (.in(C11_v6));
  LED led_132 (.in(C11_v7));
  LED led_133 (.in(C11_v8));
  LED led_134 (.in(C11_clk));
  LED led_135 (.in(C15_v1));
  Byte_Memory_Module C15 (
    .D1(disp_a), .D2(disp_b), .D3(disp_c), .D4(disp_d), .D5(disp_e), .D6(disp_f), .D7(disp_g),
    .D8(controlled_buffer_8_out), .WR(address_decode_logic_1_cell_15_w), .RESET(RESET),
    .EN(address_decode_logic_1_cell_15_e), .V1(C15_v1), .V2(C15_v2), .V3(C15_v3), .V4(C15_v4), .V5(C15_v5),
    .V6(C15_v6), .V7(C15_v7), .V8(C15_v8), .CLK(C15_clk), .O8(controlled_buffer_8_out), .O1(disp_a),
    .O2(disp_b), .O3(disp_c), .O4(disp_d), .O5(disp_e), .O6(disp_f), .O7(disp_g));
  LED led_136 (.in(C15_v2));
  LED led_137 (.in(C15_v3));
  LED led_138 (.in(C15_v4));
  LED led_139 (.in(C15_v5));
  LED led_140 (.in(C15_v6));
  LED led_141 (.in(C15_v7));
  LED led_142 (.in(C15_v8));
  LED led_143 (.in(C15_clk));

  // Notes on the sheet:
  //   MANUAL PROGRAMMING PINS
endmodule

module Binary2BCD (
  input  I128,
  input  I64,
  input  I32,
  input  I16,
  input  I8,
  input  I4,
  input  I2,
  input  I1,
  output O1_8,
  output O1_4,
  output O1_2,
  output O1_1,
  output O2_8,
  output O2_4,
  output O2_2,
  output O2_1,
  output O3_8,
  output O3_4,
  output O3_2,
  output O3_1
);

  wire and_1_out, and_2_out, and_3_out, and_4_out, and_5_out, and_6_out, and_7_out, nand_1_out, nand_2_out,
       nand_3_out, nand_4_out, nand_5_out, nand_6_out, nand_7_out, nand_8_out, nand_9_out, nand_10_out,
       nand_11_out, nand_12_out, nand_13_out, nand_14_out, nand_15_out, nand_19_out, nand_20_out,
       nand_21_out, nand_22_out, nand_23_out, nand_24_out, nand_25_out, nand_26_out, nand_27_out,
       nand_28_out, nand_29_out, nand_31_out, nand_32_out, nand_33_out, nand_34_out, nand_35_out,
       nand_36_out, nand_37_out, nand_38_out, nand_39_out, nand_40_out, nand_41_out, nand_42_out,
       nand_43_out, nand_44_out, nand_45_out, nand_46_out, nand_47_out, nand_48_out, nand_49_out,
       nand_51_out, nand_52_out, nand_53_out, nand_54_out, nand_55_out, nand_56_out, nand_57_out,
       nand_58_out, nand_59_out, nand_60_out, nand_61_out, nand_62_out, nand_63_out, nand_67_out,
       nand_68_out, nand_69_out, nor_1_out, nor_2_out, nor_3_out, nor_4_out, nor_5_out, nor_6_out, nor_7_out,
       nor_8_out, nor_9_out, nor_10_out, nor_11_out, nor_12_out, nor_13_out, nor_14_out, not_1_out,
       not_2_out, not_3_out, not_4_out, not_5_out, not_6_out, not_7_out, not_8_out, not_9_out, not_10_out,
       not_11_out, not_12_out, not_13_out, not_14_out, or_1_out, or_2_out, or_3_out, or_4_out, or_5_out,
       or_6_out, or_7_out, or_8_out, or_9_out, or_10_out, or_11_out, or_12_out, or_13_out, or_14_out,
       or_15_out, or_16_out, or_17_out, or_18_out, or_19_out, or_20_out, or_21_out, or_22_out, or_23_out,
       or_24_out, or_25_out, or_26_out, or_27_out, or_28_out;

  nand nand_1 (nand_1_out, 1'b0, I32);
  nor nor_1 (nor_1_out, I128, 1'b0);
  and and_1 (and_1_out, I64, I128);
  not not_1 (not_1_out, I32);
  not not_2 (not_2_out, I128);
  nand nand_2 (nand_2_out, nand_62_out, I4);
  nor nor_2 (nor_2_out, nand_61_out, nand_62_out);
  and and_2 (and_2_out, nand_60_out, nand_61_out);
  not not_3 (not_3_out, I4);
  not not_4 (not_4_out, nand_61_out);
  nand nand_3 (nand_3_out, nand_24_out, I2);
  nor nor_3 (nor_3_out, nand_23_out, nand_24_out);
  and and_3 (and_3_out, nand_22_out, nand_23_out);
  not not_5 (not_5_out, I2);
  not not_6 (not_6_out, nand_23_out);
  nand nand_4 (nand_4_out, I128, not_1_out);
  nand nand_5 (nand_5_out, I32, nor_1_out);
  nor nor_4 (nor_4_out, 1'b0, and_1_out);
  nand nand_6 (nand_6_out, not_1_out, 1'b0);
  or or_1 (or_1_out, I64, not_2_out);
  nand nand_7 (nand_7_out, nand_61_out, not_3_out);
  nand nand_8 (nand_8_out, I4, nor_2_out);
  nor nor_5 (nor_5_out, nand_62_out, and_2_out);
  nand nand_9 (nand_9_out, not_3_out, nand_62_out);
  or or_2 (or_2_out, nand_60_out, not_4_out);
  nand nand_10 (nand_10_out, nand_23_out, not_5_out);
  nand nand_11 (nand_11_out, I2, nor_3_out);
  nor nor_6 (nor_6_out, nand_24_out, and_3_out);
  nand nand_12 (nand_12_out, not_5_out, nand_24_out);
  or or_3 (or_3_out, nand_22_out, not_6_out);
  nand nand_13 (nand_13_out, nand_4_out, I64);
  or or_4 (or_4_out, nor_4_out, I32);
  or or_5 (or_5_out, or_1_out, I32);
  nand nand_14 (nand_14_out, nand_7_out, nand_60_out);
  or or_6 (or_6_out, nor_5_out, I4);
  or or_7 (or_7_out, or_2_out, I4);
  nand nand_15 (nand_15_out, nand_10_out, nand_22_out);
  or or_8 (or_8_out, nor_6_out, I2);
  or or_9 (or_9_out, or_3_out, I2);
  nand nand_16 (O3_2, nand_11_out, or_8_out);
  nand nand_17 (O3_4, nand_15_out, nand_12_out);
  nand nand_18 (O3_8, nand_3_out, or_9_out);
  nand nand_19 (nand_19_out, nand_5_out, or_4_out);
  nand nand_20 (nand_20_out, nand_13_out, nand_6_out);
  nand nand_21 (nand_21_out, nand_1_out, or_5_out);
  nand nand_22 (nand_22_out, nand_8_out, or_6_out);
  nand nand_23 (nand_23_out, nand_14_out, nand_9_out);
  nand nand_24 (nand_24_out, nand_2_out, or_7_out);
  or or_10 (or_10_out, nand_19_out, not_1_out);
  nand nand_25 (nand_25_out, nand_19_out, not_1_out);
  or or_11 (or_11_out, nand_22_out, not_3_out);
  nand nand_26 (nand_26_out, nand_22_out, not_3_out);
  or or_12 (or_12_out, O3_2, not_5_out);
  nand nand_27 (nand_27_out, O3_2, not_5_out);
  nand nand_28 (nand_28_out, or_10_out, nand_25_out);
  nand nand_29 (nand_29_out, or_11_out, nand_26_out);
  nand nand_30 (O2_1, or_12_out, nand_27_out);
  nand nand_31 (nand_31_out, nand_21_out, I16);
  nor nor_7 (nor_7_out, nand_20_out, nand_21_out);
  and and_4 (and_4_out, nand_19_out, nand_20_out);
  not not_7 (not_7_out, I16);
  not not_8 (not_8_out, nand_20_out);
  nand nand_32 (nand_32_out, 1'b0, nand_68_out);
  nor nor_8 (nor_8_out, nand_28_out, 1'b0);
  and and_5 (and_5_out, nand_48_out, nand_28_out);
  not not_9 (not_9_out, nand_68_out);
  not not_10 (not_10_out, nand_28_out);
  nand nand_33 (nand_33_out, nand_20_out, not_7_out);
  nand nand_34 (nand_34_out, I16, nor_7_out);
  nor nor_9 (nor_9_out, nand_21_out, and_4_out);
  nand nand_35 (nand_35_out, not_7_out, nand_21_out);
  or or_13 (or_13_out, nand_19_out, not_8_out);
  nand nand_36 (nand_36_out, nand_28_out, not_9_out);
  nand nand_37 (nand_37_out, nand_68_out, nor_8_out);
  nor nor_10 (nor_10_out, 1'b0, and_5_out);
  nand nand_38 (nand_38_out, not_9_out, 1'b0);
  or or_14 (or_14_out, nand_48_out, not_10_out);
  nand nand_39 (nand_39_out, nand_33_out, nand_19_out);
  or or_15 (or_15_out, nor_9_out, I16);
  or or_16 (or_16_out, or_13_out, I16);
  nand nand_40 (nand_40_out, nand_36_out, nand_48_out);
  or or_17 (or_17_out, nor_10_out, nand_68_out);
  or or_18 (or_18_out, or_14_out, nand_68_out);
  nand nand_41 (nand_41_out, nand_34_out, or_15_out);
  nand nand_42 (nand_42_out, nand_39_out, nand_35_out);
  nand nand_43 (nand_43_out, nand_31_out, or_16_out);
  nand nand_44 (nand_44_out, nand_37_out, or_17_out);
  nand nand_45 (nand_45_out, nand_40_out, nand_38_out);
  nand nand_46 (nand_46_out, nand_32_out, or_18_out);
  or or_19 (or_19_out, nand_41_out, not_7_out);
  nand nand_47 (nand_47_out, nand_41_out, not_7_out);
  nand nand_48 (nand_48_out, or_19_out, nand_47_out);
  or or_20 (or_20_out, nand_44_out, not_9_out);
  nand nand_49 (nand_49_out, nand_44_out, not_9_out);
  nand nand_50 (O1_2, or_20_out, nand_49_out);
  nand nand_51 (nand_51_out, nand_43_out, I8);
  nor nor_11 (nor_11_out, nand_42_out, nand_43_out);
  and and_6 (and_6_out, nand_41_out, nand_42_out);
  not not_11 (not_11_out, I8);
  not not_12 (not_12_out, nand_42_out);
  nand nand_52 (nand_52_out, nand_46_out, nand_29_out);
  nor nor_12 (nor_12_out, nand_45_out, nand_46_out);
  and and_7 (and_7_out, nand_44_out, nand_45_out);
  not not_13 (not_13_out, nand_29_out);
  not not_14 (not_14_out, nand_45_out);
  nand nand_53 (nand_53_out, nand_42_out, not_11_out);
  nand nand_54 (nand_54_out, I8, nor_11_out);
  nor nor_13 (nor_13_out, nand_43_out, and_6_out);
  nand nand_55 (nand_55_out, not_11_out, nand_43_out);
  or or_21 (or_21_out, nand_41_out, not_12_out);
  nand nand_56 (nand_56_out, nand_45_out, not_13_out);
  nand nand_57 (nand_57_out, nand_29_out, nor_12_out);
  nor nor_14 (nor_14_out, nand_46_out, and_7_out);
  nand nand_58 (nand_58_out, not_13_out, nand_46_out);
  or or_22 (or_22_out, nand_44_out, not_14_out);
  nand nand_59 (nand_59_out, nand_53_out, nand_41_out);
  or or_23 (or_23_out, nor_13_out, I8);
  or or_24 (or_24_out, or_21_out, I8);
  or or_25 (or_25_out, nor_14_out, nand_29_out);
  or or_26 (or_26_out, or_22_out, nand_29_out);
  nand nand_60 (nand_60_out, nand_54_out, or_23_out);
  nand nand_61 (nand_61_out, nand_59_out, nand_55_out);
  nand nand_62 (nand_62_out, nand_51_out, or_24_out);
  nand nand_63 (nand_63_out, nand_56_out, nand_44_out);
  nand nand_64 (O2_2, nand_57_out, or_25_out);
  nand nand_65 (O2_4, nand_63_out, nand_58_out);
  nand nand_66 (O2_8, nand_52_out, or_26_out);
  or or_27 (or_27_out, nand_60_out, not_11_out);
  nand nand_67 (nand_67_out, nand_60_out, not_11_out);
  or or_28 (or_28_out, O2_2, not_13_out);
  nand nand_68 (nand_68_out, or_27_out, nand_67_out);
  nand nand_69 (nand_69_out, O2_2, not_13_out);
  nand nand_70 (O1_1, or_28_out, nand_69_out);

  assign O3_1 = I1;

  // Notes on the sheet:
  //   DABBLER T
  //   DABBLER D
  //   DABBLER N
  //   D2
  //   T3
  //   T2
  //   T1
  //   T0
  //   D3
  //   D1
  //   D0
  //   N3
  //   N2
  //   N1
  //   N0
  //   DABBLER W
  //   DABBLER K
  //   W2
  //   W1
  //   W3
  //   W0
  //   K3
  //   K2
  //   K1
  //   K0
  //   DABBLER Z
  //   DABBLER M
  //   M1
  //   M0
  //   Z3
  //   Z2
  //   Z1
  //   Z0
  //   M3
  //   M2
endmodule
