// Logisim project Program_Counter.circ as structural Verilog: 1 circuit, main circuit main
module main (
  input  RESET,
  input  D1,
  input  D2,
  input  D3,
  input  D4,
  input  in_6,
  input  BUS_LOAD,
  input  BUS_ENABLE
);

  wire clock_1_out, n74161_1_pin11, n74161_1_pin12, n74161_1_pin13, n74161_1_pin14, n74245_1_pin1,
       n74245_1_pin15, n74245_1_pin16, n74245_1_pin17, n74245_1_pin18, not_1_out, not_2_out, not_3_out;

  Clock clock_1 (.out(clock_1_out));
  not not_1 (not_1_out, RESET);
  not not_2 (not_2_out, BUS_LOAD);
  not not_3 (not_3_out, BUS_ENABLE);
  _74161 u_74161_1 (
    .pin1(not_1_out), .pin2(clock_1_out), .pin3(D1), .pin4(D2), .pin5(D3), .pin6(D4), .pin7(in_6),
    .pin14(n74161_1_pin14), .pin13(n74161_1_pin13), .pin12(n74161_1_pin12), .pin11(n74161_1_pin11),
    .pin10(in_6), .pin9(not_2_out));  // open: pin15
  LED led_1 (.in(n74161_1_pin11));
  LED led_2 (.in(n74161_1_pin12));
  LED led_3 (.in(n74161_1_pin13));
  LED led_4 (.in(n74161_1_pin14));
  LED led_5 (.in(n74245_1_pin15));
  _74245 u_74245_1 (
    .pin1(n74245_1_pin1), .pin2(n74161_1_pin14), .pin3(n74161_1_pin13), .pin4(n74161_1_pin12),
    .pin5(n74161_1_pin11), .pin19(not_3_out), .pin18(n74245_1_pin18), .pin17(n74245_1_pin17),
    .pin16(n74245_1_pin16), .pin15(n74245_1_pin15));  // open: pin6, pin7, pin8, pin9, pin14, pin13, pin12, pin11
  LED led_6 (.in(n74245_1_pin16));
  LED led_7 (.in(n74245_1_pin17));
  LED led_8 (.in(n74245_1_pin18));
  // also tied to VCC on the sheet: n74245_1_pin1

  // Notes on the sheet:
  //   BUS
  //   CTR_ENABLE
  //   BUS
endmodule
