// Logisim project Random_Access_Memory.circ as structural Verilog: 2 circuits, main circuit main
module main (
  input  in_1,
  input  in_2,
  input  in_3,
  input  in_4,
  input  in_5,
  input  in_6,
  input  in_7,
  input  in_8,
  input  in_9,
  input  in_10,
  input  in_11,
  input  in_12,
  input  in_13,
  input  in_14,
  input  in_15,
  input  in_16,
  input  in_17,
  input  in_18,
  input  in_19,
  input  in_20,
  input  in_21,
  input  in_22,
  input  in_23,
  input  in_24,
  input  in_25,
  input  in_26,
  input  in_27,
  input  in_28,
  input  in_29,
  input  in_30,
  input  in_31,
  input  in_32,
  input  in_33,
  input  in_34,
  input  in_35,
  input  in_36,
  input  in_37,
  input  in_38,
  input  in_39,
  input  in_40,
  input  in_41,
  input  in_42,
  input  in_43,
  input  in_44,
  input  in_45,
  input  in_46,
  input  in_47,
  input  in_48,
  input  in_49,
  input  in_50,
  input  in_51,
  input  in_52,
  input  in_53,
  input  in_54,
  input  in_55,
  input  in_56,
  input  in_57
);

  wire byte_memory_module_1_clk, byte_memory_module_1_v1, byte_memory_module_1_v2, byte_memory_module_1_v3,
       byte_memory_module_1_v4, byte_memory_module_1_v5, byte_memory_module_1_v6, byte_memory_module_1_v7,
       byte_memory_module_1_v8, byte_memory_module_2_clk, byte_memory_module_2_v1, byte_memory_module_2_v2,
       byte_memory_module_2_v3, byte_memory_module_2_v4, byte_memory_module_2_v5, byte_memory_module_2_v6,
       byte_memory_module_2_v7, byte_memory_module_2_v8, byte_memory_module_3_clk, byte_memory_module_3_v1,
       byte_memory_module_3_v2, byte_memory_module_3_v3, byte_memory_module_3_v4, byte_memory_module_3_v5,
       byte_memory_module_3_v6, byte_memory_module_3_v7, byte_memory_module_3_v8, byte_memory_module_4_clk,
       byte_memory_module_4_v1, byte_memory_module_4_v2, byte_memory_module_4_v3, byte_memory_module_4_v4,
       byte_memory_module_4_v5, byte_memory_module_4_v6, byte_memory_module_4_v7, byte_memory_module_4_v8,
       byte_memory_module_5_clk, byte_memory_module_5_v1, byte_memory_module_5_v2, byte_memory_module_5_v3,
       byte_memory_module_5_v4, byte_memory_module_5_v5, byte_memory_module_5_v6, byte_memory_module_5_v7,
       byte_memory_module_5_v8, byte_memory_module_6_clk, byte_memory_module_6_v1, byte_memory_module_6_v2,
       byte_memory_module_6_v3, byte_memory_module_6_v4, byte_memory_module_6_v5, byte_memory_module_6_v6,
       byte_memory_module_6_v7, byte_memory_module_6_v8, byte_memory_module_7_clk, byte_memory_module_7_v1,
       byte_memory_module_7_v2, byte_memory_module_7_v3, byte_memory_module_7_v4, byte_memory_module_7_v5,
       byte_memory_module_7_v6, byte_memory_module_7_v7, byte_memory_module_7_v8, byte_memory_module_8_clk,
       byte_memory_module_8_v1, byte_memory_module_8_v2, byte_memory_module_8_v3, byte_memory_module_8_v4,
       byte_memory_module_8_v5, byte_memory_module_8_v6, byte_memory_module_8_v7, byte_memory_module_8_v8,
       byte_memory_module_9_clk, byte_memory_module_9_v1, byte_memory_module_9_v2, byte_memory_module_9_v3,
       byte_memory_module_9_v4, byte_memory_module_9_v5, byte_memory_module_9_v6, byte_memory_module_9_v7,
       byte_memory_module_9_v8, byte_memory_module_10_clk, byte_memory_module_10_v1,
       byte_memory_module_10_v2, byte_memory_module_10_v3, byte_memory_module_10_v4,
       byte_memory_module_10_v5, byte_memory_module_10_v6, byte_memory_module_10_v7,
       byte_memory_module_10_v8, byte_memory_module_11_clk, byte_memory_module_11_v1,
       byte_memory_module_11_v2, byte_memory_module_11_v3, byte_memory_module_11_v4,
       byte_memory_module_11_v5, byte_memory_module_11_v6, byte_memory_module_11_v7,
       byte_memory_module_11_v8, byte_memory_module_12_clk, byte_memory_module_12_v1,
       byte_memory_module_12_v2, byte_memory_module_12_v3, byte_memory_module_12_v4,
       byte_memory_module_12_v5, byte_memory_module_12_v6, byte_memory_module_12_v7,
       byte_memory_module_12_v8, byte_memory_module_13_clk, byte_memory_module_13_v1,
       byte_memory_module_13_v2, byte_memory_module_13_v3, byte_memory_module_13_v4,
       byte_memory_module_13_v5, byte_memory_module_13_v6, byte_memory_module_13_v7,
       byte_memory_module_13_v8, byte_memory_module_14_clk, byte_memory_module_14_v1,
       byte_memory_module_14_v2, byte_memory_module_14_v3, byte_memory_module_14_v4,
       byte_memory_module_14_v5, byte_memory_module_14_v6, byte_memory_module_14_v7,
       byte_memory_module_14_v8, byte_memory_module_15_clk, byte_memory_module_15_v1,
       byte_memory_module_15_v2, byte_memory_module_15_v3, byte_memory_module_15_v4,
       byte_memory_module_15_v5, byte_memory_module_15_v6, byte_memory_module_15_v7,
       byte_memory_module_15_v8, byte_memory_module_16_clk, byte_memory_module_16_v1,
       byte_memory_module_16_v2, byte_memory_module_16_v3, byte_memory_module_16_v4,
       byte_memory_module_16_v5, byte_memory_module_16_v6, byte_memory_module_16_v7,
       byte_memory_module_16_v8, controlled_buffer_1_out, controlled_buffer_2_out, controlled_buffer_3_out,
       controlled_buffer_4_out, controlled_buffer_5_out, controlled_buffer_6_out, controlled_buffer_7_out,
       controlled_buffer_8_out;

  assign controlled_buffer_1_out = in_9 ? in_1 : 1'bz;  // Controlled_Buffer controlled_buffer_1
  assign controlled_buffer_2_out = in_9 ? in_2 : 1'bz;  // Controlled_Buffer controlled_buffer_2
  assign controlled_buffer_3_out = in_9 ? in_3 : 1'bz;  // Controlled_Buffer controlled_buffer_3
  assign controlled_buffer_4_out = in_9 ? in_4 : 1'bz;  // Controlled_Buffer controlled_buffer_4
  assign controlled_buffer_5_out = in_9 ? in_5 : 1'bz;  // Controlled_Buffer controlled_buffer_5
  assign controlled_buffer_6_out = in_9 ? in_6 : 1'bz;  // Controlled_Buffer controlled_buffer_6
  assign controlled_buffer_7_out = in_9 ? in_7 : 1'bz;  // Controlled_Buffer controlled_buffer_7
  assign controlled_buffer_8_out = in_9 ? in_8 : 1'bz;  // Controlled_Buffer controlled_buffer_8
  LED led_1 (.in(byte_memory_module_1_v1));
  Byte_Memory_Module byte_memory_module_1 (
    .D1(controlled_buffer_1_out), .D2(controlled_buffer_2_out), .D3(controlled_buffer_3_out),
    .D4(controlled_buffer_4_out), .D5(controlled_buffer_5_out), .D6(controlled_buffer_6_out),
    .D7(controlled_buffer_7_out), .D8(controlled_buffer_8_out), .WR(in_10), .RESET(in_14), .EN(in_18),
    .V1(byte_memory_module_1_v1), .V2(byte_memory_module_1_v2), .V3(byte_memory_module_1_v3),
    .V4(byte_memory_module_1_v4), .V5(byte_memory_module_1_v5), .V6(byte_memory_module_1_v6),
    .V7(byte_memory_module_1_v7), .V8(byte_memory_module_1_v8), .CLK(byte_memory_module_1_clk),
    .O8(controlled_buffer_8_out), .O1(controlled_buffer_1_out), .O2(controlled_buffer_2_out),
    .O3(controlled_buffer_3_out), .O4(controlled_buffer_4_out), .O5(controlled_buffer_5_out),
    .O6(controlled_buffer_6_out), .O7(controlled_buffer_7_out));
  LED led_2 (.in(byte_memory_module_1_v2));
  LED led_3 (.in(byte_memory_module_1_v3));
  LED led_4 (.in(byte_memory_module_1_v4));
  LED led_5 (.in(byte_memory_module_1_v5));
  LED led_6 (.in(byte_memory_module_1_v6));
  LED led_7 (.in(byte_memory_module_1_v7));
  LED led_8 (.in(byte_memory_module_1_v8));
  LED led_9 (.in(byte_memory_module_1_clk));
  LED led_10 (.in(byte_memory_module_2_v1));
  Byte_Memory_Module byte_memory_module_2 (
    .D1(controlled_buffer_1_out), .D2(controlled_buffer_2_out), .D3(controlled_buffer_3_out),
    .D4(controlled_buffer_4_out), .D5(controlled_buffer_5_out), .D6(controlled_buffer_6_out),
    .D7(controlled_buffer_7_out), .D8(controlled_buffer_8_out), .WR(in_22), .RESET(in_26), .EN(in_30),
    .V1(byte_memory_module_2_v1), .V2(byte_memory_module_2_v2), .V3(byte_memory_module_2_v3),
    .V4(byte_memory_module_2_v4), .V5(byte_memory_module_2_v5), .V6(byte_memory_module_2_v6),
    .V7(byte_memory_module_2_v7), .V8(byte_memory_module_2_v8), .CLK(byte_memory_module_2_clk),
    .O8(controlled_buffer_8_out), .O1(controlled_buffer_1_out), .O2(controlled_buffer_2_out),
    .O3(controlled_buffer_3_out), .O4(controlled_buffer_4_out), .O5(controlled_buffer_5_out),
    .O6(controlled_buffer_6_out), .O7(controlled_buffer_7_out));
  LED led_11 (.in(byte_memory_module_2_v2));
  LED led_12 (.in(byte_memory_module_2_v3));
  LED led_13 (.in(byte_memory_module_2_v4));
  LED led_14 (.in(byte_memory_module_2_v5));
  LED led_15 (.in(byte_memory_module_2_v6));
  LED led_16 (.in(byte_memory_module_2_v7));
  LED led_17 (.in(byte_memory_module_2_v8));
  LED led_18 (.in(byte_memory_module_2_clk));
  LED led_19 (.in(byte_memory_module_3_v1));
  Byte_Memory_Module byte_memory_module_3 (
    .D1(controlled_buffer_1_out), .D2(controlled_buffer_2_out), .D3(controlled_buffer_3_out),
    .D4(controlled_buffer_4_out), .D5(controlled_buffer_5_out), .D6(controlled_buffer_6_out),
    .D7(controlled_buffer_7_out), .D8(controlled_buffer_8_out), .WR(in_34), .RESET(in_38), .EN(in_42),
    .V1(byte_memory_module_3_v1), .V2(byte_memory_module_3_v2), .V3(byte_memory_module_3_v3),
    .V4(byte_memory_module_3_v4), .V5(byte_memory_module_3_v5), .V6(byte_memory_module_3_v6),
    .V7(byte_memory_module_3_v7), .V8(byte_memory_module_3_v8), .CLK(byte_memory_module_3_clk),
    .O8(controlled_buffer_8_out), .O1(controlled_buffer_1_out), .O2(controlled_buffer_2_out),
    .O3(controlled_buffer_3_out), .O4(controlled_buffer_4_out), .O5(controlled_buffer_5_out),
    .O6(controlled_buffer_6_out), .O7(controlled_buffer_7_out));
  LED led_20 (.in(byte_memory_module_3_v2));
  LED led_21 (.in(byte_memory_module_3_v3));
  LED led_22 (.in(byte_memory_module_3_v4));
  LED led_23 (.in(byte_memory_module_3_v5));
  LED led_24 (.in(byte_memory_module_3_v6));
  LED led_25 (.in(byte_memory_module_3_v7));
  LED led_26 (.in(byte_memory_module_3_v8));
  LED led_27 (.in(byte_memory_module_3_clk));
  LED led_28 (.in(byte_memory_module_4_v1));
  Byte_Memory_Module byte_memory_module_4 (
    .D1(controlled_buffer_1_out), .D2(controlled_buffer_2_out), .D3(controlled_buffer_3_out),
    .D4(controlled_buffer_4_out), .D5(controlled_buffer_5_out), .D6(controlled_buffer_6_out),
    .D7(controlled_buffer_7_out), .D8(controlled_buffer_8_out), .WR(in_46), .RESET(in_50), .EN(in_54),
    .V1(byte_memory_module_4_v1), .V2(byte_memory_module_4_v2), .V3(byte_memory_module_4_v3),
    .V4(byte_memory_module_4_v4), .V5(byte_memory_module_4_v5), .V6(byte_memory_module_4_v6),
    .V7(byte_memory_module_4_v7), .V8(byte_memory_module_4_v8), .CLK(byte_memory_module_4_clk),
    .O8(controlled_buffer_8_out), .O1(controlled_buffer_1_out), .O2(controlled_buffer_2_out),
    .O3(controlled_buffer_3_out), .O4(controlled_buffer_4_out), .O5(controlled_buffer_5_out),
    .O6(controlled_buffer_6_out), .O7(controlled_buffer_7_out));
  LED led_29 (.in(byte_memory_module_4_v2));
  LED led_30 (.in(byte_memory_module_4_v3));
  LED led_31 (.in(byte_memory_module_4_v4));
  LED led_32 (.in(byte_memory_module_4_v5));
  LED led_33 (.in(byte_memory_module_4_v6));
  LED led_34 (.in(byte_memory_module_4_v7));
  LED led_35 (.in(byte_memory_module_4_v8));
  LED led_36 (.in(byte_memory_module_4_clk));
  LED led_37 (.in(byte_memory_module_5_v1));
  Byte_Memory_Module byte_memory_module_5 (
    .D1(controlled_buffer_1_out), .D2(controlled_buffer_2_out), .D3(controlled_buffer_3_out),
    .D4(controlled_buffer_4_out), .D5(controlled_buffer_5_out), .D6(controlled_buffer_6_out),
    .D7(controlled_buffer_7_out), .D8(controlled_buffer_8_out), .WR(in_11), .RESET(in_15), .EN(in_19),
    .V1(byte_memory_module_5_v1), .V2(byte_memory_module_5_v2), .V3(byte_memory_module_5_v3),
    .V4(byte_memory_module_5_v4), .V5(byte_memory_module_5_v5), .V6(byte_memory_module_5_v6),
    .V7(byte_memory_module_5_v7), .V8(byte_memory_module_5_v8), .CLK(byte_memory_module_5_clk),
    .O8(controlled_buffer_8_out), .O1(controlled_buffer_1_out), .O2(controlled_buffer_2_out),
    .O3(controlled_buffer_3_out), .O4(controlled_buffer_4_out), .O5(controlled_buffer_5_out),
    .O6(controlled_buffer_6_out), .O7(controlled_buffer_7_out));
  LED led_38 (.in(byte_memory_module_5_v2));
  LED led_39 (.in(byte_memory_module_5_v3));
  LED led_40 (.in(byte_memory_module_5_v4));
  LED led_41 (.in(byte_memory_module_5_v5));
  LED led_42 (.in(byte_memory_module_5_v6));
  LED led_43 (.in(byte_memory_module_5_v7));
  LED led_44 (.in(byte_memory_module_5_v8));
  LED led_45 (.in(byte_memory_module_5_clk));
  LED led_46 (.in(byte_memory_module_6_v1));
  Byte_Memory_Module byte_memory_module_6 (
    .D1(controlled_buffer_1_out), .D2(controlled_buffer_2_out), .D3(controlled_buffer_3_out),
    .D4(controlled_buffer_4_out), .D5(controlled_buffer_5_out), .D6(controlled_buffer_6_out),
    .D7(controlled_buffer_7_out), .D8(controlled_buffer_8_out), .WR(in_23), .RESET(in_27), .EN(in_31),
    .V1(byte_memory_module_6_v1), .V2(byte_memory_module_6_v2), .V3(byte_memory_module_6_v3),
    .V4(byte_memory_module_6_v4), .V5(byte_memory_module_6_v5), .V6(byte_memory_module_6_v6),
    .V7(byte_memory_module_6_v7), .V8(byte_memory_module_6_v8), .CLK(byte_memory_module_6_clk),
    .O8(controlled_buffer_8_out), .O1(controlled_buffer_1_out), .O2(controlled_buffer_2_out),
    .O3(controlled_buffer_3_out), .O4(controlled_buffer_4_out), .O5(controlled_buffer_5_out),
    .O6(controlled_buffer_6_out), .O7(controlled_buffer_7_out));
  LED led_47 (.in(byte_memory_module_6_v2));
  LED led_48 (.in(byte_memory_module_6_v3));
  LED led_49 (.in(byte_memory_module_6_v4));
  LED led_50 (.in(byte_memory_module_6_v5));
  LED led_51 (.in(byte_memory_module_6_v6));
  LED led_52 (.in(byte_memory_module_6_v7));
  LED led_53 (.in(byte_memory_module_6_v8));
  LED led_54 (.in(byte_memory_module_6_clk));
  LED led_55 (.in(byte_memory_module_7_v1));
  Byte_Memory_Module byte_memory_module_7 (
    .D1(controlled_buffer_1_out), .D2(controlled_buffer_2_out), .D3(controlled_buffer_3_out),
    .D4(controlled_buffer_4_out), .D5(controlled_buffer_5_out), .D6(controlled_buffer_6_out),
    .D7(controlled_buffer_7_out), .D8(controlled_buffer_8_out), .WR(in_35), .RESET(in_39), .EN(in_43),
    .V1(byte_memory_module_7_v1), .V2(byte_memory_module_7_v2), .V3(byte_memory_module_7_v3),
    .V4(byte_memory_module_7_v4), .V5(byte_memory_module_7_v5), .V6(byte_memory_module_7_v6),
    .V7(byte_memory_module_7_v7), .V8(byte_memory_module_7_v8), .CLK(byte_memory_module_7_clk),
    .O8(controlled_buffer_8_out), .O1(controlled_buffer_1_out), .O2(controlled_buffer_2_out),
    .O3(controlled_buffer_3_out), .O4(controlled_buffer_4_out), .O5(controlled_buffer_5_out),
    .O6(controlled_buffer_6_out), .O7(controlled_buffer_7_out));
  LED led_56 (.in(byte_memory_module_7_v2));
  LED led_57 (.in(byte_memory_module_7_v3));
  LED led_58 (.in(byte_memory_module_7_v4));
  LED led_59 (.in(byte_memory_module_7_v5));
  LED led_60 (.in(byte_memory_module_7_v6));
  LED led_61 (.in(byte_memory_module_7_v7));
  LED led_62 (.in(byte_memory_module_7_v8));
  LED led_63 (.in(byte_memory_module_7_clk));
  LED led_64 (.in(byte_memory_module_8_v1));
  Byte_Memory_Module byte_memory_module_8 (
    .D1(controlled_buffer_1_out), .D2(controlled_buffer_2_out), .D3(controlled_buffer_3_out),
    .D4(controlled_buffer_4_out), .D5(controlled_buffer_5_out), .D6(controlled_buffer_6_out),
    .D7(controlled_buffer_7_out), .D8(controlled_buffer_8_out), .WR(in_47), .RESET(in_51), .EN(in_55),
    .V1(byte_memory_module_8_v1), .V2(byte_memory_module_8_v2), .V3(byte_memory_module_8_v3),
    .V4(byte_memory_module_8_v4), .V5(byte_memory_module_8_v5), .V6(byte_memory_module_8_v6),
    .V7(byte_memory_module_8_v7), .V8(byte_memory_module_8_v8), .CLK(byte_memory_module_8_clk),
    .O8(controlled_buffer_8_out), .O1(controlled_buffer_1_out), .O2(controlled_buffer_2_out),
    .O3(controlled_buffer_3_out), .O4(controlled_buffer_4_out), .O5(controlled_buffer_5_out),
    .O6(controlled_buffer_6_out), .O7(controlled_buffer_7_out));
  LED led_65 (.in(byte_memory_module_8_v2));
  LED led_66 (.in(byte_memory_module_8_v3));
  LED led_67 (.in(byte_memory_module_8_v4));
  LED led_68 (.in(byte_memory_module_8_v5));
  LED led_69 (.in(byte_memory_module_8_v6));
  LED led_70 (.in(byte_memory_module_8_v7));
  LED led_71 (.in(byte_memory_module_8_v8));
  LED led_72 (.in(byte_memory_module_8_clk));
  LED led_73 (.in(byte_memory_module_9_v1));
  Byte_Memory_Module byte_memory_module_9 (
    .D1(controlled_buffer_1_out), .D2(controlled_buffer_2_out), .D3(controlled_buffer_3_out),
    .D4(controlled_buffer_4_out), .D5(controlled_buffer_5_out), .D6(controlled_buffer_6_out),
    .D7(controlled_buffer_7_out), .D8(controlled_buffer_8_out), .WR(in_12), .RESET(in_16), .EN(in_20),
    .V1(byte_memory_module_9_v1), .V2(byte_memory_module_9_v2), .V3(byte_memory_module_9_v3),
    .V4(byte_memory_module_9_v4), .V5(byte_memory_module_9_v5), .V6(byte_memory_module_9_v6),
    .V7(byte_memory_module_9_v7), .V8(byte_memory_module_9_v8), .CLK(byte_memory_module_9_clk),
    .O8(controlled_buffer_8_out), .O1(controlled_buffer_1_out), .O2(controlled_buffer_2_out),
    .O3(controlled_buffer_3_out), .O4(controlled_buffer_4_out), .O5(controlled_buffer_5_out),
    .O6(controlled_buffer_6_out), .O7(controlled_buffer_7_out));
  LED led_74 (.in(byte_memory_module_9_v2));
  LED led_75 (.in(byte_memory_module_9_v3));
  LED led_76 (.in(byte_memory_module_9_v4));
  LED led_77 (.in(byte_memory_module_9_v5));
  LED led_78 (.in(byte_memory_module_9_v6));
  LED led_79 (.in(byte_memory_module_9_v7));
  LED led_80 (.in(byte_memory_module_9_v8));
  LED led_81 (.in(byte_memory_module_9_clk));
  LED led_82 (.in(byte_memory_module_10_v1));
  Byte_Memory_Module byte_memory_module_10 (
    .D1(controlled_buffer_1_out), .D2(controlled_buffer_2_out), .D3(controlled_buffer_3_out),
    .D4(controlled_buffer_4_out), .D5(controlled_buffer_5_out), .D6(controlled_buffer_6_out),
    .D7(controlled_buffer_7_out), .D8(controlled_buffer_8_out), .WR(in_24), .RESET(in_28), .EN(in_32),
    .V1(byte_memory_module_10_v1), .V2(byte_memory_module_10_v2), .V3(byte_memory_module_10_v3),
    .V4(byte_memory_module_10_v4), .V5(byte_memory_module_10_v5), .V6(byte_memory_module_10_v6),
    .V7(byte_memory_module_10_v7), .V8(byte_memory_module_10_v8), .CLK(byte_memory_module_10_clk),
    .O8(controlled_buffer_8_out), .O1(controlled_buffer_1_out), .O2(controlled_buffer_2_out),
    .O3(controlled_buffer_3_out), .O4(controlled_buffer_4_out), .O5(controlled_buffer_5_out),
    .O6(controlled_buffer_6_out), .O7(controlled_buffer_7_out));
  LED led_83 (.in(byte_memory_module_10_v2));
  LED led_84 (.in(byte_memory_module_10_v3));
  LED led_85 (.in(byte_memory_module_10_v4));
  LED led_86 (.in(byte_memory_module_10_v5));
  LED led_87 (.in(byte_memory_module_10_v6));
  LED led_88 (.in(byte_memory_module_10_v7));
  LED led_89 (.in(byte_memory_module_10_v8));
  LED led_90 (.in(byte_memory_module_10_clk));
  LED led_91 (.in(byte_memory_module_11_v1));
  Byte_Memory_Module byte_memory_module_11 (
    .D1(controlled_buffer_1_out), .D2(controlled_buffer_2_out), .D3(controlled_buffer_3_out),
    .D4(controlled_buffer_4_out), .D5(controlled_buffer_5_out), .D6(controlled_buffer_6_out),
    .D7(controlled_buffer_7_out), .D8(controlled_buffer_8_out), .WR(in_36), .RESET(in_40), .EN(in_44),
    .V1(byte_memory_module_11_v1), .V2(byte_memory_module_11_v2), .V3(byte_memory_module_11_v3),
    .V4(byte_memory_module_11_v4), .V5(byte_memory_module_11_v5), .V6(byte_memory_module_11_v6),
    .V7(byte_memory_module_11_v7), .V8(byte_memory_module_11_v8), .CLK(byte_memory_module_11_clk),
    .O8(controlled_buffer_8_out), .O1(controlled_buffer_1_out), .O2(controlled_buffer_2_out),
    .O3(controlled_buffer_3_out), .O4(controlled_buffer_4_out), .O5(controlled_buffer_5_out),
    .O6(controlled_buffer_6_out), .O7(controlled_buffer_7_out));
  LED led_92 (.in(byte_memory_module_11_v2));
  LED led_93 (.in(byte_memory_module_11_v3));
  LED led_94 (.in(byte_memory_module_11_v4));
  LED led_95 (.in(byte_memory_module_11_v5));
  LED led_96 (.in(byte_memory_module_11_v6));
  LED led_97 (.in(byte_memory_module_11_v7));
  LED led_98 (.in(byte_memory_module_11_v8));
  LED led_99 (.in(byte_memory_module_11_clk));
  LED led_100 (.in(byte_memory_module_12_v1));
  Byte_Memory_Module byte_memory_module_12 (
    .D1(controlled_buffer_1_out), .D2(controlled_buffer_2_out), .D3(controlled_buffer_3_out),
    .D4(controlled_buffer_4_out), .D5(controlled_buffer_5_out), .D6(controlled_buffer_6_out),
    .D7(controlled_buffer_7_out), .D8(controlled_buffer_8_out), .WR(in_48), .RESET(in_52), .EN(in_56),
    .V1(byte_memory_module_12_v1), .V2(byte_memory_module_12_v2), .V3(byte_memory_module_12_v3),
    .V4(byte_memory_module_12_v4), .V5(byte_memory_module_12_v5), .V6(byte_memory_module_12_v6),
    .V7(byte_memory_module_12_v7), .V8(byte_memory_module_12_v8), .CLK(byte_memory_module_12_clk),
    .O8(controlled_buffer_8_out), .O1(controlled_buffer_1_out), .O2(controlled_buffer_2_out),
    .O3(controlled_buffer_3_out), .O4(controlled_buffer_4_out), .O5(controlled_buffer_5_out),
    .O6(controlled_buffer_6_out), .O7(controlled_buffer_7_out));
  LED led_101 (.in(byte_memory_module_12_v2));
  LED led_102 (.in(byte_memory_module_12_v3));
  LED led_103 (.in(byte_memory_module_12_v4));
  LED led_104 (.in(byte_memory_module_12_v5));
  LED led_105 (.in(byte_memory_module_12_v6));
  LED led_106 (.in(byte_memory_module_12_v7));
  LED led_107 (.in(byte_memory_module_12_v8));
  LED led_108 (.in(byte_memory_module_12_clk));
  LED led_109 (.in(byte_memory_module_13_v1));
  Byte_Memory_Module byte_memory_module_13 (
    .D1(controlled_buffer_1_out), .D2(controlled_buffer_2_out), .D3(controlled_buffer_3_out),
    .D4(controlled_buffer_4_out), .D5(controlled_buffer_5_out), .D6(controlled_buffer_6_out),
    .D7(controlled_buffer_7_out), .D8(controlled_buffer_8_out), .WR(in_13), .RESET(in_17), .EN(in_21),
    .V1(byte_memory_module_13_v1), .V2(byte_memory_module_13_v2), .V3(byte_memory_module_13_v3),
    .V4(byte_memory_module_13_v4), .V5(byte_memory_module_13_v5), .V6(byte_memory_module_13_v6),
    .V7(byte_memory_module_13_v7), .V8(byte_memory_module_13_v8), .CLK(byte_memory_module_13_clk),
    .O8(controlled_buffer_8_out), .O1(controlled_buffer_1_out), .O2(controlled_buffer_2_out),
    .O3(controlled_buffer_3_out), .O4(controlled_buffer_4_out), .O5(controlled_buffer_5_out),
    .O6(controlled_buffer_6_out), .O7(controlled_buffer_7_out));
  LED led_110 (.in(byte_memory_module_13_v2));
  LED led_111 (.in(byte_memory_module_13_v3));
  LED led_112 (.in(byte_memory_module_13_v4));
  LED led_113 (.in(byte_memory_module_13_v5));
  LED led_114 (.in(byte_memory_module_13_v6));
  LED led_115 (.in(byte_memory_module_13_v7));
  LED led_116 (.in(byte_memory_module_13_v8));
  LED led_117 (.in(byte_memory_module_13_clk));
  LED led_118 (.in(byte_memory_module_14_v1));
  Byte_Memory_Module byte_memory_module_14 (
    .D1(controlled_buffer_1_out), .D2(controlled_buffer_2_out), .D3(controlled_buffer_3_out),
    .D4(controlled_buffer_4_out), .D5(controlled_buffer_5_out), .D6(controlled_buffer_6_out),
    .D7(controlled_buffer_7_out), .D8(controlled_buffer_8_out), .WR(in_25), .RESET(in_29), .EN(in_33),
    .V1(byte_memory_module_14_v1), .V2(byte_memory_module_14_v2), .V3(byte_memory_module_14_v3),
    .V4(byte_memory_module_14_v4), .V5(byte_memory_module_14_v5), .V6(byte_memory_module_14_v6),
    .V7(byte_memory_module_14_v7), .V8(byte_memory_module_14_v8), .CLK(byte_memory_module_14_clk),
    .O8(controlled_buffer_8_out), .O1(controlled_buffer_1_out), .O2(controlled_buffer_2_out),
    .O3(controlled_buffer_3_out), .O4(controlled_buffer_4_out), .O5(controlled_buffer_5_out),
    .O6(controlled_buffer_6_out), .O7(controlled_buffer_7_out));
  LED led_119 (.in(byte_memory_module_14_v2));
  LED led_120 (.in(byte_memory_module_14_v3));
  LED led_121 (.in(byte_memory_module_14_v4));
  LED led_122 (.in(byte_memory_module_14_v5));
  LED led_123 (.in(byte_memory_module_14_v6));
  LED led_124 (.in(byte_memory_module_14_v7));
  LED led_125 (.in(byte_memory_module_14_v8));
  LED led_126 (.in(byte_memory_module_14_clk));
  LED led_127 (.in(byte_memory_module_15_v1));
  Byte_Memory_Module byte_memory_module_15 (
    .D1(controlled_buffer_1_out), .D2(controlled_buffer_2_out), .D3(controlled_buffer_3_out),
    .D4(controlled_buffer_4_out), .D5(controlled_buffer_5_out), .D6(controlled_buffer_6_out),
    .D7(controlled_buffer_7_out), .D8(controlled_buffer_8_out), .WR(in_37), .RESET(in_41), .EN(in_45),
    .V1(byte_memory_module_15_v1), .V2(byte_memory_module_15_v2), .V3(byte_memory_module_15_v3),
    .V4(byte_memory_module_15_v4), .V5(byte_memory_module_15_v5), .V6(byte_memory_module_15_v6),
    .V7(byte_memory_module_15_v7), .V8(byte_memory_module_15_v8), .CLK(byte_memory_module_15_clk),
    .O8(controlled_buffer_8_out), .O1(controlled_buffer_1_out), .O2(controlled_buffer_2_out),
    .O3(controlled_buffer_3_out), .O4(controlled_buffer_4_out), .O5(controlled_buffer_5_out),
    .O6(controlled_buffer_6_out), .O7(controlled_buffer_7_out));
  LED led_128 (.in(byte_memory_module_15_v2));
  LED led_129 (.in(byte_memory_module_15_v3));
  LED led_130 (.in(byte_memory_module_15_v4));
  LED led_131 (.in(byte_memory_module_15_v5));
  LED led_132 (.in(byte_memory_module_15_v6));
  LED led_133 (.in(byte_memory_module_15_v7));
  LED led_134 (.in(byte_memory_module_15_v8));
  LED led_135 (.in(byte_memory_module_15_clk));
  LED led_136 (.in(byte_memory_module_16_v1));
  Byte_Memory_Module byte_memory_module_16 (
    .D1(controlled_buffer_1_out), .D2(controlled_buffer_2_out), .D3(controlled_buffer_3_out),
    .D4(controlled_buffer_4_out), .D5(controlled_buffer_5_out), .D6(controlled_buffer_6_out),
    .D7(controlled_buffer_7_out), .D8(controlled_buffer_8_out), .WR(in_49), .RESET(in_53), .EN(in_57),
    .V1(byte_memory_module_16_v1), .V2(byte_memory_module_16_v2), .V3(byte_memory_module_16_v3),
    .V4(byte_memory_module_16_v4), .V5(byte_memory_module_16_v5), .V6(byte_memory_module_16_v6),
    .V7(byte_memory_module_16_v7), .V8(byte_memory_module_16_v8), .CLK(byte_memory_module_16_clk),
    .O8(controlled_buffer_8_out), .O1(controlled_buffer_1_out), .O2(controlled_buffer_2_out),
    .O3(controlled_buffer_3_out), .O4(controlled_buffer_4_out), .O5(controlled_buffer_5_out),
    .O6(controlled_buffer_6_out), .O7(controlled_buffer_7_out));
  LED led_137 (.in(byte_memory_module_16_v2));
  LED led_138 (.in(byte_memory_module_16_v3));
  LED led_139 (.in(byte_memory_module_16_v4));
  LED led_140 (.in(byte_memory_module_16_v5));
  LED led_141 (.in(byte_memory_module_16_v6));
  LED led_142 (.in(byte_memory_module_16_v7));
  LED led_143 (.in(byte_memory_module_16_v8));
  LED led_144 (.in(byte_memory_module_16_clk));
endmodule

module Byte_Memory_Module (
  input  D1,
  input  D2,
  input  D3,
  input  D4,
  input  D5,
  input  D6,
  input  D7,
  input  D8,
  input  WR,
  input  RESET,
  input  EN,
  output V1,
  output V2,
  output V3,
  output V4,
  output V5,
  output V6,
  output V7,
  output V8,
  output CLK,
  output O8,
  output O1,
  output O2,
  output O3,
  output O4,
  output O5,
  output O6,
  output O7
);

  wire controlled_buffer_1_out, controlled_buffer_2_out, controlled_buffer_3_out, controlled_buffer_4_out,
       controlled_buffer_5_out, controlled_buffer_6_out, controlled_buffer_7_out, controlled_buffer_8_out,
       d_ff_1_qn, d_ff_2_qn, d_ff_3_qn, d_ff_4_qn, d_ff_5_qn, d_ff_6_qn, d_ff_7_qn, d_ff_8_qn;

  assign controlled_buffer_1_out = WR ? D1 : 1'bz;  // Controlled_Buffer controlled_buffer_1
  assign controlled_buffer_2_out = WR ? D2 : 1'bz;  // Controlled_Buffer controlled_buffer_2
  D_Flip_Flop d_ff_1 (.D(controlled_buffer_1_out), .clk(CLK), .Q(V1), .Qn(d_ff_1_qn), .reset(RESET));  // open: preset
  Clock clock_1 (.out(CLK));
  assign controlled_buffer_3_out = WR ? D3 : 1'bz;  // Controlled_Buffer controlled_buffer_3
  D_Flip_Flop d_ff_2 (.D(controlled_buffer_2_out), .clk(CLK), .Q(V2), .Qn(d_ff_2_qn), .reset(RESET));  // open: preset
  assign O1 = EN ? ~d_ff_1_qn : 1'bz;  // Controlled_Inverter controlled_inverter_1
  assign controlled_buffer_4_out = WR ? D4 : 1'bz;  // Controlled_Buffer controlled_buffer_4
  D_Flip_Flop d_ff_3 (.D(controlled_buffer_3_out), .clk(CLK), .Q(V3), .Qn(d_ff_3_qn), .reset(RESET));  // open: preset
  D_Flip_Flop d_ff_4 (.D(controlled_buffer_4_out), .clk(CLK), .Q(V4), .Qn(d_ff_4_qn), .reset(RESET));  // open: preset
  assign O2 = EN ? ~d_ff_2_qn : 1'bz;  // Controlled_Inverter controlled_inverter_2
  assign controlled_buffer_5_out = WR ? D5 : 1'bz;  // Controlled_Buffer controlled_buffer_5
  D_Flip_Flop d_ff_5 (.D(controlled_buffer_5_out), .clk(CLK), .Q(V5), .Qn(d_ff_5_qn), .reset(RESET));  // open: preset
  assign O3 = EN ? ~d_ff_3_qn : 1'bz;  // Controlled_Inverter controlled_inverter_3
  assign controlled_buffer_6_out = WR ? D6 : 1'bz;  // Controlled_Buffer controlled_buffer_6
  D_Flip_Flop d_ff_6 (.D(controlled_buffer_6_out), .clk(CLK), .Q(V6), .Qn(d_ff_6_qn), .reset(RESET));  // open: preset
  assign O4 = EN ? ~d_ff_4_qn : 1'bz;  // Controlled_Inverter controlled_inverter_4
  assign O5 = EN ? ~d_ff_5_qn : 1'bz;  // Controlled_Inverter controlled_inverter_5
  assign controlled_buffer_7_out = WR ? D7 : 1'bz;  // Controlled_Buffer controlled_buffer_7
  D_Flip_Flop d_ff_7 (.D(controlled_buffer_7_out), .clk(CLK), .Q(V7), .Qn(d_ff_7_qn), .reset(RESET));  // open: preset
  assign O6 = EN ? ~d_ff_6_qn : 1'bz;  // Controlled_Inverter controlled_inverter_6
  assign controlled_buffer_8_out = WR ? D8 : 1'bz;  // Controlled_Buffer controlled_buffer_8
  D_Flip_Flop d_ff_8 (.D(controlled_buffer_8_out), .clk(CLK), .Q(V8), .Qn(d_ff_8_qn), .reset(RESET));  // open: preset
  assign O7 = EN ? ~d_ff_7_qn : 1'bz;  // Controlled_Inverter controlled_inverter_7
  assign O8 = EN ? ~d_ff_8_qn : 1'bz;  // Controlled_Inverter controlled_inverter_8
endmodule
