// Logisim project System_Integration_MPC_Data_Memory.circ as structural Verilog: 17 circuits, main circuit main
module main (
  input  in_1,
  input  in_2,
  input  in_3,
  input  in_4,
  input  in_5,
  input  in_6,
  input  in_7,
  input  in_8,
  input  in_9,
  input  in_10,
  input  in_11,
  input  in_12,
  input  in_13,
  input  in_14,
  input  in_15,
  input  in_16,
  input  in_17,
  input  in_18,
  input  in_19,
  input  in_20,
  input  in_21,
  input  in_22,
  input  in_23,
  input  in_24,
  input  in_25,
  input  in_26,
  input  in_27,
  input  in_28,
  input  in_29,
  input  in_30,
  input  in_31,
  input  in_32,
  input  in_33,
  input  in_34,
  input  in_35,
  input  in_36,
  input  in_37,
  input  in_38,
  input  in_39,
  input  in_40,
  input  in_41,
  input  in_42,
  input  in_43,
  input  in_44,
  input  in_45,
  input  in_46,
  input  in_47,
  input  in_48,
  input  in_49,
  input  in_50,
  input  in_51,
  input  in_52,
  input  in_53,
  input  in_54,
  input  in_55,
  input  in_56,
  input  in_57,
  input  in_58,
  input  in_59,
  input  in_60,
  input  in_61,
  input  in_62,
  input  in_63,
  input  in_64,
  input  in_65,
  input  in_66,
  input  in_67,
  input  in_68,
  input  in_69,
  input  in_70,
  input  in_71,
  input  in_72,
  input  in_73,
  input  in_74,
  input  in_75,
  input  in_76,
  input  in_77,
  input  in_78,
  input  in_79,
  input  in_80,
  input  in_81,
  input  in_82,
  input  in_83,
  input  in_84,
  input  in_85,
  input  in_86,
  input  in_87,
  input  in_88,
  input  in_89,
  input  in_90,
  input  in_91,
  input  in_92,
  input  in_93,
  input  in_94,
  input  in_95,
  input  in_96,
  input  in_97,
  input  in_98,
  input  in_99,
  input  in_100,
  input  in_101,
  input  in_102,
  input  in_103,
  input  in_104,
  input  in_105,
  input  in_106,
  input  in_107,
  input  in_108,
  input  in_109,
  input  in_110,
  input  in_111,
  input  in_112,
  input  in_113,
  input  in_114,
  input  in_115,
  input  in_116,
  input  in_117,
  input  in_118,
  input  in_119,
  input  in_120,
  input  in_121,
  input  in_122,
  input  in_123,
  input  in_124,
  input  in_125,
  input  in_126,
  input  in_127,
  input  in_128,
  input  in_129,
  input  in_130,
  input  in_131,
  input  in_132,
  input  in_133,
  input  in_134,
  input  in_135,
  input  in_136,
  input  in_137,
  input  in_138,
  input  in_139,
  input  in_140,
  input  in_141,
  input  in_142,
  input  in_143,
  input  in_144,
  input  in_145,
  input  in_146,
  input  in_147,
  input  in_148,
  input  in_149,
  input  in_150,
  input  in_151,
  input  in_152,
  input  in_153,
  input  in_154,
  input  in_155,
  input  in_156,
  input  in_157,
  input  in_158,
  input  in_159,
  input  in_160,
  input  in_161,
  input  in_162,
  input  in_163,
  input  in_164,
  input  in_165,
  input  in_166,
  input  in_167,
  input  in_168,
  input  in_169,
  input  in_170,
  input  in_171,
  input  in_172,
  input  in_173,
  input  in_174,
  input  in_175,
  input  in_176,
  input  in_177,
  input  in_178,
  input  in_179,
  input  in_180,
  input  in_181,
  input  in_182,
  input  in_183,
  input  in_184,
  input  in_185,
  input  in_186,
  input  in_187,
  input  in_188,
  input  in_189,
  input  in_190,
  input  in_191,
  input  in_192,
  input  in_193,
  input  in_194,
  input  in_195,
  input  in_196,
  input  in_197,
  input  in_198,
  input  in_199,
  input  in_200,
  input  in_201,
  input  in_202,
  input  in_203,
  input  in_204,
  input  in_205,
  input  in_206,
  input  in_207,
  input  in_208,
  input  in_209,
  input  in_210,
  input  in_211,
  input  in_212,
  input  in_213,
  input  in_214,
  input  in_215,
  input  in_216,
  input  in_217,
  input  in_218,
  input  in_219,
  input  in_220,
  input  in_221,
  input  in_222,
  input  in_223
);

  wire clock_1_out, clock_2_out, clock_3_out, clock_4_out, clock_5_out, controlled_buffer_1_out,
       controlled_buffer_2_out, controlled_buffer_3_out, controlled_buffer_4_out, controlled_buffer_5_out,
       controlled_buffer_6_out, controlled_buffer_7_out, controlled_buffer_8_out, controlled_buffer_9_out,
       controlled_buffer_10_out, controlled_buffer_11_out, controlled_buffer_12_out,
       controlled_buffer_13_out, controlled_buffer_14_out, controlled_buffer_15_out,
       controlled_buffer_16_out, data_flow_memory_1_o1, data_flow_memory_1_o2, data_flow_memory_1_o3,
       data_flow_memory_1_o4, data_flow_memory_1_o5, data_flow_memory_1_o6, data_flow_memory_1_o7,
       data_flow_memory_1_o8, data_flow_memory_2_o1, data_flow_memory_2_o2, data_flow_memory_2_o3,
       data_flow_memory_2_o4, data_flow_memory_2_o5, data_flow_memory_2_o6, data_flow_memory_2_o7,
       data_flow_memory_2_o8, display_1_a1o, display_1_a2o, display_1_a3o, display_1_b1o, display_1_b2o,
       display_1_b3o, display_1_c1o, display_1_c2o, display_1_c3o, display_1_d1o, display_1_d2o,
       display_1_d3o, display_1_e1o, display_1_e2o, display_1_e3o, display_1_f1o, display_1_f2o,
       display_1_f3o, display_1_g1o, display_1_g2o, display_1_g3o, memory_address_register_1_o1,
       memory_address_register_1_o2, memory_address_register_1_o3, memory_address_register_1_o4,
       program_counter_1_v1, program_counter_1_v2, program_counter_1_v3, program_counter_1_v4,
       program_flow_memory_1_o1, program_flow_memory_1_o2, program_flow_memory_1_o3,
       program_flow_memory_1_o4, program_flow_memory_1_o5, program_flow_memory_1_o6,
       program_flow_memory_1_o7, program_flow_memory_1_o8, program_flow_memory_1_o9,
       program_flow_memory_1_o10, program_flow_memory_1_o11, program_flow_memory_1_o12,
       program_flow_memory_1_o13, program_flow_memory_1_o14, program_flow_memory_1_o15,
       program_flow_memory_1_o16, program_flow_memory_2_o1, program_flow_memory_2_o2,
       program_flow_memory_2_o3, program_flow_memory_2_o4, program_flow_memory_2_o5,
       program_flow_memory_2_o6, program_flow_memory_2_o7, program_flow_memory_2_o8,
       program_flow_memory_2_o9, program_flow_memory_2_o10, program_flow_memory_2_o11,
       program_flow_memory_2_o12, program_flow_memory_2_o13, program_flow_memory_2_o14,
       program_flow_memory_2_o15, program_flow_memory_2_o16, register_a_1_a1, register_a_1_a2,
       register_a_1_a4, register_a_1_a8, register_a_1_a16, register_a_1_a32, register_a_1_a64,
       register_a_1_a128, register_b_1_b1, register_b_1_b2, register_b_1_b4, register_b_1_b8,
       register_b_1_b16, register_b_1_b32, register_b_1_b64, register_b_1_b128;

  Data_Flow_Memory data_flow_memory_1 (
    .I1_1(in_5), .I2_1(in_7), .I3_1(in_9), .I4_1(in_12), .I1_2(in_15), .I2_2(in_18), .I3_2(in_21),
    .I4_2(in_24), .I1_3(in_27), .I2_3(in_31), .I3_3(in_34), .I4_3(in_37), .I1_4(in_40), .I2_4(in_43),
    .I3_4(in_46), .I4_4(in_48), .I1_5(in_50), .I2_5(in_52), .I3_5(in_54), .I4_5(in_56), .I1_6(in_58),
    .I2_6(in_60), .I3_6(in_63), .I4_6(in_66), .I1_7(in_69), .I2_7(in_72), .I3_7(in_74), .I4_7(in_76),
    .I1_8(in_78), .I2_8(in_80), .I3_8(in_82), .I4_8(in_84), .LOAD(in_86), .O1(data_flow_memory_1_o1),
    .O2(data_flow_memory_1_o2), .O3(data_flow_memory_1_o3), .O4(data_flow_memory_1_o4),
    .O5(data_flow_memory_1_o5), .O6(data_flow_memory_1_o6), .O7(data_flow_memory_1_o7),
    .O8(data_flow_memory_1_o8));  // open: COM1, COM2, COM3, COM4, COM5, COM6, COM7, COM8
  Data_Flow_Memory data_flow_memory_2 (
    .COM1(data_flow_memory_1_o1), .COM2(data_flow_memory_1_o2), .COM3(data_flow_memory_1_o3),
    .COM4(data_flow_memory_1_o4), .COM5(data_flow_memory_1_o5), .COM6(data_flow_memory_1_o6),
    .COM7(data_flow_memory_1_o7), .COM8(data_flow_memory_1_o8), .I1_1(in_6), .I2_1(in_8), .I3_1(in_10),
    .I4_1(in_13), .I1_2(in_16), .I2_2(in_19), .I3_2(in_22), .I4_2(in_25), .I1_3(in_28), .I2_3(in_32),
    .I3_3(in_35), .I4_3(in_38), .I1_4(in_41), .I2_4(in_44), .I3_4(in_47), .I4_4(in_49), .I1_5(in_51),
    .I2_5(in_53), .I3_5(in_55), .I4_5(in_57), .I1_6(in_59), .I2_6(in_61), .I3_6(in_64), .I4_6(in_67),
    .I1_7(in_70), .I2_7(in_73), .I3_7(in_75), .I4_7(in_77), .I1_8(in_79), .I2_8(in_81), .I3_8(in_83),
    .I4_8(in_85), .LOAD(in_87), .O1(data_flow_memory_2_o1), .O2(data_flow_memory_2_o2),
    .O3(data_flow_memory_2_o3), .O4(data_flow_memory_2_o4), .O5(data_flow_memory_2_o5),
    .O6(data_flow_memory_2_o6), .O7(data_flow_memory_2_o7), .O8(data_flow_memory_2_o8));
  assign controlled_buffer_1_out = data_flow_memory_2_o1 ? data_flow_memory_2_o1 : 1'bz;  // Controlled_Buffer controlled_buffer_1
  assign controlled_buffer_2_out = data_flow_memory_2_o2 ? data_flow_memory_2_o2 : 1'bz;  // Controlled_Buffer controlled_buffer_2
  assign controlled_buffer_3_out = data_flow_memory_2_o3 ? data_flow_memory_2_o3 : 1'bz;  // Controlled_Buffer controlled_buffer_3
  assign controlled_buffer_4_out = data_flow_memory_2_o4 ? data_flow_memory_2_o4 : 1'bz;  // Controlled_Buffer controlled_buffer_4
  assign controlled_buffer_5_out = data_flow_memory_2_o5 ? data_flow_memory_2_o5 : 1'bz;  // Controlled_Buffer controlled_buffer_5
  assign controlled_buffer_6_out = data_flow_memory_2_o6 ? data_flow_memory_2_o6 : 1'bz;  // Controlled_Buffer controlled_buffer_6
  assign controlled_buffer_7_out = data_flow_memory_2_o7 ? data_flow_memory_2_o7 : 1'bz;  // Controlled_Buffer controlled_buffer_7
  assign controlled_buffer_8_out = data_flow_memory_2_o8 ? data_flow_memory_2_o8 : 1'bz;  // Controlled_Buffer controlled_buffer_8
  Clock clock_1 (.out(clock_1_out));
  Clock clock_2 (.out(clock_2_out));
  Register_A register_a_1 (
    .CLR(in_2), .BUS1(controlled_buffer_1_out), .BUS2(controlled_buffer_2_out),
    .BUS3(controlled_buffer_3_out), .BUS4(controlled_buffer_4_out), .BUS5(controlled_buffer_5_out),
    .BUS6(controlled_buffer_6_out), .BUS7(controlled_buffer_7_out), .BUS8(controlled_buffer_8_out),
    .CLK(clock_2_out), .LOAD(program_flow_memory_1_o1), .ENABLE(program_flow_memory_1_o2),
    .A1(register_a_1_a1), .A2(register_a_1_a2), .A4(register_a_1_a4), .A8(register_a_1_a8),
    .A16(register_a_1_a16), .A32(register_a_1_a32), .A64(register_a_1_a64), .A128(register_a_1_a128),
    .O1(controlled_buffer_1_out), .O2(controlled_buffer_2_out), .O3(controlled_buffer_3_out),
    .O4(controlled_buffer_4_out), .O5(controlled_buffer_5_out), .O6(controlled_buffer_6_out),
    .O7(controlled_buffer_7_out), .O8(controlled_buffer_8_out));
  Program_Counter program_counter_1 (
    .RST(in_45), .CLK(clock_1_out), .D1(controlled_buffer_1_out), .D2(controlled_buffer_2_out),
    .D3(controlled_buffer_3_out), .D4(controlled_buffer_4_out), .CTR_EN(program_flow_memory_1_o10),
    .BUS_LOAD(program_flow_memory_1_o11), .BUS_ENABLE(program_flow_memory_1_o12), .V1(program_counter_1_v1),
    .V2(program_counter_1_v2), .V3(program_counter_1_v3), .V4(program_counter_1_v4),
    .O1(controlled_buffer_1_out), .O2(controlled_buffer_2_out), .O3(controlled_buffer_3_out),
    .O4(controlled_buffer_4_out));
  Program_Flow_Memory program_flow_memory_1 (
    .COM1(program_flow_memory_2_o1), .COM2(program_flow_memory_2_o2), .COM3(program_flow_memory_2_o3),
    .COM4(program_flow_memory_2_o4), .COM5(program_flow_memory_2_o5), .COM6(program_flow_memory_2_o6),
    .COM7(program_flow_memory_2_o7), .COM8(program_flow_memory_2_o8), .COM9(program_flow_memory_2_o9),
    .COM10(program_flow_memory_2_o10), .COM11(program_flow_memory_2_o11), .COM12(program_flow_memory_2_o12),
    .COM13(program_flow_memory_2_o13), .COM14(program_flow_memory_2_o14), .COM15(program_flow_memory_2_o15),
    .COM16(program_flow_memory_2_o16), .I1_1(in_88), .I2_1(in_105), .I3_1(in_122), .I4_1(in_139),
    .I1_2(in_89), .I2_2(in_106), .I3_2(in_123), .I4_2(in_140), .I1_3(in_90), .I2_3(in_107), .I3_3(in_124),
    .I4_3(in_141), .I1_4(in_91), .I2_4(in_108), .I3_4(in_125), .I4_4(in_142), .I1_5(in_92), .I2_5(in_109),
    .I3_5(in_126), .I4_5(in_143), .I1_6(in_93), .I2_6(in_110), .I3_6(in_127), .I4_6(in_144), .I1_7(in_94),
    .I2_7(in_111), .I3_7(in_128), .I4_7(in_145), .I1_8(in_95), .I2_8(in_112), .I3_8(in_129), .I4_8(in_146),
    .I1_9(in_96), .I2_9(in_113), .I3_9(in_130), .I4_9(in_147), .I1_10(in_97), .I2_10(in_114), .I3_10(in_131),
    .I4_10(in_148), .I1_11(in_98), .I2_11(in_115), .I3_11(in_132), .I4_11(in_149), .I1_12(in_99),
    .I2_12(in_116), .I3_12(in_133), .I4_12(in_150), .I1_13(in_100), .I2_13(in_117), .I3_13(in_134),
    .I4_13(in_151), .I1_14(in_101), .I2_14(in_118), .I3_14(in_135), .I4_14(in_152), .I1_15(in_102),
    .I2_15(in_119), .I3_15(in_136), .I4_15(in_153), .I1_16(in_103), .I2_16(in_120), .I3_16(in_137),
    .I4_16(in_154), .LOAD_I1(in_104), .LOAD_I2(in_121), .LOAD_I3(in_138), .LOAD_I4(in_155),
    .O1(program_flow_memory_1_o1), .O2(program_flow_memory_1_o2), .O3(program_flow_memory_1_o3),
    .O4(program_flow_memory_1_o4), .O5(program_flow_memory_1_o5), .O6(program_flow_memory_1_o6),
    .O7(program_flow_memory_1_o7), .O8(program_flow_memory_1_o8), .O9(program_flow_memory_1_o9),
    .O10(program_flow_memory_1_o10), .O11(program_flow_memory_1_o11), .O12(program_flow_memory_1_o12),
    .O13(program_flow_memory_1_o13), .O14(program_flow_memory_1_o14), .O15(program_flow_memory_1_o15),
    .O16(program_flow_memory_1_o16));
  Program_Flow_Memory program_flow_memory_2 (
    .I1_1(in_156), .I2_1(in_173), .I3_1(in_190), .I4_1(in_207), .I1_2(in_157), .I2_2(in_174), .I3_2(in_191),
    .I4_2(in_208), .I1_3(in_158), .I2_3(in_175), .I3_3(in_192), .I4_3(in_209), .I1_4(in_159), .I2_4(in_176),
    .I3_4(in_193), .I4_4(in_210), .I1_5(in_160), .I2_5(in_177), .I3_5(in_194), .I4_5(in_211), .I1_6(in_161),
    .I2_6(in_178), .I3_6(in_195), .I4_6(in_212), .I1_7(in_162), .I2_7(in_179), .I3_7(in_196), .I4_7(in_213),
    .I1_8(in_163), .I2_8(in_180), .I3_8(in_197), .I4_8(in_214), .I1_9(in_164), .I2_9(in_181), .I3_9(in_198),
    .I4_9(in_215), .I1_10(in_165), .I2_10(in_182), .I3_10(in_199), .I4_10(in_216), .I1_11(in_166),
    .I2_11(in_183), .I3_11(in_200), .I4_11(in_217), .I1_12(in_167), .I2_12(in_184), .I3_12(in_201),
    .I4_12(in_218), .I1_13(in_168), .I2_13(in_185), .I3_13(in_202), .I4_13(in_219), .I1_14(in_169),
    .I2_14(in_186), .I3_14(in_203), .I4_14(in_220), .I1_15(in_170), .I2_15(in_187), .I3_15(in_204),
    .I4_15(in_221), .I1_16(in_171), .I2_16(in_188), .I3_16(in_205), .I4_16(in_222), .LOAD_I1(in_172),
    .LOAD_I2(in_189), .LOAD_I3(in_206), .LOAD_I4(in_223), .O1(program_flow_memory_2_o1),
    .O2(program_flow_memory_2_o2), .O3(program_flow_memory_2_o3), .O4(program_flow_memory_2_o4),
    .O5(program_flow_memory_2_o5), .O6(program_flow_memory_2_o6), .O7(program_flow_memory_2_o7),
    .O8(program_flow_memory_2_o8), .O9(program_flow_memory_2_o9), .O10(program_flow_memory_2_o10),
    .O11(program_flow_memory_2_o11), .O12(program_flow_memory_2_o12), .O13(program_flow_memory_2_o13),
    .O14(program_flow_memory_2_o14), .O15(program_flow_memory_2_o15), .O16(program_flow_memory_2_o16));  // open: COM1, COM2, COM3, COM4, COM5, COM6, COM7, COM8, COM9, COM10, COM11, COM12, COM13, COM14, COM15, COM16
  LED led_1 (.in(program_counter_1_v1));
  LED led_2 (.in(program_counter_1_v2));
  LED led_3 (.in(program_counter_1_v3));
  LED led_4 (.in(program_counter_1_v4));
  LED led_5 (.in(register_a_1_a1));
  LED led_6 (.in(register_a_1_a2));
  LED led_7 (.in(register_a_1_a4));
  LED led_8 (.in(register_a_1_a8));
  LED led_9 (.in(register_a_1_a16));
  LED led_10 (.in(register_a_1_a32));
  LED led_11 (.in(register_a_1_a64));
  LED led_12 (.in(register_a_1_a128));
  ALU alu_1 (
    .A1(register_a_1_a1), .A2(register_a_1_a2), .A4(register_a_1_a4), .A8(register_a_1_a8),
    .A16(register_a_1_a16), .A32(register_a_1_a32), .A64(register_a_1_a64), .A128(register_a_1_a128),
    .B1(register_b_1_b1), .B2(register_b_1_b2), .B4(register_b_1_b4), .B8(register_b_1_b8),
    .B16(register_b_1_b16), .B32(register_b_1_b32), .B64(register_b_1_b64), .B128(register_b_1_b128),
    .O_Enable(program_flow_memory_1_o13), .SUB(program_flow_memory_1_o14), .O_1(controlled_buffer_1_out),
    .O_2(controlled_buffer_2_out), .O_4(controlled_buffer_3_out), .O_8(controlled_buffer_4_out),
    .O_16(controlled_buffer_5_out), .O_32(controlled_buffer_6_out), .O_64(controlled_buffer_7_out),
    .O_128(controlled_buffer_8_out));
  Clock clock_3 (.out(clock_3_out));
  Clock clock_4 (.out(clock_4_out));
  Register_B register_b_1 (
    .CLR(in_3), .BUS1(controlled_buffer_1_out), .BUS2(controlled_buffer_2_out),
    .BUS3(controlled_buffer_3_out), .BUS4(controlled_buffer_4_out), .BUS5(controlled_buffer_5_out),
    .BUS6(controlled_buffer_6_out), .BUS7(controlled_buffer_7_out), .BUS8(controlled_buffer_8_out),
    .CLK(clock_4_out), .LOAD(program_flow_memory_1_o3), .ENABLE(program_flow_memory_1_o4),
    .B1(register_b_1_b1), .B2(register_b_1_b2), .B4(register_b_1_b4), .B8(register_b_1_b8),
    .B16(register_b_1_b16), .B32(register_b_1_b32), .B64(register_b_1_b64), .B128(register_b_1_b128),
    .O1(controlled_buffer_1_out), .O2(controlled_buffer_2_out), .O3(controlled_buffer_3_out),
    .O4(controlled_buffer_4_out), .O5(controlled_buffer_5_out), .O6(controlled_buffer_6_out),
    .O7(controlled_buffer_7_out), .O8(controlled_buffer_8_out));
  Instruction_Register instruction_register_1 (
    .CLR(in_29), .BUS1(controlled_buffer_1_out), .BUS2(controlled_buffer_2_out),
    .BUS3(controlled_buffer_3_out), .BUS4(controlled_buffer_4_out), .BUS5(controlled_buffer_5_out),
    .BUS6(controlled_buffer_6_out), .BUS7(controlled_buffer_7_out), .BUS8(controlled_buffer_8_out),
    .CLK(clock_3_out), .LOAD(program_flow_memory_1_o15), .ENABLE(program_flow_memory_1_o16),
    .O1(controlled_buffer_1_out), .O2(controlled_buffer_2_out), .O3(controlled_buffer_3_out),
    .O4(controlled_buffer_4_out));  // open: O5, O6, O7, O8
  LED led_13 (.in(register_b_1_b1));
  LED led_14 (.in(register_b_1_b2));
  LED led_15 (.in(register_b_1_b4));
  LED led_16 (.in(register_b_1_b8));
  LED led_17 (.in(register_b_1_b16));
  LED led_18 (.in(register_b_1_b32));
  LED led_19 (.in(register_b_1_b64));
  LED led_20 (.in(register_b_1_b128));
  Clock clock_5 (.out(clock_5_out));
  assign controlled_buffer_9_out = controlled_buffer_8_out ? controlled_buffer_8_out : 1'bz;  // Controlled_Buffer controlled_buffer_9
  assign controlled_buffer_10_out = controlled_buffer_7_out ? controlled_buffer_7_out : 1'bz;  // Controlled_Buffer controlled_buffer_10
  assign controlled_buffer_11_out = controlled_buffer_6_out ? controlled_buffer_6_out : 1'bz;  // Controlled_Buffer controlled_buffer_11
  assign controlled_buffer_12_out = controlled_buffer_5_out ? controlled_buffer_5_out : 1'bz;  // Controlled_Buffer controlled_buffer_12
  assign controlled_buffer_13_out = controlled_buffer_4_out ? controlled_buffer_4_out : 1'bz;  // Controlled_Buffer controlled_buffer_13
  assign controlled_buffer_14_out = controlled_buffer_3_out ? controlled_buffer_3_out : 1'bz;  // Controlled_Buffer controlled_buffer_14
  assign controlled_buffer_15_out = controlled_buffer_2_out ? controlled_buffer_2_out : 1'bz;  // Controlled_Buffer controlled_buffer_15
  assign controlled_buffer_16_out = controlled_buffer_1_out ? controlled_buffer_1_out : 1'bz;  // Controlled_Buffer controlled_buffer_16
  Memory_Address_Register memory_address_register_1 (
    .CLR(in_4), .A0(controlled_buffer_1_out), .A1(controlled_buffer_2_out), .A2(controlled_buffer_3_out),
    .A3(controlled_buffer_4_out), .CLK(clock_5_out), .LOAD(program_flow_memory_1_o5),
    .ENABLE(program_flow_memory_1_o6), .O1(memory_address_register_1_o1), .O2(memory_address_register_1_o2),
    .O3(memory_address_register_1_o3), .O4(memory_address_register_1_o4));
  Display display_1 (
    .a(in_11), .b(in_14), .c(in_17), .d(in_20), .e(in_23), .f(in_26), .g(in_30), .A0(in_33), .A1(in_36),
    .A2(in_39), .A3(in_42), .BUS1(controlled_buffer_9_out), .BUS2(controlled_buffer_10_out),
    .BUS3(controlled_buffer_11_out), .BUS4(controlled_buffer_12_out), .BUS5(controlled_buffer_13_out),
    .BUS6(controlled_buffer_14_out), .BUS7(controlled_buffer_15_out), .BUS8(controlled_buffer_16_out),
    .E0W1(in_62), .CHIP_EN(in_65), .RST(in_68), .DATA_EN(in_71), .a1o(display_1_a1o), .b1o(display_1_b1o),
    .c1o(display_1_c1o), .d1o(display_1_d1o), .e1o(display_1_e1o), .f1o(display_1_f1o), .g1o(display_1_g1o),
    .a2o(display_1_a2o), .b2o(display_1_b2o), .c2o(display_1_c2o), .d2o(display_1_d2o), .e2o(display_1_e2o),
    .f2o(display_1_f2o), .g2o(display_1_g2o), .a3o(display_1_a3o), .b3o(display_1_b3o), .c3o(display_1_c3o),
    .d3o(display_1_d3o), .e3o(display_1_e3o), .f3o(display_1_f3o), .g3o(display_1_g3o));
  _7_Segment_Display u_7_segment_display_1 (
    .g(display_1_g1o), .f(display_1_f1o), .a(display_1_a1o), .b(display_1_b1o), .e(display_1_e1o),
    .d(display_1_d1o), .c(display_1_c1o));  // open: dp
  _7_Segment_Display u_7_segment_display_2 (
    .g(display_1_g2o), .f(display_1_f2o), .a(display_1_a2o), .b(display_1_b2o), .e(display_1_e2o),
    .d(display_1_d2o), .c(display_1_c2o));  // open: dp
  _7_Segment_Display u_7_segment_display_3 (
    .g(display_1_g3o), .f(display_1_f3o), .a(display_1_a3o), .b(display_1_b3o), .e(display_1_e3o),
    .d(display_1_d3o), .c(display_1_c3o));  // open: dp
  Random_Access_Memory random_access_memory_1 (
    .RST_RAM(in_1), .D1(controlled_buffer_1_out), .D2(controlled_buffer_2_out), .D3(controlled_buffer_3_out),
    .D4(controlled_buffer_4_out), .D5(controlled_buffer_5_out), .D6(controlled_buffer_6_out),
    .D7(controlled_buffer_7_out), .D8(controlled_buffer_8_out), .DATA_EN(program_flow_memory_1_o7),
    .A0(memory_address_register_1_o1), .A1(memory_address_register_1_o2), .A2(memory_address_register_1_o3),
    .A3(memory_address_register_1_o4), .CHIP_EN(program_flow_memory_1_o8), .E0W1(program_flow_memory_1_o9),
    .O1(controlled_buffer_1_out), .O2(controlled_buffer_2_out), .O3(controlled_buffer_3_out),
    .O4(controlled_buffer_4_out), .O5(controlled_buffer_5_out), .O6(controlled_buffer_6_out),
    .O7(controlled_buffer_7_out), .O8(controlled_buffer_8_out));
  LED led_21 (.in(controlled_buffer_1_out));
  LED led_22 (.in(controlled_buffer_2_out));
  LED led_23 (.in(controlled_buffer_3_out));
  LED led_24 (.in(controlled_buffer_4_out));
  LED led_25 (.in(controlled_buffer_5_out));
  LED led_26 (.in(controlled_buffer_6_out));
  LED led_27 (.in(controlled_buffer_7_out));
  LED led_28 (.in(controlled_buffer_8_out));
endmodule

module Binary2BCD (
  input  I128,
  input  I64,
  input  I32,
  input  I16,
  input  I8,
  input  I4,
  input  I2,
  input  I1,
  output O1_8,
  output O1_4,
  output O1_2,
  output O1_1,
  output O2_8,
  output O2_4,
  output O2_2,
  output O2_1,
  output O3_8,
  output O3_4,
  output O3_2,
  output O3_1
);

  wire and_1_out, and_2_out, and_3_out, and_4_out, and_5_out, and_6_out, and_7_out, nand_1_out, nand_2_out,
       nand_3_out, nand_4_out, nand_5_out, nand_6_out, nand_7_out, nand_8_out, nand_9_out, nand_10_out,
       nand_11_out, nand_12_out, nand_13_out, nand_14_out, nand_15_out, nand_19_out, nand_20_out,
       nand_21_out, nand_22_out, nand_23_out, nand_24_out, nand_25_out, nand_26_out, nand_27_out,
       nand_28_out, nand_29_out, nand_31_out, nand_32_out, nand_33_out, nand_34_out, nand_35_out,
       nand_36_out, nand_37_out, nand_38_out, nand_39_out, nand_40_out, nand_41_out, nand_42_out,
       nand_43_out, nand_44_out, nand_45_out, nand_46_out, nand_47_out, nand_48_out, nand_49_out,
       nand_51_out, nand_52_out, nand_53_out, nand_54_out, nand_55_out, nand_56_out, nand_57_out,
       nand_58_out, nand_59_out, nand_60_out, nand_61_out, nand_62_out, nand_63_out, nand_67_out,
       nand_68_out, nand_69_out, nor_1_out, nor_2_out, nor_3_out, nor_4_out, nor_5_out, nor_6_out, nor_7_out,
       nor_8_out, nor_9_out, nor_10_out, nor_11_out, nor_12_out, nor_13_out, nor_14_out, not_1_out,
       not_2_out, not_3_out, not_4_out, not_5_out, not_6_out, not_7_out, not_8_out, not_9_out, not_10_out,
       not_11_out, not_12_out, not_13_out, not_14_out, or_1_out, or_2_out, or_3_out, or_4_out, or_5_out,
       or_6_out, or_7_out, or_8_out, or_9_out, or_10_out, or_11_out, or_12_out, or_13_out, or_14_out,
       or_15_out, or_16_out, or_17_out, or_18_out, or_19_out, or_20_out, or_21_out, or_22_out, or_23_out,
       or_24_out, or_25_out, or_26_out, or_27_out, or_28_out;

  nand nand_1 (nand_1_out, 1'b0, I32);
  nor nor_1 (nor_1_out, I128, 1'b0);
  and and_1 (and_1_out, I64, I128);
  not not_1 (not_1_out, I32);
  not not_2 (not_2_out, I128);
  nand nand_2 (nand_2_out, nand_62_out, I4);
  nor nor_2 (nor_2_out, nand_61_out, nand_62_out);
  and and_2 (and_2_out, nand_60_out, nand_61_out);
  not not_3 (not_3_out, I4);
  not not_4 (not_4_out, nand_61_out);
  nand nand_3 (nand_3_out, nand_24_out, I2);
  nor nor_3 (nor_3_out, nand_23_out, nand_24_out);
  and and_3 (and_3_out, nand_22_out, nand_23_out);
  not not_5 (not_5_out, I2);
  not not_6 (not_6_out, nand_23_out);
  nand nand_4 (nand_4_out, I128, not_1_out);
  nand nand_5 (nand_5_out, I32, nor_1_out);
  nor nor_4 (nor_4_out, 1'b0, and_1_out);
  nand nand_6 (nand_6_out, not_1_out, 1'b0);
  or or_1 (or_1_out, I64, not_2_out);
  nand nand_7 (nand_7_out, nand_61_out, not_3_out);
  nand nand_8 (nand_8_out, I4, nor_2_out);
  nor nor_5 (nor_5_out, nand_62_out, and_2_out);
  nand nand_9 (nand_9_out, not_3_out, nand_62_out);
  or or_2 (or_2_out, nand_60_out, not_4_out);
  nand nand_10 (nand_10_out, nand_23_out, not_5_out);
  nand nand_11 (nand_11_out, I2, nor_3_out);
  nor nor_6 (nor_6_out, nand_24_out, and_3_out);
  nand nand_12 (nand_12_out, not_5_out, nand_24_out);
  or or_3 (or_3_out, nand_22_out, not_6_out);
  nand nand_13 (nand_13_out, nand_4_out, I64);
  or or_4 (or_4_out, nor_4_out, I32);
  or or_5 (or_5_out, or_1_out, I32);
  nand nand_14 (nand_14_out, nand_7_out, nand_60_out);
  or or_6 (or_6_out, nor_5_out, I4);
  or or_7 (or_7_out, or_2_out, I4);
  nand nand_15 (nand_15_out, nand_10_out, nand_22_out);
  or or_8 (or_8_out, nor_6_out, I2);
  or or_9 (or_9_out, or_3_out, I2);
  nand nand_16 (O3_2, nand_11_out, or_8_out);
  nand nand_17 (O3_4, nand_15_out, nand_12_out);
  nand nand_18 (O3_8, nand_3_out, or_9_out);
  nand nand_19 (nand_19_out, nand_5_out, or_4_out);
  nand nand_20 (nand_20_out, nand_13_out, nand_6_out);
  nand nand_21 (nand_21_out, nand_1_out, or_5_out);
  nand nand_22 (nand_22_out, nand_8_out, or_6_out);
  nand nand_23 (nand_23_out, nand_14_out, nand_9_out);
  nand nand_24 (nand_24_out, nand_2_out, or_7_out);
  or or_10 (or_10_out, nand_19_out, not_1_out);
  nand nand_25 (nand_25_out, nand_19_out, not_1_out);
  or or_11 (or_11_out, nand_22_out, not_3_out);
  nand nand_26 (nand_26_out, nand_22_out, not_3_out);
  or or_12 (or_12_out, O3_2, not_5_out);
  nand nand_27 (nand_27_out, O3_2, not_5_out);
  nand nand_28 (nand_28_out, or_10_out, nand_25_out);
  nand nand_29 (nand_29_out, or_11_out, nand_26_out);
  nand nand_30 (O2_1, or_12_out, nand_27_out);
  nand nand_31 (nand_31_out, nand_21_out, I16);
  nor nor_7 (nor_7_out, nand_20_out, nand_21_out);
  and and_4 (and_4_out, nand_19_out, nand_20_out);
  not not_7 (not_7_out, I16);
  not not_8 (not_8_out, nand_20_out);
  nand nand_32 (nand_32_out, 1'b0, nand_68_out);
  nor nor_8 (nor_8_out, nand_28_out, 1'b0);
  and and_5 (and_5_out, nand_48_out, nand_28_out);
  not not_9 (not_9_out, nand_68_out);
  not not_10 (not_10_out, nand_28_out);
  nand nand_33 (nand_33_out, nand_20_out, not_7_out);
  nand nand_34 (nand_34_out, I16, nor_7_out);
  nor nor_9 (nor_9_out, nand_21_out, and_4_out);
  nand nand_35 (nand_35_out, not_7_out, nand_21_out);
  or or_13 (or_13_out, nand_19_out, not_8_out);
  nand nand_36 (nand_36_out, nand_28_out, not_9_out);
  nand nand_37 (nand_37_out, nand_68_out, nor_8_out);
  nor nor_10 (nor_10_out, 1'b0, and_5_out);
  nand nand_38 (nand_38_out, not_9_out, 1'b0);
  or or_14 (or_14_out, nand_48_out, not_10_out);
  nand nand_39 (nand_39_out, nand_33_out, nand_19_out);
  or or_15 (or_15_out, nor_9_out, I16);
  or or_16 (or_16_out, or_13_out, I16);
  nand nand_40 (nand_40_out, nand_36_out, nand_48_out);
  or or_17 (or_17_out, nor_10_out, nand_68_out);
  or or_18 (or_18_out, or_14_out, nand_68_out);
  nand nand_41 (nand_41_out, nand_34_out, or_15_out);
  nand nand_42 (nand_42_out, nand_39_out, nand_35_out);
  nand nand_43 (nand_43_out, nand_31_out, or_16_out);
  nand nand_44 (nand_44_out, nand_37_out, or_17_out);
  nand nand_45 (nand_45_out, nand_40_out, nand_38_out);
  nand nand_46 (nand_46_out, nand_32_out, or_18_out);
  or or_19 (or_19_out, nand_41_out, not_7_out);
  nand nand_47 (nand_47_out, nand_41_out, not_7_out);
  nand nand_48 (nand_48_out, or_19_out, nand_47_out);
  or or_20 (or_20_out, nand_44_out, not_9_out);
  nand nand_49 (nand_49_out, nand_44_out, not_9_out);
  nand nand_50 (O1_2, or_20_out, nand_49_out);
  nand nand_51 (nand_51_out, nand_43_out, I8);
  nor nor_11 (nor_11_out, nand_42_out, nand_43_out);
  and and_6 (and_6_out, nand_41_out, nand_42_out);
  not not_11 (not_11_out, I8);
  not not_12 (not_12_out, nand_42_out);
  nand nand_52 (nand_52_out, nand_46_out, nand_29_out);
  nor nor_12 (nor_12_out, nand_45_out, nand_46_out);
  and and_7 (and_7_out, nand_44_out, nand_45_out);
  not not_13 (not_13_out, nand_29_out);
  not not_14 (not_14_out, nand_45_out);
  nand nand_53 (nand_53_out, nand_42_out, not_11_out);
  nand nand_54 (nand_54_out, I8, nor_11_out);
  nor nor_13 (nor_13_out, nand_43_out, and_6_out);
  nand nand_55 (nand_55_out, not_11_out, nand_43_out);
  or or_21 (or_21_out, nand_41_out, not_12_out);
  nand nand_56 (nand_56_out, nand_45_out, not_13_out);
  nand nand_57 (nand_57_out, nand_29_out, nor_12_out);
  nor nor_14 (nor_14_out, nand_46_out, and_7_out);
  nand nand_58 (nand_58_out, not_13_out, nand_46_out);
  or or_22 (or_22_out, nand_44_out, not_14_out);
  nand nand_59 (nand_59_out, nand_53_out, nand_41_out);
  or or_23 (or_23_out, nor_13_out, I8);
  or or_24 (or_24_out, or_21_out, I8);
  or or_25 (or_25_out, nor_14_out, nand_29_out);
  or or_26 (or_26_out, or_22_out, nand_29_out);
  nand nand_60 (nand_60_out, nand_54_out, or_23_out);
  nand nand_61 (nand_61_out, nand_59_out, nand_55_out);
  nand nand_62 (nand_62_out, nand_51_out, or_24_out);
  nand nand_63 (nand_63_out, nand_56_out, nand_44_out);
  nand nand_64 (O2_2, nand_57_out, or_25_out);
  nand nand_65 (O2_4, nand_63_out, nand_58_out);
  nand nand_66 (O2_8, nand_52_out, or_26_out);
  or or_27 (or_27_out, nand_60_out, not_11_out);
  nand nand_67 (nand_67_out, nand_60_out, not_11_out);
  or or_28 (or_28_out, O2_2, not_13_out);
  nand nand_68 (nand_68_out, or_27_out, nand_67_out);
  nand nand_69 (nand_69_out, O2_2, not_13_out);
  nand nand_70 (O1_1, or_28_out, nand_69_out);

  assign O3_1 = I1;

  // Notes on the sheet:
  //   DABBLER T
  //   DABBLER D
  //   DABBLER N
  //   D2
  //   T3
  //   T2
  //   T1
  //   T0
  //   D3
  //   D1
  //   D0
  //   N3
  //   N2
  //   N1
  //   N0
  //   DABBLER W
  //   DABBLER K
  //   W2
  //   W1
  //   W3
  //   W0
  //   K3
  //   K2
  //   K1
  //   K0
  //   DABBLER Z
  //   DABBLER M
  //   M1
  //   M0
  //   Z3
  //   Z2
  //   Z1
  //   Z0
  //   M3
  //   M2
endmodule

module ALU (
  input  A1,
  input  A2,
  input  A4,
  input  A8,
  input  A16,
  input  A32,
  input  A64,
  input  A128,
  input  B1,
  input  B2,
  input  B4,
  input  B8,
  input  B16,
  input  B32,
  input  B64,
  input  B128,
  input  O_Enable,
  input  SUB,
  output O_1,
  output O_2,
  output O_4,
  output O_8,
  output O_16,
  output O_32,
  output O_64,
  output O_128
);

  wire n7486_1_pin3, n7486_1_pin6, n7486_1_pin8, n7486_1_pin11, n7486_2_pin3, n7486_2_pin6, n7486_2_pin8,
       n7486_2_pin11, n74283_1_pin1, n74283_1_pin4, n74283_1_pin9, n74283_1_pin10, n74283_1_pin13,
       n74283_2_pin1, n74283_2_pin4, n74283_2_pin10, n74283_2_pin13, not_1_out;

  _7486 u_7486_1 (
    .pin1(B4), .pin2(SUB), .pin3(n7486_1_pin3), .pin4(B8), .pin5(SUB), .pin6(n7486_1_pin6), .pin13(SUB),
    .pin12(B2), .pin11(n7486_1_pin11), .pin10(SUB), .pin9(B1), .pin8(n7486_1_pin8));
  _7486 u_7486_2 (
    .pin1(B64), .pin2(SUB), .pin3(n7486_2_pin3), .pin4(B128), .pin5(SUB), .pin6(n7486_2_pin6), .pin13(SUB),
    .pin12(B32), .pin11(n7486_2_pin11), .pin10(SUB), .pin9(B16), .pin8(n7486_2_pin8));
  not not_1 (not_1_out, O_Enable);
  _74283 u_74283_1 (
    .pin1(n74283_1_pin1), .pin2(A2), .pin3(n7486_1_pin11), .pin4(n74283_1_pin4), .pin5(n7486_1_pin8),
    .pin6(A1), .pin7(SUB), .pin15(A4), .pin14(n7486_1_pin3), .pin13(n74283_1_pin13), .pin12(n7486_1_pin6),
    .pin11(A8), .pin10(n74283_1_pin10), .pin9(n74283_1_pin9));
  _74283 u_74283_2 (
    .pin1(n74283_2_pin1), .pin2(A32), .pin3(n7486_2_pin11), .pin4(n74283_2_pin4), .pin5(n7486_2_pin8),
    .pin6(A16), .pin7(n74283_1_pin9), .pin15(A64), .pin14(n7486_2_pin3), .pin13(n74283_2_pin13),
    .pin12(n7486_2_pin6), .pin11(A128), .pin10(n74283_2_pin10));  // open: pin9
  _74245 u_74245_1 (
    .pin2(O_128), .pin3(O_64), .pin4(O_32), .pin5(O_16), .pin6(O_8), .pin7(O_4), .pin8(O_2), .pin9(O_1),
    .pin19(not_1_out), .pin18(n74283_2_pin10), .pin17(n74283_2_pin13), .pin16(n74283_2_pin1),
    .pin15(n74283_2_pin4), .pin14(n74283_1_pin10), .pin13(n74283_1_pin13), .pin12(n74283_1_pin1),
    .pin11(n74283_1_pin4));  // open: pin1
  LED O1 (.in(O_1));
  LED O2 (.in(O_2));
  LED O4 (.in(O_4));
  LED O8 (.in(O_8));
  LED O16 (.in(O_16));
  LED O32 (.in(O_32));
  LED O64 (.in(O_64));
  LED O128 (.in(O_128));
endmodule

module Byte_Memory_Module (
  input  D1,
  input  D2,
  input  D3,
  input  D4,
  input  D5,
  input  D6,
  input  D7,
  input  D8,
  input  WR,
  input  RESET,
  input  EN,
  output V1,
  output V2,
  output V3,
  output V4,
  output V5,
  output V6,
  output V7,
  output V8,
  output CLK,
  output O8,
  output O1,
  output O2,
  output O3,
  output O4,
  output O5,
  output O6,
  output O7
);

  wire controlled_buffer_1_out, controlled_buffer_2_out, controlled_buffer_3_out, controlled_buffer_4_out,
       controlled_buffer_5_out, controlled_buffer_6_out, controlled_buffer_7_out, controlled_buffer_8_out,
       d_ff_1_qn, d_ff_2_qn, d_ff_3_qn, d_ff_4_qn, d_ff_5_qn, d_ff_6_qn, d_ff_7_qn, d_ff_8_qn;

  assign controlled_buffer_1_out = WR ? D1 : 1'bz;  // Controlled_Buffer controlled_buffer_1
  assign controlled_buffer_2_out = WR ? D2 : 1'bz;  // Controlled_Buffer controlled_buffer_2
  D_Flip_Flop d_ff_1 (.D(controlled_buffer_1_out), .clk(CLK), .Q(V1), .Qn(d_ff_1_qn), .reset(RESET));  // open: preset
  Clock clock_1 (.out(CLK));
  assign controlled_buffer_3_out = WR ? D3 : 1'bz;  // Controlled_Buffer controlled_buffer_3
  D_Flip_Flop d_ff_2 (.D(controlled_buffer_2_out), .clk(CLK), .Q(V2), .Qn(d_ff_2_qn), .reset(RESET));  // open: preset
  assign O1 = EN ? ~d_ff_1_qn : 1'bz;  // Controlled_Inverter controlled_inverter_1
  assign controlled_buffer_4_out = WR ? D4 : 1'bz;  // Controlled_Buffer controlled_buffer_4
  D_Flip_Flop d_ff_3 (.D(controlled_buffer_3_out), .clk(CLK), .Q(V3), .Qn(d_ff_3_qn), .reset(RESET));  // open: preset
  D_Flip_Flop d_ff_4 (.D(controlled_buffer_4_out), .clk(CLK), .Q(V4), .Qn(d_ff_4_qn), .reset(RESET));  // open: preset
  assign O2 = EN ? ~d_ff_2_qn : 1'bz;  // Controlled_Inverter controlled_inverter_2
  assign controlled_buffer_5_out = WR ? D5 : 1'bz;  // Controlled_Buffer controlled_buffer_5
  D_Flip_Flop d_ff_5 (.D(controlled_buffer_5_out), .clk(CLK), .Q(V5), .Qn(d_ff_5_qn), .reset(RESET));  // open: preset
  assign O3 = EN ? ~d_ff_3_qn : 1'bz;  // Controlled_Inverter controlled_inverter_3
  assign controlled_buffer_6_out = WR ? D6 : 1'bz;  // Controlled_Buffer controlled_buffer_6
  D_Flip_Flop d_ff_6 (.D(controlled_buffer_6_out), .clk(CLK), .Q(V6), .Qn(d_ff_6_qn), .reset(RESET));  // open: preset
  assign O4 = EN ? ~d_ff_4_qn : 1'bz;  // Controlled_Inverter controlled_inverter_4
  assign O5 = EN ? ~d_ff_5_qn : 1'bz;  // Controlled_Inverter controlled_inverter_5
  assign controlled_buffer_7_out = WR ? D7 : 1'bz;  // Controlled_Buffer controlled_buffer_7
  D_Flip_Flop d_ff_7 (.D(controlled_buffer_7_out), .clk(CLK), .Q(V7), .Qn(d_ff_7_qn), .reset(RESET));  // open: preset
  assign O6 = EN ? ~d_ff_6_qn : 1'bz;  // Controlled_Inverter controlled_inverter_6
  assign controlled_buffer_8_out = WR ? D8 : 1'bz;  // Controlled_Buffer controlled_buffer_8
  D_Flip_Flop d_ff_8 (.D(controlled_buffer_8_out), .clk(CLK), .Q(V8), .Qn(d_ff_8_qn), .reset(RESET));  // open: preset
  assign O7 = EN ? ~d_ff_7_qn : 1'bz;  // Controlled_Inverter controlled_inverter_7
  assign O8 = EN ? ~d_ff_8_qn : 1'bz;  // Controlled_Inverter controlled_inverter_8
endmodule

module Adress_Decode_Logic (
  input  A0,
  input  A1,
  input  A2,
  input  A3,
  input  OUT_CONTROL,
  input  E0W1,
  output CELL_0_E,
  output CELL_0_W,
  output CELL_1_E,
  output CELL_1_W,
  output CELL_2_E,
  output CELL_2_W,
  output CELL_3_E,
  output CELL_3_W,
  output CELL_4_E,
  output CELL_4_W,
  output CELL_5_E,
  output CELL_5_W,
  output CELL_6_E,
  output CELL_6_W,
  output CELL_7_E,
  output CELL_7_W,
  output CELL_8_E,
  output CELL_8_W,
  output CELL_9_E,
  output CELL_9_W,
  output CELL_10_E,
  output CELL_10_W,
  output CELL_11_E,
  output CELL_11_W,
  output CELL_12_E,
  output CELL_12_W,
  output CELL_13_E,
  output CELL_13_W,
  output CELL_14_E,
  output CELL_14_W,
  output CELL_15_E,
  output CELL_15_W
);

  wire and_1_out, and_2_out, and_3_out, and_4_out, and_5_out, and_6_out, and_7_out, and_8_out, and_9_out,
       and_10_out, and_11_out, and_12_out, and_13_out, and_14_out, and_15_out, and_16_out, and_17_out,
       and_18_out, and_19_out, and_20_out, and_21_out, and_22_out, and_23_out, and_24_out, and_25_out,
       and_26_out, and_27_out, and_28_out, and_29_out, and_30_out, and_31_out, and_32_out, not_1_out,
       not_2_out, not_3_out, not_4_out;

  not not_1 (not_1_out, A0);
  not not_2 (not_2_out, A1);
  not not_3 (not_3_out, A2);
  not not_4 (not_4_out, A3);
  and and_1 (and_1_out, not_1_out, not_2_out, not_3_out, not_4_out);
  and and_2 (and_2_out, A0, not_2_out, not_3_out, not_4_out);
  and and_3 (and_3_out, not_1_out, A1, not_3_out, not_4_out);
  and and_4 (and_4_out, A0, A1, not_3_out, not_4_out);
  and and_5 (and_5_out, not_1_out, not_2_out, A2, not_4_out);
  and and_6 (and_6_out, A0, not_2_out, A2, not_4_out);
  and and_7 (and_7_out, not_1_out, A1, A2, not_4_out);
  and and_8 (and_8_out, A0, A1, A2, not_4_out);
  and and_9 (and_9_out, not_1_out, not_2_out, not_3_out, A3);
  and and_10 (and_10_out, A0, not_2_out, not_3_out, A3);
  and and_11 (and_11_out, not_1_out, A1, not_3_out, A3);
  and and_12 (and_12_out, A0, A1, not_3_out, A3);
  and and_13 (and_13_out, not_1_out, not_2_out, A2, A3);
  and and_14 (and_14_out, A0, not_2_out, A2, A3);
  and and_15 (and_15_out, not_1_out, A1, A2, A3);
  and and_16 (and_16_out, A0, A1, A2, A3);
  and and_17 (and_17_out, and_1_out, OUT_CONTROL);
  Demultiplexer demultiplexer_1 (.out0(CELL_0_E), .out1(CELL_0_W), .in(and_17_out), .sel(E0W1));
  and and_18 (and_18_out, and_2_out, OUT_CONTROL);
  Demultiplexer demultiplexer_2 (.out0(CELL_1_E), .out1(CELL_1_W), .in(and_18_out), .sel(E0W1));
  and and_19 (and_19_out, and_3_out, OUT_CONTROL);
  Demultiplexer demultiplexer_3 (.out0(CELL_2_E), .out1(CELL_2_W), .in(and_19_out), .sel(E0W1));
  and and_20 (and_20_out, and_4_out, OUT_CONTROL);
  Demultiplexer demultiplexer_4 (.out0(CELL_3_E), .out1(CELL_3_W), .in(and_20_out), .sel(E0W1));
  and and_21 (and_21_out, and_5_out, OUT_CONTROL);
  Demultiplexer demultiplexer_5 (.out0(CELL_4_E), .out1(CELL_4_W), .in(and_21_out), .sel(E0W1));
  and and_22 (and_22_out, and_6_out, OUT_CONTROL);
  Demultiplexer demultiplexer_6 (.out0(CELL_5_E), .out1(CELL_5_W), .in(and_22_out), .sel(E0W1));
  and and_23 (and_23_out, and_7_out, OUT_CONTROL);
  Demultiplexer demultiplexer_7 (.out0(CELL_6_E), .out1(CELL_6_W), .in(and_23_out), .sel(E0W1));
  and and_24 (and_24_out, and_8_out, OUT_CONTROL);
  Demultiplexer demultiplexer_8 (.out0(CELL_7_E), .out1(CELL_7_W), .in(and_24_out), .sel(E0W1));
  and and_25 (and_25_out, and_9_out, OUT_CONTROL);
  Demultiplexer demultiplexer_9 (.out0(CELL_8_E), .out1(CELL_8_W), .in(and_25_out), .sel(E0W1));
  and and_26 (and_26_out, and_10_out, OUT_CONTROL);
  Demultiplexer demultiplexer_10 (.out0(CELL_9_E), .out1(CELL_9_W), .in(and_26_out), .sel(E0W1));
  and and_27 (and_27_out, and_11_out, OUT_CONTROL);
  Demultiplexer demultiplexer_11 (.out0(CELL_10_E), .out1(CELL_10_W), .in(and_27_out), .sel(E0W1));
  and and_28 (and_28_out, and_12_out, OUT_CONTROL);
  Demultiplexer demultiplexer_12 (.out0(CELL_11_E), .out1(CELL_11_W), .in(and_28_out), .sel(E0W1));
  and and_29 (and_29_out, and_13_out, OUT_CONTROL);
  Demultiplexer demultiplexer_13 (.out0(CELL_12_E), .out1(CELL_12_W), .in(and_29_out), .sel(E0W1));
  and and_30 (and_30_out, and_14_out, OUT_CONTROL);
  Demultiplexer demultiplexer_14 (.out0(CELL_13_E), .out1(CELL_13_W), .in(and_30_out), .sel(E0W1));
  and and_31 (and_31_out, and_15_out, OUT_CONTROL);
  Demultiplexer demultiplexer_15 (.out0(CELL_14_E), .out1(CELL_14_W), .in(and_31_out), .sel(E0W1));
  and and_32 (and_32_out, and_16_out, OUT_CONTROL);
  Demultiplexer demultiplexer_16 (.out0(CELL_15_E), .out1(CELL_15_W), .in(and_32_out), .sel(E0W1));
endmodule

module Random_Access_Memory (
  input  RST_RAM,
  input  D1,
  input  D2,
  input  D3,
  input  D4,
  input  D5,
  input  D6,
  input  D7,
  input  D8,
  input  DATA_EN,
  input  A0,
  input  A1,
  input  A2,
  input  A3,
  input  CHIP_EN,
  input  E0W1,
  output O1,
  output O2,
  output O3,
  output O4,
  output O5,
  output O6,
  output O7,
  output O8
);

  wire adress_decode_logic_1_cell_0_e, adress_decode_logic_1_cell_0_w, adress_decode_logic_1_cell_1_e,
       adress_decode_logic_1_cell_1_w, adress_decode_logic_1_cell_2_e, adress_decode_logic_1_cell_2_w,
       adress_decode_logic_1_cell_3_e, adress_decode_logic_1_cell_3_w, adress_decode_logic_1_cell_4_e,
       adress_decode_logic_1_cell_4_w, adress_decode_logic_1_cell_5_e, adress_decode_logic_1_cell_5_w,
       adress_decode_logic_1_cell_6_e, adress_decode_logic_1_cell_6_w, adress_decode_logic_1_cell_7_e,
       adress_decode_logic_1_cell_7_w, adress_decode_logic_1_cell_8_e, adress_decode_logic_1_cell_8_w,
       adress_decode_logic_1_cell_9_e, adress_decode_logic_1_cell_9_w, adress_decode_logic_1_cell_10_e,
       adress_decode_logic_1_cell_10_w, adress_decode_logic_1_cell_11_e, adress_decode_logic_1_cell_11_w,
       adress_decode_logic_1_cell_12_e, adress_decode_logic_1_cell_12_w, adress_decode_logic_1_cell_13_e,
       adress_decode_logic_1_cell_13_w, adress_decode_logic_1_cell_14_e, adress_decode_logic_1_cell_14_w,
       adress_decode_logic_1_cell_15_e, adress_decode_logic_1_cell_15_w, C0_clk, C0_v1, C0_v2, C0_v3, C0_v4,
       C0_v5, C0_v6, C0_v7, C0_v8, C1_clk, C1_v1, C1_v2, C1_v3, C1_v4, C1_v5, C1_v6, C1_v7, C1_v8, C2_clk,
       C2_v1, C2_v2, C2_v3, C2_v4, C2_v5, C2_v6, C2_v7, C2_v8, C3_clk, C3_v1, C3_v2, C3_v3, C3_v4, C3_v5,
       C3_v6, C3_v7, C3_v8, C4_clk, C4_v1, C4_v2, C4_v3, C4_v4, C4_v5, C4_v6, C4_v7, C4_v8, C5_clk, C5_v1,
       C5_v2, C5_v3, C5_v4, C5_v5, C5_v6, C5_v7, C5_v8, C6_clk, C6_v1, C6_v2, C6_v3, C6_v4, C6_v5, C6_v6,
       C6_v7, C6_v8, C7_clk, C7_v1, C7_v2, C7_v3, C7_v4, C7_v5, C7_v6, C7_v7, C7_v8, C8_clk, C8_v1, C8_v2,
       C8_v3, C8_v4, C8_v5, C8_v6, C8_v7, C8_v8, C9_clk, C9_v1, C9_v2, C9_v3, C9_v4, C9_v5, C9_v6, C9_v7,
       C9_v8, C10_clk, C10_v1, C10_v2, C10_v3, C10_v4, C10_v5, C10_v6, C10_v7, C10_v8, C11_clk, C11_v1,
       C11_v2, C11_v3, C11_v4, C11_v5, C11_v6, C11_v7, C11_v8, C12_clk, C12_v1, C12_v2, C12_v3, C12_v4,
       C12_v5, C12_v6, C12_v7, C12_v8, C13_clk, C13_v1, C13_v2, C13_v3, C13_v4, C13_v5, C13_v6, C13_v7,
       C13_v8, C14_clk, C14_v1, C14_v2, C14_v3, C14_v4, C14_v5, C14_v6, C14_v7, C14_v8, C15_clk, C15_v1,
       C15_v2, C15_v3, C15_v4, C15_v5, C15_v6, C15_v7, C15_v8, controlled_buffer_1_out,
       controlled_buffer_2_out, controlled_buffer_3_out, controlled_buffer_4_out, controlled_buffer_5_out,
       controlled_buffer_6_out, controlled_buffer_7_out, controlled_buffer_8_out;

  Adress_Decode_Logic adress_decode_logic_1 (
    .A0(A0), .A1(A1), .A2(A2), .A3(A3), .OUT_CONTROL(CHIP_EN), .E0W1(E0W1),
    .CELL_0_E(adress_decode_logic_1_cell_0_e), .CELL_0_W(adress_decode_logic_1_cell_0_w),
    .CELL_1_E(adress_decode_logic_1_cell_1_e), .CELL_1_W(adress_decode_logic_1_cell_1_w),
    .CELL_2_E(adress_decode_logic_1_cell_2_e), .CELL_2_W(adress_decode_logic_1_cell_2_w),
    .CELL_3_E(adress_decode_logic_1_cell_3_e), .CELL_3_W(adress_decode_logic_1_cell_3_w),
    .CELL_4_E(adress_decode_logic_1_cell_4_e), .CELL_4_W(adress_decode_logic_1_cell_4_w),
    .CELL_5_E(adress_decode_logic_1_cell_5_e), .CELL_5_W(adress_decode_logic_1_cell_5_w),
    .CELL_6_E(adress_decode_logic_1_cell_6_e), .CELL_6_W(adress_decode_logic_1_cell_6_w),
    .CELL_7_E(adress_decode_logic_1_cell_7_e), .CELL_7_W(adress_decode_logic_1_cell_7_w),
    .CELL_8_E(adress_decode_logic_1_cell_8_e), .CELL_8_W(adress_decode_logic_1_cell_8_w),
    .CELL_9_E(adress_decode_logic_1_cell_9_e), .CELL_9_W(adress_decode_logic_1_cell_9_w),
    .CELL_10_E(adress_decode_logic_1_cell_10_e), .CELL_10_W(adress_decode_logic_1_cell_10_w),
    .CELL_11_E(adress_decode_logic_1_cell_11_e), .CELL_11_W(adress_decode_logic_1_cell_11_w),
    .CELL_12_E(adress_decode_logic_1_cell_12_e), .CELL_12_W(adress_decode_logic_1_cell_12_w),
    .CELL_13_E(adress_decode_logic_1_cell_13_e), .CELL_13_W(adress_decode_logic_1_cell_13_w),
    .CELL_14_E(adress_decode_logic_1_cell_14_e), .CELL_14_W(adress_decode_logic_1_cell_14_w),
    .CELL_15_E(adress_decode_logic_1_cell_15_e), .CELL_15_W(adress_decode_logic_1_cell_15_w));
  assign controlled_buffer_1_out = DATA_EN ? D1 : 1'bz;  // Controlled_Buffer controlled_buffer_1
  assign controlled_buffer_2_out = DATA_EN ? D2 : 1'bz;  // Controlled_Buffer controlled_buffer_2
  assign controlled_buffer_3_out = DATA_EN ? D3 : 1'bz;  // Controlled_Buffer controlled_buffer_3
  assign controlled_buffer_4_out = DATA_EN ? D4 : 1'bz;  // Controlled_Buffer controlled_buffer_4
  assign controlled_buffer_5_out = DATA_EN ? D5 : 1'bz;  // Controlled_Buffer controlled_buffer_5
  assign controlled_buffer_6_out = DATA_EN ? D6 : 1'bz;  // Controlled_Buffer controlled_buffer_6
  assign controlled_buffer_7_out = DATA_EN ? D7 : 1'bz;  // Controlled_Buffer controlled_buffer_7
  assign controlled_buffer_8_out = DATA_EN ? D8 : 1'bz;  // Controlled_Buffer controlled_buffer_8
  LED led_1 (.in(C0_v1));
  Byte_Memory_Module C0 (
    .D1(controlled_buffer_1_out), .D2(controlled_buffer_2_out), .D3(controlled_buffer_3_out),
    .D4(controlled_buffer_4_out), .D5(controlled_buffer_5_out), .D6(controlled_buffer_6_out),
    .D7(controlled_buffer_7_out), .D8(controlled_buffer_8_out), .WR(adress_decode_logic_1_cell_0_w),
    .RESET(RST_RAM), .EN(adress_decode_logic_1_cell_0_e), .V1(C0_v1), .V2(C0_v2), .V3(C0_v3), .V4(C0_v4),
    .V5(C0_v5), .V6(C0_v6), .V7(C0_v7), .V8(C0_v8), .CLK(C0_clk), .O8(controlled_buffer_8_out),
    .O1(controlled_buffer_1_out), .O2(controlled_buffer_2_out), .O3(controlled_buffer_3_out),
    .O4(controlled_buffer_4_out), .O5(controlled_buffer_5_out), .O6(controlled_buffer_6_out),
    .O7(controlled_buffer_7_out));
  LED led_2 (.in(C0_v2));
  LED led_3 (.in(C0_v3));
  LED led_4 (.in(C0_v4));
  LED led_5 (.in(C0_v5));
  LED led_6 (.in(C0_v6));
  LED led_7 (.in(C0_v7));
  LED led_8 (.in(C0_v8));
  LED led_9 (.in(C0_clk));
  LED led_10 (.in(C4_v1));
  Byte_Memory_Module C4 (
    .D1(controlled_buffer_1_out), .D2(controlled_buffer_2_out), .D3(controlled_buffer_3_out),
    .D4(controlled_buffer_4_out), .D5(controlled_buffer_5_out), .D6(controlled_buffer_6_out),
    .D7(controlled_buffer_7_out), .D8(controlled_buffer_8_out), .WR(adress_decode_logic_1_cell_4_w),
    .RESET(RST_RAM), .EN(adress_decode_logic_1_cell_4_e), .V1(C4_v1), .V2(C4_v2), .V3(C4_v3), .V4(C4_v4),
    .V5(C4_v5), .V6(C4_v6), .V7(C4_v7), .V8(C4_v8), .CLK(C4_clk), .O8(controlled_buffer_8_out),
    .O1(controlled_buffer_1_out), .O2(controlled_buffer_2_out), .O3(controlled_buffer_3_out),
    .O4(controlled_buffer_4_out), .O5(controlled_buffer_5_out), .O6(controlled_buffer_6_out),
    .O7(controlled_buffer_7_out));
  LED led_11 (.in(C4_v2));
  LED led_12 (.in(C4_v3));
  LED led_13 (.in(C4_v4));
  LED led_14 (.in(C4_v5));
  LED led_15 (.in(C4_v6));
  LED led_16 (.in(C4_v7));
  LED led_17 (.in(C4_v8));
  LED led_18 (.in(C4_clk));
  LED led_19 (.in(C8_v1));
  Byte_Memory_Module C8 (
    .D1(controlled_buffer_1_out), .D2(controlled_buffer_2_out), .D3(controlled_buffer_3_out),
    .D4(controlled_buffer_4_out), .D5(controlled_buffer_5_out), .D6(controlled_buffer_6_out),
    .D7(controlled_buffer_7_out), .D8(controlled_buffer_8_out), .WR(adress_decode_logic_1_cell_8_w),
    .RESET(RST_RAM), .EN(adress_decode_logic_1_cell_8_e), .V1(C8_v1), .V2(C8_v2), .V3(C8_v3), .V4(C8_v4),
    .V5(C8_v5), .V6(C8_v6), .V7(C8_v7), .V8(C8_v8), .CLK(C8_clk), .O8(controlled_buffer_8_out),
    .O1(controlled_buffer_1_out), .O2(controlled_buffer_2_out), .O3(controlled_buffer_3_out),
    .O4(controlled_buffer_4_out), .O5(controlled_buffer_5_out), .O6(controlled_buffer_6_out),
    .O7(controlled_buffer_7_out));
  LED led_20 (.in(C8_v2));
  LED led_21 (.in(C8_v3));
  LED led_22 (.in(C8_v4));
  LED led_23 (.in(C8_v5));
  LED led_24 (.in(C8_v6));
  LED led_25 (.in(C8_v7));
  LED led_26 (.in(C8_v8));
  LED led_27 (.in(C8_clk));
  LED led_28 (.in(C12_v1));
  Byte_Memory_Module C12 (
    .D1(controlled_buffer_1_out), .D2(controlled_buffer_2_out), .D3(controlled_buffer_3_out),
    .D4(controlled_buffer_4_out), .D5(controlled_buffer_5_out), .D6(controlled_buffer_6_out),
    .D7(controlled_buffer_7_out), .D8(controlled_buffer_8_out), .WR(adress_decode_logic_1_cell_12_w),
    .RESET(RST_RAM), .EN(adress_decode_logic_1_cell_12_e), .V1(C12_v1), .V2(C12_v2), .V3(C12_v3),
    .V4(C12_v4), .V5(C12_v5), .V6(C12_v6), .V7(C12_v7), .V8(C12_v8), .CLK(C12_clk),
    .O8(controlled_buffer_8_out), .O1(controlled_buffer_1_out), .O2(controlled_buffer_2_out),
    .O3(controlled_buffer_3_out), .O4(controlled_buffer_4_out), .O5(controlled_buffer_5_out),
    .O6(controlled_buffer_6_out), .O7(controlled_buffer_7_out));
  LED led_29 (.in(C12_v2));
  LED led_30 (.in(C12_v3));
  LED led_31 (.in(C12_v4));
  LED led_32 (.in(C12_v5));
  LED led_33 (.in(C12_v6));
  LED led_34 (.in(C12_v7));
  LED led_35 (.in(C12_v8));
  LED led_36 (.in(C12_clk));
  LED led_37 (.in(C1_v1));
  Byte_Memory_Module C1 (
    .D1(controlled_buffer_1_out), .D2(controlled_buffer_2_out), .D3(controlled_buffer_3_out),
    .D4(controlled_buffer_4_out), .D5(controlled_buffer_5_out), .D6(controlled_buffer_6_out),
    .D7(controlled_buffer_7_out), .D8(controlled_buffer_8_out), .WR(adress_decode_logic_1_cell_1_w),
    .RESET(RST_RAM), .EN(adress_decode_logic_1_cell_1_e), .V1(C1_v1), .V2(C1_v2), .V3(C1_v3), .V4(C1_v4),
    .V5(C1_v5), .V6(C1_v6), .V7(C1_v7), .V8(C1_v8), .CLK(C1_clk), .O8(controlled_buffer_8_out),
    .O1(controlled_buffer_1_out), .O2(controlled_buffer_2_out), .O3(controlled_buffer_3_out),
    .O4(controlled_buffer_4_out), .O5(controlled_buffer_5_out), .O6(controlled_buffer_6_out),
    .O7(controlled_buffer_7_out));
  LED led_38 (.in(C1_v2));
  LED led_39 (.in(C1_v3));
  LED led_40 (.in(C1_v4));
  LED led_41 (.in(C1_v5));
  LED led_42 (.in(C1_v6));
  LED led_43 (.in(C1_v7));
  LED led_44 (.in(C1_v8));
  LED led_45 (.in(C1_clk));
  LED led_46 (.in(C5_v1));
  Byte_Memory_Module C5 (
    .D1(controlled_buffer_1_out), .D2(controlled_buffer_2_out), .D3(controlled_buffer_3_out),
    .D4(controlled_buffer_4_out), .D5(controlled_buffer_5_out), .D6(controlled_buffer_6_out),
    .D7(controlled_buffer_7_out), .D8(controlled_buffer_8_out), .WR(adress_decode_logic_1_cell_5_w),
    .RESET(RST_RAM), .EN(adress_decode_logic_1_cell_5_e), .V1(C5_v1), .V2(C5_v2), .V3(C5_v3), .V4(C5_v4),
    .V5(C5_v5), .V6(C5_v6), .V7(C5_v7), .V8(C5_v8), .CLK(C5_clk), .O8(controlled_buffer_8_out),
    .O1(controlled_buffer_1_out), .O2(controlled_buffer_2_out), .O3(controlled_buffer_3_out),
    .O4(controlled_buffer_4_out), .O5(controlled_buffer_5_out), .O6(controlled_buffer_6_out),
    .O7(controlled_buffer_7_out));
  LED led_47 (.in(C5_v2));
  LED led_48 (.in(C5_v3));
  LED led_49 (.in(C5_v4));
  LED led_50 (.in(C5_v5));
  LED led_51 (.in(C5_v6));
  LED led_52 (.in(C5_v7));
  LED led_53 (.in(C5_v8));
  LED led_54 (.in(C5_clk));
  LED led_55 (.in(C9_v1));
  Byte_Memory_Module C9 (
    .D1(controlled_buffer_1_out), .D2(controlled_buffer_2_out), .D3(controlled_buffer_3_out),
    .D4(controlled_buffer_4_out), .D5(controlled_buffer_5_out), .D6(controlled_buffer_6_out),
    .D7(controlled_buffer_7_out), .D8(controlled_buffer_8_out), .WR(adress_decode_logic_1_cell_9_w),
    .RESET(RST_RAM), .EN(adress_decode_logic_1_cell_9_e), .V1(C9_v1), .V2(C9_v2), .V3(C9_v3), .V4(C9_v4),
    .V5(C9_v5), .V6(C9_v6), .V7(C9_v7), .V8(C9_v8), .CLK(C9_clk), .O8(controlled_buffer_8_out),
    .O1(controlled_buffer_1_out), .O2(controlled_buffer_2_out), .O3(controlled_buffer_3_out),
    .O4(controlled_buffer_4_out), .O5(controlled_buffer_5_out), .O6(controlled_buffer_6_out),
    .O7(controlled_buffer_7_out));
  LED led_56 (.in(C9_v2));
  LED led_57 (.in(C9_v3));
  LED led_58 (.in(C9_v4));
  LED led_59 (.in(C9_v5));
  LED led_60 (.in(C9_v6));
  LED led_61 (.in(C9_v7));
  LED led_62 (.in(C9_v8));
  LED led_63 (.in(C9_clk));
  LED led_64 (.in(C13_v1));
  Byte_Memory_Module C13 (
    .D1(controlled_buffer_1_out), .D2(controlled_buffer_2_out), .D3(controlled_buffer_3_out),
    .D4(controlled_buffer_4_out), .D5(controlled_buffer_5_out), .D6(controlled_buffer_6_out),
    .D7(controlled_buffer_7_out), .D8(controlled_buffer_8_out), .WR(adress_decode_logic_1_cell_13_w),
    .RESET(RST_RAM), .EN(adress_decode_logic_1_cell_13_e), .V1(C13_v1), .V2(C13_v2), .V3(C13_v3),
    .V4(C13_v4), .V5(C13_v5), .V6(C13_v6), .V7(C13_v7), .V8(C13_v8), .CLK(C13_clk),
    .O8(controlled_buffer_8_out), .O1(controlled_buffer_1_out), .O2(controlled_buffer_2_out),
    .O3(controlled_buffer_3_out), .O4(controlled_buffer_4_out), .O5(controlled_buffer_5_out),
    .O6(controlled_buffer_6_out), .O7(controlled_buffer_7_out));
  LED led_65 (.in(C13_v2));
  LED led_66 (.in(C13_v3));
  LED led_67 (.in(C13_v4));
  LED led_68 (.in(C13_v5));
  LED led_69 (.in(C13_v6));
  LED led_70 (.in(C13_v7));
  LED led_71 (.in(C13_v8));
  LED led_72 (.in(C13_clk));
  LED led_73 (.in(C2_v1));
  Byte_Memory_Module C2 (
    .D1(controlled_buffer_1_out), .D2(controlled_buffer_2_out), .D3(controlled_buffer_3_out),
    .D4(controlled_buffer_4_out), .D5(controlled_buffer_5_out), .D6(controlled_buffer_6_out),
    .D7(controlled_buffer_7_out), .D8(controlled_buffer_8_out), .WR(adress_decode_logic_1_cell_2_w),
    .RESET(RST_RAM), .EN(adress_decode_logic_1_cell_2_e), .V1(C2_v1), .V2(C2_v2), .V3(C2_v3), .V4(C2_v4),
    .V5(C2_v5), .V6(C2_v6), .V7(C2_v7), .V8(C2_v8), .CLK(C2_clk), .O8(controlled_buffer_8_out),
    .O1(controlled_buffer_1_out), .O2(controlled_buffer_2_out), .O3(controlled_buffer_3_out),
    .O4(controlled_buffer_4_out), .O5(controlled_buffer_5_out), .O6(controlled_buffer_6_out),
    .O7(controlled_buffer_7_out));
  LED led_74 (.in(C2_v2));
  LED led_75 (.in(C2_v3));
  LED led_76 (.in(C2_v4));
  LED led_77 (.in(C2_v5));
  LED led_78 (.in(C2_v6));
  LED led_79 (.in(C2_v7));
  LED led_80 (.in(C2_v8));
  LED led_81 (.in(C2_clk));
  LED led_82 (.in(C6_v1));
  Byte_Memory_Module C6 (
    .D1(controlled_buffer_1_out), .D2(controlled_buffer_2_out), .D3(controlled_buffer_3_out),
    .D4(controlled_buffer_4_out), .D5(controlled_buffer_5_out), .D6(controlled_buffer_6_out),
    .D7(controlled_buffer_7_out), .D8(controlled_buffer_8_out), .WR(adress_decode_logic_1_cell_6_w),
    .RESET(RST_RAM), .EN(adress_decode_logic_1_cell_6_e), .V1(C6_v1), .V2(C6_v2), .V3(C6_v3), .V4(C6_v4),
    .V5(C6_v5), .V6(C6_v6), .V7(C6_v7), .V8(C6_v8), .CLK(C6_clk), .O8(controlled_buffer_8_out),
    .O1(controlled_buffer_1_out), .O2(controlled_buffer_2_out), .O3(controlled_buffer_3_out),
    .O4(controlled_buffer_4_out), .O5(controlled_buffer_5_out), .O6(controlled_buffer_6_out),
    .O7(controlled_buffer_7_out));
  LED led_83 (.in(C6_v2));
  LED led_84 (.in(C6_v3));
  LED led_85 (.in(C6_v4));
  LED led_86 (.in(C6_v5));
  LED led_87 (.in(C6_v6));
  LED led_88 (.in(C6_v7));
  LED led_89 (.in(C6_v8));
  LED led_90 (.in(C6_clk));
  LED led_91 (.in(C10_v1));
  Byte_Memory_Module C10 (
    .D1(controlled_buffer_1_out), .D2(controlled_buffer_2_out), .D3(controlled_buffer_3_out),
    .D4(controlled_buffer_4_out), .D5(controlled_buffer_5_out), .D6(controlled_buffer_6_out),
    .D7(controlled_buffer_7_out), .D8(controlled_buffer_8_out), .WR(adress_decode_logic_1_cell_10_w),
    .RESET(RST_RAM), .EN(adress_decode_logic_1_cell_10_e), .V1(C10_v1), .V2(C10_v2), .V3(C10_v3),
    .V4(C10_v4), .V5(C10_v5), .V6(C10_v6), .V7(C10_v7), .V8(C10_v8), .CLK(C10_clk),
    .O8(controlled_buffer_8_out), .O1(controlled_buffer_1_out), .O2(controlled_buffer_2_out),
    .O3(controlled_buffer_3_out), .O4(controlled_buffer_4_out), .O5(controlled_buffer_5_out),
    .O6(controlled_buffer_6_out), .O7(controlled_buffer_7_out));
  LED led_92 (.in(C10_v2));
  LED led_93 (.in(C10_v3));
  LED led_94 (.in(C10_v4));
  LED led_95 (.in(C10_v5));
  LED led_96 (.in(C10_v6));
  LED led_97 (.in(C10_v7));
  LED led_98 (.in(C10_v8));
  LED led_99 (.in(C10_clk));
  LED led_100 (.in(C14_v1));
  Byte_Memory_Module C14 (
    .D1(controlled_buffer_1_out), .D2(controlled_buffer_2_out), .D3(controlled_buffer_3_out),
    .D4(controlled_buffer_4_out), .D5(controlled_buffer_5_out), .D6(controlled_buffer_6_out),
    .D7(controlled_buffer_7_out), .D8(controlled_buffer_8_out), .WR(adress_decode_logic_1_cell_14_w),
    .RESET(RST_RAM), .EN(adress_decode_logic_1_cell_14_e), .V1(C14_v1), .V2(C14_v2), .V3(C14_v3),
    .V4(C14_v4), .V5(C14_v5), .V6(C14_v6), .V7(C14_v7), .V8(C14_v8), .CLK(C14_clk),
    .O8(controlled_buffer_8_out), .O1(controlled_buffer_1_out), .O2(controlled_buffer_2_out),
    .O3(controlled_buffer_3_out), .O4(controlled_buffer_4_out), .O5(controlled_buffer_5_out),
    .O6(controlled_buffer_6_out), .O7(controlled_buffer_7_out));
  LED led_101 (.in(C14_v2));
  LED led_102 (.in(C14_v3));
  LED led_103 (.in(C14_v4));
  LED led_104 (.in(C14_v5));
  LED led_105 (.in(C14_v6));
  LED led_106 (.in(C14_v7));
  LED led_107 (.in(C14_v8));
  LED led_108 (.in(C14_clk));
  LED led_109 (.in(C3_v1));
  Byte_Memory_Module C3 (
    .D1(controlled_buffer_1_out), .D2(controlled_buffer_2_out), .D3(controlled_buffer_3_out),
    .D4(controlled_buffer_4_out), .D5(controlled_buffer_5_out), .D6(controlled_buffer_6_out),
    .D7(controlled_buffer_7_out), .D8(controlled_buffer_8_out), .WR(adress_decode_logic_1_cell_3_w),
    .RESET(RST_RAM), .EN(adress_decode_logic_1_cell_3_e), .V1(C3_v1), .V2(C3_v2), .V3(C3_v3), .V4(C3_v4),
    .V5(C3_v5), .V6(C3_v6), .V7(C3_v7), .V8(C3_v8), .CLK(C3_clk), .O8(controlled_buffer_8_out),
    .O1(controlled_buffer_1_out), .O2(controlled_buffer_2_out), .O3(controlled_buffer_3_out),
    .O4(controlled_buffer_4_out), .O5(controlled_buffer_5_out), .O6(controlled_buffer_6_out),
    .O7(controlled_buffer_7_out));
  LED led_110 (.in(C3_v2));
  LED led_111 (.in(C3_v3));
  LED led_112 (.in(C3_v4));
  LED led_113 (.in(C3_v5));
  LED led_114 (.in(C3_v6));
  LED led_115 (.in(C3_v7));
  LED led_116 (.in(C3_v8));
  LED led_117 (.in(C3_clk));
  LED led_118 (.in(C7_v1));
  Byte_Memory_Module C7 (
    .D1(controlled_buffer_1_out), .D2(controlled_buffer_2_out), .D3(controlled_buffer_3_out),
    .D4(controlled_buffer_4_out), .D5(controlled_buffer_5_out), .D6(controlled_buffer_6_out),
    .D7(controlled_buffer_7_out), .D8(controlled_buffer_8_out), .WR(adress_decode_logic_1_cell_7_w),
    .RESET(RST_RAM), .EN(adress_decode_logic_1_cell_7_e), .V1(C7_v1), .V2(C7_v2), .V3(C7_v3), .V4(C7_v4),
    .V5(C7_v5), .V6(C7_v6), .V7(C7_v7), .V8(C7_v8), .CLK(C7_clk), .O8(controlled_buffer_8_out),
    .O1(controlled_buffer_1_out), .O2(controlled_buffer_2_out), .O3(controlled_buffer_3_out),
    .O4(controlled_buffer_4_out), .O5(controlled_buffer_5_out), .O6(controlled_buffer_6_out),
    .O7(controlled_buffer_7_out));
  LED led_119 (.in(C7_v2));
  LED led_120 (.in(C7_v3));
  LED led_121 (.in(C7_v4));
  LED led_122 (.in(C7_v5));
  LED led_123 (.in(C7_v6));
  LED led_124 (.in(C7_v7));
  LED led_125 (.in(C7_v8));
  LED led_126 (.in(C7_clk));
  LED led_127 (.in(C11_v1));
  Byte_Memory_Module C11 (
    .D1(controlled_buffer_1_out), .D2(controlled_buffer_2_out), .D3(controlled_buffer_3_out),
    .D4(controlled_buffer_4_out), .D5(controlled_buffer_5_out), .D6(controlled_buffer_6_out),
    .D7(controlled_buffer_7_out), .D8(controlled_buffer_8_out), .WR(adress_decode_logic_1_cell_11_w),
    .RESET(RST_RAM), .EN(adress_decode_logic_1_cell_11_e), .V1(C11_v1), .V2(C11_v2), .V3(C11_v3),
    .V4(C11_v4), .V5(C11_v5), .V6(C11_v6), .V7(C11_v7), .V8(C11_v8), .CLK(C11_clk),
    .O8(controlled_buffer_8_out), .O1(controlled_buffer_1_out), .O2(controlled_buffer_2_out),
    .O3(controlled_buffer_3_out), .O4(controlled_buffer_4_out), .O5(controlled_buffer_5_out),
    .O6(controlled_buffer_6_out), .O7(controlled_buffer_7_out));
  LED led_128 (.in(C11_v2));
  LED led_129 (.in(C11_v3));
  LED led_130 (.in(C11_v4));
  LED led_131 (.in(C11_v5));
  LED led_132 (.in(C11_v6));
  LED led_133 (.in(C11_v7));
  LED led_134 (.in(C11_v8));
  LED led_135 (.in(C11_clk));
  LED led_136 (.in(C15_v1));
  Byte_Memory_Module C15 (
    .D1(controlled_buffer_1_out), .D2(controlled_buffer_2_out), .D3(controlled_buffer_3_out),
    .D4(controlled_buffer_4_out), .D5(controlled_buffer_5_out), .D6(controlled_buffer_6_out),
    .D7(controlled_buffer_7_out), .D8(controlled_buffer_8_out), .WR(adress_decode_logic_1_cell_15_w),
    .RESET(RST_RAM), .EN(adress_decode_logic_1_cell_15_e), .V1(C15_v1), .V2(C15_v2), .V3(C15_v3),
    .V4(C15_v4), .V5(C15_v5), .V6(C15_v6), .V7(C15_v7), .V8(C15_v8), .CLK(C15_clk),
    .O8(controlled_buffer_8_out), .O1(controlled_buffer_1_out), .O2(controlled_buffer_2_out),
    .O3(controlled_buffer_3_out), .O4(controlled_buffer_4_out), .O5(controlled_buffer_5_out),
    .O6(controlled_buffer_6_out), .O7(controlled_buffer_7_out));
  LED led_137 (.in(C15_v2));
  LED led_138 (.in(C15_v3));
  LED led_139 (.in(C15_v4));
  LED led_140 (.in(C15_v5));
  LED led_141 (.in(C15_v6));
  LED led_142 (.in(C15_v7));
  LED led_143 (.in(C15_v8));
  LED led_144 (.in(C15_clk));
  assign O1 = controlled_buffer_1_out ? controlled_buffer_1_out : 1'bz;  // Controlled_Buffer controlled_buffer_9
  assign O2 = controlled_buffer_2_out ? controlled_buffer_2_out : 1'bz;  // Controlled_Buffer controlled_buffer_10
  assign O7 = controlled_buffer_7_out ? controlled_buffer_7_out : 1'bz;  // Controlled_Buffer controlled_buffer_11
  assign O8 = controlled_buffer_8_out ? controlled_buffer_8_out : 1'bz;  // Controlled_Buffer controlled_buffer_12
  assign O3 = controlled_buffer_3_out ? controlled_buffer_3_out : 1'bz;  // Controlled_Buffer controlled_buffer_13
  assign O5 = controlled_buffer_5_out ? controlled_buffer_5_out : 1'bz;  // Controlled_Buffer controlled_buffer_14
  assign O6 = controlled_buffer_6_out ? controlled_buffer_6_out : 1'bz;  // Controlled_Buffer controlled_buffer_15
  assign O4 = controlled_buffer_4_out ? controlled_buffer_4_out : 1'bz;  // Controlled_Buffer controlled_buffer_16
endmodule

module Program_Counter (
  input  RST,
  input  CLK,
  input  D1,
  input  D2,
  input  D3,
  input  D4,
  input  CTR_EN,
  input  BUS_LOAD,
  input  BUS_ENABLE,
  output V1,
  output V2,
  output V3,
  output V4,
  output O1,
  output O2,
  output O3,
  output O4
);

  wire n74245_1_pin1, not_1_out, not_2_out, not_3_out;

  not not_1 (not_1_out, RST);
  not not_2 (not_2_out, BUS_LOAD);
  not not_3 (not_3_out, BUS_ENABLE);
  _74161 u_74161_1 (
    .pin1(not_1_out), .pin2(CLK), .pin3(D1), .pin4(D2), .pin5(D3), .pin6(D4), .pin7(CTR_EN), .pin14(V1),
    .pin13(V2), .pin12(V3), .pin11(V4), .pin10(CTR_EN), .pin9(not_2_out));  // open: pin15
  _74245 u_74245_1 (
    .pin1(n74245_1_pin1), .pin2(V1), .pin3(V2), .pin4(V3), .pin5(V4), .pin19(not_3_out), .pin18(O1),
    .pin17(O2), .pin16(O3), .pin15(O4));  // open: pin6, pin7, pin8, pin9, pin14, pin13, pin12, pin11
  LED led_1 (.in(O4));
  LED led_2 (.in(O3));
  LED led_3 (.in(O2));
  LED led_4 (.in(O1));
  // also tied to VCC on the sheet: n74245_1_pin1
endmodule

module Memory_Address_Register (
  input  CLR,
  input  A0,
  input  A1,
  input  A2,
  input  A3,
  input  CLK,
  input  LOAD,
  input  ENABLE,
  output O1,
  output O2,
  output O3,
  output O4
);

  wire and_1_out, controlled_buffer_1_out, controlled_buffer_2_out, controlled_buffer_3_out,
       controlled_buffer_4_out, controlled_buffer_5_out, controlled_buffer_6_out, controlled_buffer_7_out,
       controlled_buffer_8_out, n74175_1_pin2, n74175_1_pin7, n74175_1_pin10, n74175_1_pin15, n74245_1_pin1,
       not_1_out, not_2_out, undriven, undriven_2, undriven_3, undriven_4;

  not not_1 (not_1_out, CLR);
  assign controlled_buffer_1_out = A0 ? A0 : 1'bz;  // Controlled_Buffer controlled_buffer_1
  assign controlled_buffer_2_out = A1 ? A1 : 1'bz;  // Controlled_Buffer controlled_buffer_2
  assign controlled_buffer_3_out = A2 ? A2 : 1'bz;  // Controlled_Buffer controlled_buffer_3
  assign controlled_buffer_4_out = A3 ? A3 : 1'bz;  // Controlled_Buffer controlled_buffer_4
  assign controlled_buffer_5_out = undriven ? undriven : 1'bz;  // Controlled_Buffer controlled_buffer_5
  assign controlled_buffer_6_out = undriven_2 ? undriven_2 : 1'bz;  // Controlled_Buffer controlled_buffer_6
  assign controlled_buffer_7_out = undriven_3 ? undriven_3 : 1'bz;  // Controlled_Buffer controlled_buffer_7
  assign controlled_buffer_8_out = undriven_4 ? undriven_4 : 1'bz;  // Controlled_Buffer controlled_buffer_8
  and and_1 (and_1_out, CLK, LOAD);
  LED led_1 (.in(n74175_1_pin2));
  LED led_2 (.in(n74175_1_pin7));
  LED led_3 (.in(n74175_1_pin10));
  LED led_4 (.in(n74175_1_pin15));
  _74175 u_74175_1 (
    .pin1(not_1_out), .pin2(n74175_1_pin2), .pin4(controlled_buffer_1_out), .pin5(controlled_buffer_2_out),
    .pin7(n74175_1_pin7), .pin15(n74175_1_pin15), .pin13(controlled_buffer_4_out),
    .pin12(controlled_buffer_3_out), .pin10(n74175_1_pin10), .pin9(and_1_out));  // open: pin3, pin6, pin14, pin11
  _74175 u_74175_2 (
    .pin1(not_1_out), .pin4(controlled_buffer_5_out), .pin5(controlled_buffer_6_out),
    .pin13(controlled_buffer_8_out), .pin12(controlled_buffer_7_out), .pin9(and_1_out));  // open: pin2, pin3, pin6, pin7, pin15, pin14, pin11, pin10
  not not_2 (not_2_out, ENABLE);
  _74245 u_74245_1 (
    .pin1(n74245_1_pin1), .pin2(n74175_1_pin2), .pin3(n74175_1_pin7), .pin4(n74175_1_pin10),
    .pin5(n74175_1_pin15), .pin19(not_2_out), .pin18(O1), .pin17(O2), .pin16(O3), .pin15(O4));  // open: pin6, pin7, pin8, pin9, pin14, pin13, pin12, pin11
  // also tied to VCC on the sheet: n74245_1_pin1

  // Notes on the sheet:
  //   DATA
  //   Data Input Module
  //   Data Output Module
endmodule

module Instruction_Register (
  input  CLR,
  input  BUS1,
  input  BUS2,
  input  BUS3,
  input  BUS4,
  input  BUS5,
  input  BUS6,
  input  BUS7,
  input  BUS8,
  input  CLK,
  input  LOAD,
  input  ENABLE,
  output O1,
  output O2,
  output O3,
  output O4,
  output O5,
  output O6,
  output O7,
  output O8
);

  wire and_1_out, controlled_buffer_1_out, controlled_buffer_2_out, controlled_buffer_3_out,
       controlled_buffer_4_out, controlled_buffer_5_out, controlled_buffer_6_out, controlled_buffer_7_out,
       controlled_buffer_8_out, n74175_1_pin2, n74175_1_pin7, n74175_1_pin10, n74175_1_pin15, n74175_2_pin2,
       n74175_2_pin7, n74175_2_pin11, n74175_2_pin15, n74245_1_pin1, not_1_out, not_2_out, not_3_out;

  not not_1 (not_1_out, CLR);
  assign controlled_buffer_1_out = BUS1 ? BUS1 : 1'bz;  // Controlled_Buffer controlled_buffer_1
  assign controlled_buffer_2_out = BUS2 ? BUS2 : 1'bz;  // Controlled_Buffer controlled_buffer_2
  assign controlled_buffer_3_out = BUS3 ? BUS3 : 1'bz;  // Controlled_Buffer controlled_buffer_3
  assign controlled_buffer_4_out = BUS4 ? BUS4 : 1'bz;  // Controlled_Buffer controlled_buffer_4
  assign controlled_buffer_5_out = BUS5 ? BUS5 : 1'bz;  // Controlled_Buffer controlled_buffer_5
  assign controlled_buffer_6_out = BUS6 ? BUS6 : 1'bz;  // Controlled_Buffer controlled_buffer_6
  assign controlled_buffer_7_out = BUS7 ? BUS7 : 1'bz;  // Controlled_Buffer controlled_buffer_7
  assign controlled_buffer_8_out = BUS8 ? BUS8 : 1'bz;  // Controlled_Buffer controlled_buffer_8
  and and_1 (and_1_out, CLK, LOAD);
  LED led_1 (.in(n74175_1_pin2));
  LED led_2 (.in(n74175_1_pin7));
  LED led_3 (.in(n74175_1_pin10));
  LED led_4 (.in(n74175_1_pin15));
  _74175 u_74175_1 (
    .pin1(not_1_out), .pin2(n74175_1_pin2), .pin4(controlled_buffer_1_out), .pin5(controlled_buffer_2_out),
    .pin7(n74175_1_pin7), .pin15(n74175_1_pin15), .pin13(controlled_buffer_4_out),
    .pin12(controlled_buffer_3_out), .pin10(n74175_1_pin10), .pin9(and_1_out));  // open: pin3, pin6, pin14, pin11
  _74175 u_74175_2 (
    .pin1(not_1_out), .pin2(n74175_2_pin2), .pin4(controlled_buffer_5_out), .pin5(controlled_buffer_6_out),
    .pin7(n74175_2_pin7), .pin15(n74175_2_pin15), .pin13(controlled_buffer_8_out),
    .pin12(controlled_buffer_7_out), .pin11(n74175_2_pin11), .pin9(and_1_out));  // open: pin3, pin6, pin14, pin10
  LED led_5 (.in(n74175_2_pin2));
  LED led_6 (.in(n74175_2_pin7));
  LED led_7 (.in(not_2_out));
  LED led_8 (.in(n74175_2_pin15));
  not not_2 (not_2_out, n74175_2_pin11);
  not not_3 (not_3_out, ENABLE);
  _74245 u_74245_1 (
    .pin1(n74245_1_pin1), .pin2(n74175_1_pin2), .pin3(n74175_1_pin7), .pin4(n74175_1_pin10),
    .pin5(n74175_1_pin15), .pin6(n74175_2_pin2), .pin7(n74175_2_pin7), .pin8(not_2_out),
    .pin9(n74175_2_pin15), .pin19(not_3_out), .pin18(O1), .pin17(O2), .pin16(O3), .pin15(O4), .pin14(O5),
    .pin13(O6), .pin12(O7), .pin11(O8));
  // also tied to VCC on the sheet: n74245_1_pin1

  // Notes on the sheet:
  //   DATA
  //   Data Input Module
  //   Data Output Module
endmodule

module PROM_Chip (
  input  a,
  input  b,
  input  c,
  input  d,
  input  e,
  input  f,
  input  g,
  input  DATA_ENABLE,
  input  RESET,
  input  AO,
  input  A1,
  input  A2,
  input  A3,
  input  CHIP_ENABLE,
  input  E0W1,
  output disp_a,
  output disp_b,
  output disp_c,
  output disp_d,
  output disp_e,
  output disp_f,
  output disp_g,
  output CLK
);

  wire adress_decode_logic_1_cell_0_e, adress_decode_logic_1_cell_0_w, adress_decode_logic_1_cell_1_e,
       adress_decode_logic_1_cell_1_w, adress_decode_logic_1_cell_2_e, adress_decode_logic_1_cell_2_w,
       adress_decode_logic_1_cell_3_e, adress_decode_logic_1_cell_3_w, adress_decode_logic_1_cell_4_e,
       adress_decode_logic_1_cell_4_w, adress_decode_logic_1_cell_5_e, adress_decode_logic_1_cell_5_w,
       adress_decode_logic_1_cell_6_e, adress_decode_logic_1_cell_6_w, adress_decode_logic_1_cell_7_e,
       adress_decode_logic_1_cell_7_w, adress_decode_logic_1_cell_8_e, adress_decode_logic_1_cell_8_w,
       adress_decode_logic_1_cell_9_e, adress_decode_logic_1_cell_9_w, adress_decode_logic_1_cell_10_e,
       adress_decode_logic_1_cell_10_w, adress_decode_logic_1_cell_11_e, adress_decode_logic_1_cell_11_w,
       adress_decode_logic_1_cell_12_e, adress_decode_logic_1_cell_12_w, adress_decode_logic_1_cell_13_e,
       adress_decode_logic_1_cell_13_w, adress_decode_logic_1_cell_14_e, adress_decode_logic_1_cell_14_w,
       adress_decode_logic_1_cell_15_e, adress_decode_logic_1_cell_15_w, C0_clk, C0_v1, C0_v2, C0_v3, C0_v4,
       C0_v5, C0_v6, C0_v7, C0_v8, C1_clk, C1_v1, C1_v2, C1_v3, C1_v4, C1_v5, C1_v6, C1_v7, C1_v8, C2_clk,
       C2_v1, C2_v2, C2_v3, C2_v4, C2_v5, C2_v6, C2_v7, C2_v8, C3_clk, C3_v1, C3_v2, C3_v3, C3_v4, C3_v5,
       C3_v6, C3_v7, C3_v8, C4_v1, C4_v2, C4_v3, C4_v4, C4_v5, C4_v6, C4_v7, C4_v8, C5_clk, C5_v1, C5_v2,
       C5_v3, C5_v4, C5_v5, C5_v6, C5_v7, C5_v8, C6_clk, C6_v1, C6_v2, C6_v3, C6_v4, C6_v5, C6_v6, C6_v7,
       C6_v8, C7_clk, C7_v1, C7_v2, C7_v3, C7_v4, C7_v5, C7_v6, C7_v7, C7_v8, C8_clk, C8_v1, C8_v2, C8_v3,
       C8_v4, C8_v5, C8_v6, C8_v7, C8_v8, C9_clk, C9_v1, C9_v2, C9_v3, C9_v4, C9_v5, C9_v6, C9_v7, C9_v8,
       C10_clk, C10_v1, C10_v2, C10_v3, C10_v4, C10_v5, C10_v6, C10_v7, C10_v8, C11_clk, C11_v1, C11_v2,
       C11_v3, C11_v4, C11_v5, C11_v6, C11_v7, C11_v8, C12_clk, C12_v1, C12_v2, C12_v3, C12_v4, C12_v5,
       C12_v6, C12_v7, C12_v8, C13_clk, C13_v1, C13_v2, C13_v3, C13_v4, C13_v5, C13_v6, C13_v7, C13_v8,
       C14_clk, C14_v1, C14_v2, C14_v3, C14_v4, C14_v5, C14_v6, C14_v7, C14_v8, C15_clk, C15_v1, C15_v2,
       C15_v3, C15_v4, C15_v5, C15_v6, C15_v7, C15_v8, controlled_buffer_8_out, undriven;

  Adress_Decode_Logic adress_decode_logic_1 (
    .A0(AO), .A1(A1), .A2(A2), .A3(A3), .OUT_CONTROL(CHIP_ENABLE), .E0W1(E0W1),
    .CELL_0_E(adress_decode_logic_1_cell_0_e), .CELL_0_W(adress_decode_logic_1_cell_0_w),
    .CELL_1_E(adress_decode_logic_1_cell_1_e), .CELL_1_W(adress_decode_logic_1_cell_1_w),
    .CELL_2_E(adress_decode_logic_1_cell_2_e), .CELL_2_W(adress_decode_logic_1_cell_2_w),
    .CELL_3_E(adress_decode_logic_1_cell_3_e), .CELL_3_W(adress_decode_logic_1_cell_3_w),
    .CELL_4_E(adress_decode_logic_1_cell_4_e), .CELL_4_W(adress_decode_logic_1_cell_4_w),
    .CELL_5_E(adress_decode_logic_1_cell_5_e), .CELL_5_W(adress_decode_logic_1_cell_5_w),
    .CELL_6_E(adress_decode_logic_1_cell_6_e), .CELL_6_W(adress_decode_logic_1_cell_6_w),
    .CELL_7_E(adress_decode_logic_1_cell_7_e), .CELL_7_W(adress_decode_logic_1_cell_7_w),
    .CELL_8_E(adress_decode_logic_1_cell_8_e), .CELL_8_W(adress_decode_logic_1_cell_8_w),
    .CELL_9_E(adress_decode_logic_1_cell_9_e), .CELL_9_W(adress_decode_logic_1_cell_9_w),
    .CELL_10_E(adress_decode_logic_1_cell_10_e), .CELL_10_W(adress_decode_logic_1_cell_10_w),
    .CELL_11_E(adress_decode_logic_1_cell_11_e), .CELL_11_W(adress_decode_logic_1_cell_11_w),
    .CELL_12_E(adress_decode_logic_1_cell_12_e), .CELL_12_W(adress_decode_logic_1_cell_12_w),
    .CELL_13_E(adress_decode_logic_1_cell_13_e), .CELL_13_W(adress_decode_logic_1_cell_13_w),
    .CELL_14_E(adress_decode_logic_1_cell_14_e), .CELL_14_W(adress_decode_logic_1_cell_14_w),
    .CELL_15_E(adress_decode_logic_1_cell_15_e), .CELL_15_W(adress_decode_logic_1_cell_15_w));
  assign disp_a = DATA_ENABLE ? a : 1'bz;  // Controlled_Buffer controlled_buffer_1
  assign disp_b = DATA_ENABLE ? b : 1'bz;  // Controlled_Buffer controlled_buffer_2
  assign disp_c = DATA_ENABLE ? c : 1'bz;  // Controlled_Buffer controlled_buffer_3
  assign disp_d = DATA_ENABLE ? d : 1'bz;  // Controlled_Buffer controlled_buffer_4
  assign disp_e = DATA_ENABLE ? e : 1'bz;  // Controlled_Buffer controlled_buffer_5
  assign disp_f = DATA_ENABLE ? f : 1'bz;  // Controlled_Buffer controlled_buffer_6
  assign disp_g = DATA_ENABLE ? g : 1'bz;  // Controlled_Buffer controlled_buffer_7
  assign controlled_buffer_8_out = DATA_ENABLE ? undriven : 1'bz;  // Controlled_Buffer controlled_buffer_8
  LED led_1 (.in(C0_v1));
  Byte_Memory_Module C0 (
    .D1(disp_a), .D2(disp_b), .D3(disp_c), .D4(disp_d), .D5(disp_e), .D6(disp_f), .D7(disp_g),
    .D8(controlled_buffer_8_out), .WR(adress_decode_logic_1_cell_0_w), .RESET(RESET),
    .EN(adress_decode_logic_1_cell_0_e), .V1(C0_v1), .V2(C0_v2), .V3(C0_v3), .V4(C0_v4), .V5(C0_v5),
    .V6(C0_v6), .V7(C0_v7), .V8(C0_v8), .CLK(C0_clk), .O8(controlled_buffer_8_out), .O1(disp_a), .O2(disp_b),
    .O3(disp_c), .O4(disp_d), .O5(disp_e), .O6(disp_f), .O7(disp_g));
  LED led_2 (.in(C0_v2));
  LED led_3 (.in(C0_v3));
  LED led_4 (.in(C0_v4));
  LED led_5 (.in(C0_v5));
  LED led_6 (.in(C0_v6));
  LED led_7 (.in(C0_v7));
  LED led_8 (.in(C0_v8));
  LED led_9 (.in(C0_clk));
  LED led_10 (.in(C4_v1));
  Byte_Memory_Module C4 (
    .D1(disp_a), .D2(disp_b), .D3(disp_c), .D4(disp_d), .D5(disp_e), .D6(disp_f), .D7(disp_g),
    .D8(controlled_buffer_8_out), .WR(adress_decode_logic_1_cell_4_w), .RESET(RESET),
    .EN(adress_decode_logic_1_cell_4_e), .V1(C4_v1), .V2(C4_v2), .V3(C4_v3), .V4(C4_v4), .V5(C4_v5),
    .V6(C4_v6), .V7(C4_v7), .V8(C4_v8), .CLK(CLK), .O8(controlled_buffer_8_out), .O1(disp_a), .O2(disp_b),
    .O3(disp_c), .O4(disp_d), .O5(disp_e), .O6(disp_f), .O7(disp_g));
  LED led_11 (.in(C4_v2));
  LED led_12 (.in(C4_v3));
  LED led_13 (.in(C4_v4));
  LED led_14 (.in(C4_v5));
  LED led_15 (.in(C4_v6));
  LED led_16 (.in(C4_v7));
  LED led_17 (.in(C4_v8));
  LED led_18 (.in(C8_v1));
  Byte_Memory_Module C8 (
    .D1(disp_a), .D2(disp_b), .D3(disp_c), .D4(disp_d), .D5(disp_e), .D6(disp_f), .D7(disp_g),
    .D8(controlled_buffer_8_out), .WR(adress_decode_logic_1_cell_8_w), .RESET(RESET),
    .EN(adress_decode_logic_1_cell_8_e), .V1(C8_v1), .V2(C8_v2), .V3(C8_v3), .V4(C8_v4), .V5(C8_v5),
    .V6(C8_v6), .V7(C8_v7), .V8(C8_v8), .CLK(C8_clk), .O8(controlled_buffer_8_out), .O1(disp_a), .O2(disp_b),
    .O3(disp_c), .O4(disp_d), .O5(disp_e), .O6(disp_f), .O7(disp_g));
  LED led_19 (.in(C8_v2));
  LED led_20 (.in(C8_v3));
  LED led_21 (.in(C8_v4));
  LED led_22 (.in(C8_v5));
  LED led_23 (.in(C8_v6));
  LED led_24 (.in(C8_v7));
  LED led_25 (.in(C8_v8));
  LED led_26 (.in(C8_clk));
  LED led_27 (.in(C12_v1));
  Byte_Memory_Module C12 (
    .D1(disp_a), .D2(disp_b), .D3(disp_c), .D4(disp_d), .D5(disp_e), .D6(disp_f), .D7(disp_g),
    .D8(controlled_buffer_8_out), .WR(adress_decode_logic_1_cell_12_w), .RESET(RESET),
    .EN(adress_decode_logic_1_cell_12_e), .V1(C12_v1), .V2(C12_v2), .V3(C12_v3), .V4(C12_v4), .V5(C12_v5),
    .V6(C12_v6), .V7(C12_v7), .V8(C12_v8), .CLK(C12_clk), .O8(controlled_buffer_8_out), .O1(disp_a),
    .O2(disp_b), .O3(disp_c), .O4(disp_d), .O5(disp_e), .O6(disp_f), .O7(disp_g));
  LED led_28 (.in(C12_v2));
  LED led_29 (.in(C12_v3));
  LED led_30 (.in(C12_v4));
  LED led_31 (.in(C12_v5));
  LED led_32 (.in(C12_v6));
  LED led_33 (.in(C12_v7));
  LED led_34 (.in(C12_v8));
  LED led_35 (.in(C12_clk));
  LED led_36 (.in(C1_v1));
  Byte_Memory_Module C1 (
    .D1(disp_a), .D2(disp_b), .D3(disp_c), .D4(disp_d), .D5(disp_e), .D6(disp_f), .D7(disp_g),
    .D8(controlled_buffer_8_out), .WR(adress_decode_logic_1_cell_1_w), .RESET(RESET),
    .EN(adress_decode_logic_1_cell_1_e), .V1(C1_v1), .V2(C1_v2), .V3(C1_v3), .V4(C1_v4), .V5(C1_v5),
    .V6(C1_v6), .V7(C1_v7), .V8(C1_v8), .CLK(C1_clk), .O8(controlled_buffer_8_out), .O1(disp_a), .O2(disp_b),
    .O3(disp_c), .O4(disp_d), .O5(disp_e), .O6(disp_f), .O7(disp_g));
  LED led_37 (.in(C1_v2));
  LED led_38 (.in(C1_v3));
  LED led_39 (.in(C1_v4));
  LED led_40 (.in(C1_v5));
  LED led_41 (.in(C1_v6));
  LED led_42 (.in(C1_v7));
  LED led_43 (.in(C1_v8));
  LED led_44 (.in(C1_clk));
  LED led_45 (.in(C5_v1));
  Byte_Memory_Module C5 (
    .D1(disp_a), .D2(disp_b), .D3(disp_c), .D4(disp_d), .D5(disp_e), .D6(disp_f), .D7(disp_g),
    .D8(controlled_buffer_8_out), .WR(adress_decode_logic_1_cell_5_w), .RESET(RESET),
    .EN(adress_decode_logic_1_cell_5_e), .V1(C5_v1), .V2(C5_v2), .V3(C5_v3), .V4(C5_v4), .V5(C5_v5),
    .V6(C5_v6), .V7(C5_v7), .V8(C5_v8), .CLK(C5_clk), .O8(controlled_buffer_8_out), .O1(disp_a), .O2(disp_b),
    .O3(disp_c), .O4(disp_d), .O5(disp_e), .O6(disp_f), .O7(disp_g));
  LED led_46 (.in(C5_v2));
  LED led_47 (.in(C5_v3));
  LED led_48 (.in(C5_v4));
  LED led_49 (.in(C5_v5));
  LED led_50 (.in(C5_v6));
  LED led_51 (.in(C5_v7));
  LED led_52 (.in(C5_v8));
  LED led_53 (.in(C5_clk));
  LED led_54 (.in(C9_v1));
  Byte_Memory_Module C9 (
    .D1(disp_a), .D2(disp_b), .D3(disp_c), .D4(disp_d), .D5(disp_e), .D6(disp_f), .D7(disp_g),
    .D8(controlled_buffer_8_out), .WR(adress_decode_logic_1_cell_9_w), .RESET(RESET),
    .EN(adress_decode_logic_1_cell_9_e), .V1(C9_v1), .V2(C9_v2), .V3(C9_v3), .V4(C9_v4), .V5(C9_v5),
    .V6(C9_v6), .V7(C9_v7), .V8(C9_v8), .CLK(C9_clk), .O8(controlled_buffer_8_out), .O1(disp_a), .O2(disp_b),
    .O3(disp_c), .O4(disp_d), .O5(disp_e), .O6(disp_f), .O7(disp_g));
  LED led_55 (.in(C9_v2));
  LED led_56 (.in(C9_v3));
  LED led_57 (.in(C9_v4));
  LED led_58 (.in(C9_v5));
  LED led_59 (.in(C9_v6));
  LED led_60 (.in(C9_v7));
  LED led_61 (.in(C9_v8));
  LED led_62 (.in(C9_clk));
  LED led_63 (.in(C13_v1));
  Byte_Memory_Module C13 (
    .D1(disp_a), .D2(disp_b), .D3(disp_c), .D4(disp_d), .D5(disp_e), .D6(disp_f), .D7(disp_g),
    .D8(controlled_buffer_8_out), .WR(adress_decode_logic_1_cell_13_w), .RESET(RESET),
    .EN(adress_decode_logic_1_cell_13_e), .V1(C13_v1), .V2(C13_v2), .V3(C13_v3), .V4(C13_v4), .V5(C13_v5),
    .V6(C13_v6), .V7(C13_v7), .V8(C13_v8), .CLK(C13_clk), .O8(controlled_buffer_8_out), .O1(disp_a),
    .O2(disp_b), .O3(disp_c), .O4(disp_d), .O5(disp_e), .O6(disp_f), .O7(disp_g));
  LED led_64 (.in(C13_v2));
  LED led_65 (.in(C13_v3));
  LED led_66 (.in(C13_v4));
  LED led_67 (.in(C13_v5));
  LED led_68 (.in(C13_v6));
  LED led_69 (.in(C13_v7));
  LED led_70 (.in(C13_v8));
  LED led_71 (.in(C13_clk));
  LED led_72 (.in(C2_v1));
  Byte_Memory_Module C2 (
    .D1(disp_a), .D2(disp_b), .D3(disp_c), .D4(disp_d), .D5(disp_e), .D6(disp_f), .D7(disp_g),
    .D8(controlled_buffer_8_out), .WR(adress_decode_logic_1_cell_2_w), .RESET(RESET),
    .EN(adress_decode_logic_1_cell_2_e), .V1(C2_v1), .V2(C2_v2), .V3(C2_v3), .V4(C2_v4), .V5(C2_v5),
    .V6(C2_v6), .V7(C2_v7), .V8(C2_v8), .CLK(C2_clk), .O8(controlled_buffer_8_out), .O1(disp_a), .O2(disp_b),
    .O3(disp_c), .O4(disp_d), .O5(disp_e), .O6(disp_f), .O7(disp_g));
  LED led_73 (.in(C2_v2));
  LED led_74 (.in(C2_v3));
  LED led_75 (.in(C2_v4));
  LED led_76 (.in(C2_v5));
  LED led_77 (.in(C2_v6));
  LED led_78 (.in(C2_v7));
  LED led_79 (.in(C2_v8));
  LED led_80 (.in(C2_clk));
  LED led_81 (.in(C6_v1));
  Byte_Memory_Module C6 (
    .D1(disp_a), .D2(disp_b), .D3(disp_c), .D4(disp_d), .D5(disp_e), .D6(disp_f), .D7(disp_g),
    .D8(controlled_buffer_8_out), .WR(adress_decode_logic_1_cell_6_w), .RESET(RESET),
    .EN(adress_decode_logic_1_cell_6_e), .V1(C6_v1), .V2(C6_v2), .V3(C6_v3), .V4(C6_v4), .V5(C6_v5),
    .V6(C6_v6), .V7(C6_v7), .V8(C6_v8), .CLK(C6_clk), .O8(controlled_buffer_8_out), .O1(disp_a), .O2(disp_b),
    .O3(disp_c), .O4(disp_d), .O5(disp_e), .O6(disp_f), .O7(disp_g));
  LED led_82 (.in(C6_v2));
  LED led_83 (.in(C6_v3));
  LED led_84 (.in(C6_v4));
  LED led_85 (.in(C6_v5));
  LED led_86 (.in(C6_v6));
  LED led_87 (.in(C6_v7));
  LED led_88 (.in(C6_v8));
  LED led_89 (.in(C6_clk));
  LED led_90 (.in(C10_v1));
  Byte_Memory_Module C10 (
    .D1(disp_a), .D2(disp_b), .D3(disp_c), .D4(disp_d), .D5(disp_e), .D6(disp_f), .D7(disp_g),
    .D8(controlled_buffer_8_out), .WR(adress_decode_logic_1_cell_10_w), .RESET(RESET),
    .EN(adress_decode_logic_1_cell_10_e), .V1(C10_v1), .V2(C10_v2), .V3(C10_v3), .V4(C10_v4), .V5(C10_v5),
    .V6(C10_v6), .V7(C10_v7), .V8(C10_v8), .CLK(C10_clk), .O8(controlled_buffer_8_out), .O1(disp_a),
    .O2(disp_b), .O3(disp_c), .O4(disp_d), .O5(disp_e), .O6(disp_f), .O7(disp_g));
  LED led_91 (.in(C10_v2));
  LED led_92 (.in(C10_v3));
  LED led_93 (.in(C10_v4));
  LED led_94 (.in(C10_v5));
  LED led_95 (.in(C10_v6));
  LED led_96 (.in(C10_v7));
  LED led_97 (.in(C10_v8));
  LED led_98 (.in(C10_clk));
  LED led_99 (.in(C14_v1));
  Byte_Memory_Module C14 (
    .D1(disp_a), .D2(disp_b), .D3(disp_c), .D4(disp_d), .D5(disp_e), .D6(disp_f), .D7(disp_g),
    .D8(controlled_buffer_8_out), .WR(adress_decode_logic_1_cell_14_w), .RESET(RESET),
    .EN(adress_decode_logic_1_cell_14_e), .V1(C14_v1), .V2(C14_v2), .V3(C14_v3), .V4(C14_v4), .V5(C14_v5),
    .V6(C14_v6), .V7(C14_v7), .V8(C14_v8), .CLK(C14_clk), .O8(controlled_buffer_8_out), .O1(disp_a),
    .O2(disp_b), .O3(disp_c), .O4(disp_d), .O5(disp_e), .O6(disp_f), .O7(disp_g));
  LED led_100 (.in(C14_v2));
  LED led_101 (.in(C14_v3));
  LED led_102 (.in(C14_v4));
  LED led_103 (.in(C14_v5));
  LED led_104 (.in(C14_v6));
  LED led_105 (.in(C14_v7));
  LED led_106 (.in(C14_v8));
  LED led_107 (.in(C14_clk));
  LED led_108 (.in(C3_v1));
  Byte_Memory_Module C3 (
    .D1(disp_a), .D2(disp_b), .D3(disp_c), .D4(disp_d), .D5(disp_e), .D6(disp_f), .D7(disp_g),
    .D8(controlled_buffer_8_out), .WR(adress_decode_logic_1_cell_3_w), .RESET(RESET),
    .EN(adress_decode_logic_1_cell_3_e), .V1(C3_v1), .V2(C3_v2), .V3(C3_v3), .V4(C3_v4), .V5(C3_v5),
    .V6(C3_v6), .V7(C3_v7), .V8(C3_v8), .CLK(C3_clk), .O8(controlled_buffer_8_out), .O1(disp_a), .O2(disp_b),
    .O3(disp_c), .O4(disp_d), .O5(disp_e), .O6(disp_f), .O7(disp_g));
  LED led_109 (.in(C3_v2));
  LED led_110 (.in(C3_v3));
  LED led_111 (.in(C3_v4));
  LED led_112 (.in(C3_v5));
  LED led_113 (.in(C3_v6));
  LED led_114 (.in(C3_v7));
  LED led_115 (.in(C3_v8));
  LED led_116 (.in(C3_clk));
  LED led_117 (.in(C7_v1));
  Byte_Memory_Module C7 (
    .D1(disp_a), .D2(disp_b), .D3(disp_c), .D4(disp_d), .D5(disp_e), .D6(disp_f), .D7(disp_g),
    .D8(controlled_buffer_8_out), .WR(adress_decode_logic_1_cell_7_w), .RESET(RESET),
    .EN(adress_decode_logic_1_cell_7_e), .V1(C7_v1), .V2(C7_v2), .V3(C7_v3), .V4(C7_v4), .V5(C7_v5),
    .V6(C7_v6), .V7(C7_v7), .V8(C7_v8), .CLK(C7_clk), .O8(controlled_buffer_8_out), .O1(disp_a), .O2(disp_b),
    .O3(disp_c), .O4(disp_d), .O5(disp_e), .O6(disp_f), .O7(disp_g));
  LED led_118 (.in(C7_v2));
  LED led_119 (.in(C7_v3));
  LED led_120 (.in(C7_v4));
  LED led_121 (.in(C7_v5));
  LED led_122 (.in(C7_v6));
  LED led_123 (.in(C7_v7));
  LED led_124 (.in(C7_v8));
  LED led_125 (.in(C7_clk));
  LED led_126 (.in(C11_v1));
  Byte_Memory_Module C11 (
    .D1(disp_a), .D2(disp_b), .D3(disp_c), .D4(disp_d), .D5(disp_e), .D6(disp_f), .D7(disp_g),
    .D8(controlled_buffer_8_out), .WR(adress_decode_logic_1_cell_11_w), .RESET(RESET),
    .EN(adress_decode_logic_1_cell_11_e), .V1(C11_v1), .V2(C11_v2), .V3(C11_v3), .V4(C11_v4), .V5(C11_v5),
    .V6(C11_v6), .V7(C11_v7), .V8(C11_v8), .CLK(C11_clk), .O8(controlled_buffer_8_out), .O1(disp_a),
    .O2(disp_b), .O3(disp_c), .O4(disp_d), .O5(disp_e), .O6(disp_f), .O7(disp_g));
  LED led_127 (.in(C11_v2));
  LED led_128 (.in(C11_v3));
  LED led_129 (.in(C11_v4));
  LED led_130 (.in(C11_v5));
  LED led_131 (.in(C11_v6));
  LED led_132 (.in(C11_v7));
  LED led_133 (.in(C11_v8));
  LED led_134 (.in(C11_clk));
  LED led_135 (.in(C15_v1));
  Byte_Memory_Module C15 (
    .D1(disp_a), .D2(disp_b), .D3(disp_c), .D4(disp_d), .D5(disp_e), .D6(disp_f), .D7(disp_g),
    .D8(controlled_buffer_8_out), .WR(adress_decode_logic_1_cell_15_w), .RESET(RESET),
    .EN(adress_decode_logic_1_cell_15_e), .V1(C15_v1), .V2(C15_v2), .V3(C15_v3), .V4(C15_v4), .V5(C15_v5),
    .V6(C15_v6), .V7(C15_v7), .V8(C15_v8), .CLK(C15_clk), .O8(controlled_buffer_8_out), .O1(disp_a),
    .O2(disp_b), .O3(disp_c), .O4(disp_d), .O5(disp_e), .O6(disp_f), .O7(disp_g));
  LED led_136 (.in(C15_v2));
  LED led_137 (.in(C15_v3));
  LED led_138 (.in(C15_v4));
  LED led_139 (.in(C15_v5));
  LED led_140 (.in(C15_v6));
  LED led_141 (.in(C15_v7));
  LED led_142 (.in(C15_v8));
  LED led_143 (.in(C15_clk));

  // Notes on the sheet:
  //   MANUAL PROGRAMMING PINS
endmodule

module Display (
  input  a,
  input  b,
  input  c,
  input  d,
  input  e,
  input  f,
  input  g,
  input  A0,
  input  A1,
  input  A2,
  input  A3,
  input  BUS1,
  input  BUS2,
  input  BUS3,
  input  BUS4,
  input  BUS5,
  input  BUS6,
  input  BUS7,
  input  BUS8,
  input  E0W1,
  input  CHIP_EN,
  input  RST,
  input  DATA_EN,
  output a1o,
  output b1o,
  output c1o,
  output d1o,
  output e1o,
  output f1o,
  output g1o,
  output a2o,
  output b2o,
  output c2o,
  output d2o,
  output e2o,
  output f2o,
  output g2o,
  output a3o,
  output b3o,
  output c3o,
  output d3o,
  output e3o,
  output f3o,
  output g3o
);

  wire binary2bcd_1_o1_1, binary2bcd_1_o1_2, binary2bcd_1_o2_1, binary2bcd_1_o2_2, binary2bcd_1_o2_4,
       binary2bcd_1_o2_8, binary2bcd_1_o3_1, binary2bcd_1_o3_2, binary2bcd_1_o3_4, binary2bcd_1_o3_8,
       or_1_out, or_2_out, or_3_out, or_4_out, or_5_out, or_6_out, or_7_out, or_8_out, or_9_out, or_10_out;

  Binary2BCD binary2bcd_1 (
    .I128(BUS1), .I64(BUS2), .I32(BUS3), .I16(BUS4), .I8(BUS5), .I4(BUS6), .I2(BUS7), .I1(BUS8),
    .O1_2(binary2bcd_1_o1_2), .O1_1(binary2bcd_1_o1_1), .O2_8(binary2bcd_1_o2_8), .O2_4(binary2bcd_1_o2_4),
    .O2_2(binary2bcd_1_o2_2), .O2_1(binary2bcd_1_o2_1), .O3_8(binary2bcd_1_o3_8), .O3_4(binary2bcd_1_o3_4),
    .O3_2(binary2bcd_1_o3_2), .O3_1(binary2bcd_1_o3_1));  // open: O1_8, O1_4
  or or_1 (or_1_out, A0, binary2bcd_1_o1_1);
  or or_2 (or_2_out, A1, binary2bcd_1_o1_2);
  or or_3 (or_3_out, A0, binary2bcd_1_o2_1);
  or or_4 (or_4_out, binary2bcd_1_o2_2, A1);
  or or_5 (or_5_out, A0, binary2bcd_1_o3_1);
  or or_6 (or_6_out, binary2bcd_1_o3_2, A1);
  or or_7 (or_7_out, binary2bcd_1_o2_4, A2);
  or or_8 (or_8_out, binary2bcd_1_o3_4, A2);
  or or_9 (or_9_out, A3, binary2bcd_1_o2_8);
  or or_10 (or_10_out, binary2bcd_1_o3_8, A3);
  PROM_Chip prom_chip_1 (
    .a(a), .b(b), .c(c), .d(d), .e(e), .f(f), .g(g), .DATA_ENABLE(DATA_EN), .RESET(RST), .AO(or_1_out),
    .A1(or_2_out), .A2(A2), .A3(A3), .CHIP_ENABLE(CHIP_EN), .E0W1(E0W1), .disp_a(a1o), .disp_b(b1o),
    .disp_c(c1o), .disp_d(d1o), .disp_e(e1o), .disp_f(f1o), .disp_g(g1o));  // open: CLK
  PROM_Chip prom_chip_2 (
    .a(a), .b(b), .c(c), .d(d), .e(e), .f(f), .g(g), .DATA_ENABLE(DATA_EN), .RESET(RST), .AO(or_3_out),
    .A1(or_4_out), .A2(or_7_out), .A3(or_9_out), .CHIP_ENABLE(CHIP_EN), .E0W1(E0W1), .disp_a(a2o),
    .disp_b(b2o), .disp_c(c2o), .disp_d(d2o), .disp_e(e2o), .disp_f(f2o), .disp_g(g2o));  // open: CLK
  PROM_Chip prom_chip_3 (
    .a(a), .b(b), .c(c), .d(d), .e(e), .f(f), .g(g), .DATA_ENABLE(DATA_EN), .RESET(RST), .AO(or_5_out),
    .A1(or_6_out), .A2(or_8_out), .A3(or_10_out), .CHIP_ENABLE(CHIP_EN), .E0W1(E0W1), .disp_a(a3o),
    .disp_b(b3o), .disp_c(c3o), .disp_d(d3o), .disp_e(e3o), .disp_f(f3o), .disp_g(g3o));  // open: CLK
endmodule

module Register_A (
  input  CLR,
  input  BUS1,
  input  BUS2,
  input  BUS3,
  input  BUS4,
  input  BUS5,
  input  BUS6,
  input  BUS7,
  input  BUS8,
  input  CLK,
  input  LOAD,
  input  ENABLE,
  output A1,
  output A2,
  output A4,
  output A8,
  output A16,
  output A32,
  output A64,
  output A128,
  output O1,
  output O2,
  output O3,
  output O4,
  output O5,
  output O6,
  output O7,
  output O8
);

  wire and_1_out, controlled_buffer_1_out, controlled_buffer_2_out, controlled_buffer_3_out,
       controlled_buffer_4_out, controlled_buffer_5_out, controlled_buffer_6_out, controlled_buffer_7_out,
       controlled_buffer_8_out, n74245_1_pin1, not_1_out, not_2_out;

  assign controlled_buffer_1_out = BUS1 ? BUS1 : 1'bz;  // Controlled_Buffer controlled_buffer_1
  assign controlled_buffer_2_out = BUS2 ? BUS2 : 1'bz;  // Controlled_Buffer controlled_buffer_2
  assign controlled_buffer_3_out = BUS3 ? BUS3 : 1'bz;  // Controlled_Buffer controlled_buffer_3
  assign controlled_buffer_4_out = BUS4 ? BUS4 : 1'bz;  // Controlled_Buffer controlled_buffer_4
  assign controlled_buffer_5_out = BUS5 ? BUS5 : 1'bz;  // Controlled_Buffer controlled_buffer_5
  assign controlled_buffer_6_out = BUS6 ? BUS6 : 1'bz;  // Controlled_Buffer controlled_buffer_6
  assign controlled_buffer_7_out = BUS7 ? BUS7 : 1'bz;  // Controlled_Buffer controlled_buffer_7
  assign controlled_buffer_8_out = BUS8 ? BUS8 : 1'bz;  // Controlled_Buffer controlled_buffer_8
  not not_1 (not_1_out, CLR);
  and and_1 (and_1_out, CLK, LOAD);
  _74175 u_74175_1 (
    .pin1(not_1_out), .pin2(A1), .pin4(controlled_buffer_1_out), .pin5(controlled_buffer_2_out), .pin7(A2),
    .pin15(A8), .pin13(controlled_buffer_4_out), .pin12(controlled_buffer_3_out), .pin10(A4), .pin9(and_1_out));  // open: pin3, pin6, pin14, pin11
  _74175 u_74175_2 (
    .pin1(not_1_out), .pin2(A16), .pin4(controlled_buffer_5_out), .pin5(controlled_buffer_6_out), .pin7(A32),
    .pin15(A128), .pin13(controlled_buffer_8_out), .pin12(controlled_buffer_7_out), .pin10(A64),
    .pin9(and_1_out));  // open: pin3, pin6, pin14, pin11
  not not_2 (not_2_out, ENABLE);
  _74245 u_74245_1 (
    .pin1(n74245_1_pin1), .pin2(A1), .pin3(A2), .pin4(A4), .pin5(A8), .pin6(A16), .pin7(A32), .pin8(A64),
    .pin9(A128), .pin19(not_2_out), .pin18(O1), .pin17(O2), .pin16(O3), .pin15(O4), .pin14(O5), .pin13(O6),
    .pin12(O7), .pin11(O8));
  // also tied to VCC on the sheet: n74245_1_pin1

  // Notes on the sheet:
  //   DATA
  //   Data Input Module
  //   Data Output Module
endmodule

module Register_B (
  input  CLR,
  input  BUS1,
  input  BUS2,
  input  BUS3,
  input  BUS4,
  input  BUS5,
  input  BUS6,
  input  BUS7,
  input  BUS8,
  input  CLK,
  input  LOAD,
  input  ENABLE,
  output B1,
  output B2,
  output B4,
  output B8,
  output B16,
  output B32,
  output B64,
  output B128,
  output O1,
  output O2,
  output O3,
  output O4,
  output O5,
  output O6,
  output O7,
  output O8
);

  wire and_1_out, controlled_buffer_1_out, controlled_buffer_2_out, controlled_buffer_3_out,
       controlled_buffer_4_out, controlled_buffer_5_out, controlled_buffer_6_out, controlled_buffer_7_out,
       controlled_buffer_8_out, n74245_1_pin1, not_1_out, not_2_out;

  assign controlled_buffer_1_out = BUS1 ? BUS1 : 1'bz;  // Controlled_Buffer controlled_buffer_1
  assign controlled_buffer_2_out = BUS2 ? BUS2 : 1'bz;  // Controlled_Buffer controlled_buffer_2
  assign controlled_buffer_3_out = BUS3 ? BUS3 : 1'bz;  // Controlled_Buffer controlled_buffer_3
  assign controlled_buffer_4_out = BUS4 ? BUS4 : 1'bz;  // Controlled_Buffer controlled_buffer_4
  assign controlled_buffer_5_out = BUS5 ? BUS5 : 1'bz;  // Controlled_Buffer controlled_buffer_5
  assign controlled_buffer_6_out = BUS6 ? BUS6 : 1'bz;  // Controlled_Buffer controlled_buffer_6
  assign controlled_buffer_7_out = BUS7 ? BUS7 : 1'bz;  // Controlled_Buffer controlled_buffer_7
  assign controlled_buffer_8_out = BUS8 ? BUS8 : 1'bz;  // Controlled_Buffer controlled_buffer_8
  not not_1 (not_1_out, CLR);
  and and_1 (and_1_out, CLK, LOAD);
  _74175 u_74175_1 (
    .pin1(not_1_out), .pin2(B1), .pin4(controlled_buffer_1_out), .pin5(controlled_buffer_2_out), .pin7(B2),
    .pin15(B8), .pin13(controlled_buffer_4_out), .pin12(controlled_buffer_3_out), .pin10(B4), .pin9(and_1_out));  // open: pin3, pin6, pin14, pin11
  _74175 u_74175_2 (
    .pin1(not_1_out), .pin2(B16), .pin4(controlled_buffer_5_out), .pin5(controlled_buffer_6_out), .pin7(B32),
    .pin15(B128), .pin13(controlled_buffer_8_out), .pin12(controlled_buffer_7_out), .pin10(B64),
    .pin9(and_1_out));  // open: pin3, pin6, pin14, pin11
  not not_2 (not_2_out, ENABLE);
  _74245 u_74245_1 (
    .pin1(n74245_1_pin1), .pin2(B1), .pin3(B2), .pin4(B4), .pin5(B8), .pin6(B16), .pin7(B32), .pin8(B64),
    .pin9(B128), .pin19(not_2_out), .pin18(O1), .pin17(O2), .pin16(O3), .pin15(O4), .pin14(O5), .pin13(O6),
    .pin12(O7), .pin11(O8));
  // also tied to VCC on the sheet: n74245_1_pin1

  // Notes on the sheet:
  //   DATA
  //   Data Input Module
  //   Data Output Module
endmodule

module Program_Active_Memory (
  input  in_1,
  input  in_2,
  input  in_3,
  input  in_4,
  input  in_5,
  input  in_6,
  input  in_7,
  input  in_8,
  input  in_9,
  input  in_10,
  input  in_11,
  input  in_12,
  input  in_13,
  input  in_14,
  input  in_15,
  input  in_16,
  input  INITIAL_LOAD,
  output out_18,
  output out_19,
  output out_20,
  output out_21,
  output out_22,
  output out_23,
  output out_24,
  output out_25,
  output out_26,
  output out_27,
  output out_28,
  output out_29,
  output out_30,
  output out_31,
  output out_32,
  output out_33
);

  wire clock_1_out, or_1_out;

  Clock clock_1 (.out(clock_1_out));
  or or_1 (or_1_out, clock_1_out, INITIAL_LOAD);
  D_Flip_Flop d_ff_1 (.D(in_1), .clk(or_1_out), .Q(out_18));  // open: Qn, preset, reset
  D_Flip_Flop d_ff_2 (.D(in_2), .clk(or_1_out), .Q(out_19));  // open: Qn, preset, reset
  D_Flip_Flop d_ff_3 (.D(in_3), .clk(or_1_out), .Q(out_20));  // open: Qn, preset, reset
  D_Flip_Flop d_ff_4 (.D(in_4), .clk(or_1_out), .Q(out_21));  // open: Qn, preset, reset
  D_Flip_Flop d_ff_5 (.D(in_5), .clk(or_1_out), .Q(out_22));  // open: Qn, preset, reset
  D_Flip_Flop d_ff_6 (.D(in_6), .clk(or_1_out), .Q(out_23));  // open: Qn, preset, reset
  D_Flip_Flop d_ff_7 (.D(in_7), .clk(or_1_out), .Q(out_24));  // open: Qn, preset, reset
  D_Flip_Flop d_ff_8 (.D(in_8), .clk(or_1_out), .Q(out_25));  // open: Qn, preset, reset
  D_Flip_Flop d_ff_9 (.D(in_9), .clk(or_1_out), .Q(out_26));  // open: Qn, preset, reset
  D_Flip_Flop d_ff_10 (.D(in_10), .clk(or_1_out), .Q(out_27));  // open: Qn, preset, reset
  D_Flip_Flop d_ff_11 (.D(in_11), .clk(or_1_out), .Q(out_28));  // open: Qn, preset, reset
  D_Flip_Flop d_ff_12 (.D(in_12), .clk(or_1_out), .Q(out_29));  // open: Qn, preset, reset
  D_Flip_Flop d_ff_13 (.D(in_13), .clk(or_1_out), .Q(out_30));  // open: Qn, preset, reset
  D_Flip_Flop d_ff_14 (.D(in_14), .clk(or_1_out), .Q(out_31));  // open: Qn, preset, reset
  D_Flip_Flop d_ff_15 (.D(in_15), .clk(or_1_out), .Q(out_32));  // open: Qn, preset, reset
  D_Flip_Flop d_ff_16 (.D(in_16), .clk(or_1_out), .Q(out_33));  // open: Qn, preset, reset
endmodule
module Program_Flow_Memory (
  input  COM1,
  input  COM2,
  input  COM3,
  input  COM4,
  input  COM5,
  input  COM6,
  input  COM7,
  input  COM8,
  input  COM9,
  input  COM10,
  input  COM11,
  input  COM12,
  input  COM13,
  input  COM14,
  input  COM15,
  input  COM16,
  input  I1_1,
  input  I2_1,
  input  I3_1,
  input  I4_1,
  input  I1_2,
  input  I2_2,
  input  I3_2,
  input  I4_2,
  input  I1_3,
  input  I2_3,
  input  I3_3,
  input  I4_3,
  input  I1_4,
  input  I2_4,
  input  I3_4,
  input  I4_4,
  input  I1_5,
  input  I2_5,
  input  I3_5,
  input  I4_5,
  input  I1_6,
  input  I2_6,
  input  I3_6,
  input  I4_6,
  input  I1_7,
  input  I2_7,
  input  I3_7,
  input  I4_7,
  input  I1_8,
  input  I2_8,
  input  I3_8,
  input  I4_8,
  input  I1_9,
  input  I2_9,
  input  I3_9,
  input  I4_9,
  input  I1_10,
  input  I2_10,
  input  I3_10,
  input  I4_10,
  input  I1_11,
  input  I2_11,
  input  I3_11,
  input  I4_11,
  input  I1_12,
  input  I2_12,
  input  I3_12,
  input  I4_12,
  input  I1_13,
  input  I2_13,
  input  I3_13,
  input  I4_13,
  input  I1_14,
  input  I2_14,
  input  I3_14,
  input  I4_14,
  input  I1_15,
  input  I2_15,
  input  I3_15,
  input  I4_15,
  input  I1_16,
  input  I2_16,
  input  I3_16,
  input  I4_16,
  input  LOAD_I1,
  input  LOAD_I2,
  input  LOAD_I3,
  input  LOAD_I4,
  output O1,
  output O2,
  output O3,
  output O4,
  output O5,
  output O6,
  output O7,
  output O8,
  output O9,
  output O10,
  output O11,
  output O12,
  output O13,
  output O14,
  output O15,
  output O16
);

  wire clock_1_out, or_1_out, or_2_out, or_3_out, or_4_out, or_5_out, or_6_out, or_7_out, or_8_out, or_9_out,
       or_10_out, or_11_out, or_12_out, or_13_out, or_14_out, or_15_out, or_16_out, or_17_out, or_18_out,
       or_19_out, or_20_out, or_21_out, or_22_out, or_23_out, or_24_out, or_25_out, or_26_out, or_27_out,
       or_28_out, or_29_out, or_30_out, or_31_out, or_32_out, or_33_out, or_34_out, or_35_out, or_36_out,
       or_37_out, or_38_out, or_39_out, or_40_out, or_41_out, or_42_out, or_43_out, or_44_out, or_45_out,
       or_46_out, or_47_out, or_48_out, or_49_out, or_50_out, or_51_out, or_52_out, or_53_out, or_54_out,
       or_55_out, or_56_out, or_57_out, or_58_out, or_59_out, or_60_out, or_61_out, or_62_out, or_63_out,
       or_64_out, program_active_memory_1_out_18, program_active_memory_1_out_19,
       program_active_memory_1_out_20, program_active_memory_1_out_21, program_active_memory_1_out_22,
       program_active_memory_1_out_23, program_active_memory_1_out_24, program_active_memory_1_out_25,
       program_active_memory_1_out_26, program_active_memory_1_out_27, program_active_memory_1_out_28,
       program_active_memory_1_out_29, program_active_memory_1_out_30, program_active_memory_1_out_31,
       program_active_memory_1_out_32, program_active_memory_1_out_33, program_active_memory_2_out_18,
       program_active_memory_2_out_19, program_active_memory_2_out_20, program_active_memory_2_out_21,
       program_active_memory_2_out_22, program_active_memory_2_out_23, program_active_memory_2_out_24,
       program_active_memory_2_out_25, program_active_memory_2_out_26, program_active_memory_2_out_27,
       program_active_memory_2_out_28, program_active_memory_2_out_29, program_active_memory_2_out_30,
       program_active_memory_2_out_31, program_active_memory_2_out_32, program_active_memory_2_out_33,
       program_active_memory_3_out_18, program_active_memory_3_out_19, program_active_memory_3_out_20,
       program_active_memory_3_out_21, program_active_memory_3_out_22, program_active_memory_3_out_23,
       program_active_memory_3_out_24, program_active_memory_3_out_25, program_active_memory_3_out_26,
       program_active_memory_3_out_27, program_active_memory_3_out_28, program_active_memory_3_out_29,
       program_active_memory_3_out_30, program_active_memory_3_out_31, program_active_memory_3_out_32,
       program_active_memory_3_out_33, program_active_memory_4_out_18, program_active_memory_4_out_19,
       program_active_memory_4_out_20, program_active_memory_4_out_21, program_active_memory_4_out_22,
       program_active_memory_4_out_23, program_active_memory_4_out_24, program_active_memory_4_out_25,
       program_active_memory_4_out_26, program_active_memory_4_out_27, program_active_memory_4_out_28,
       program_active_memory_4_out_29, program_active_memory_4_out_30, program_active_memory_4_out_31,
       program_active_memory_4_out_32, program_active_memory_4_out_33;

  Clock clock_1 (.out(clock_1_out));
  Program_Active_Memory program_active_memory_1 (
    .in_1(COM1), .in_2(COM2), .in_3(COM3), .in_4(COM4), .in_5(COM5), .in_6(COM6), .in_7(COM7), .in_8(COM8),
    .in_9(COM9), .in_10(COM10), .in_11(COM11), .in_12(COM12), .in_13(COM13), .in_14(COM14), .in_15(COM15),
    .in_16(COM16), .INITIAL_LOAD(clock_1_out), .out_18(program_active_memory_1_out_18),
    .out_19(program_active_memory_1_out_19), .out_20(program_active_memory_1_out_20),
    .out_21(program_active_memory_1_out_21), .out_22(program_active_memory_1_out_22),
    .out_23(program_active_memory_1_out_23), .out_24(program_active_memory_1_out_24),
    .out_25(program_active_memory_1_out_25), .out_26(program_active_memory_1_out_26),
    .out_27(program_active_memory_1_out_27), .out_28(program_active_memory_1_out_28),
    .out_29(program_active_memory_1_out_29), .out_30(program_active_memory_1_out_30),
    .out_31(program_active_memory_1_out_31), .out_32(program_active_memory_1_out_32),
    .out_33(program_active_memory_1_out_33));
  or or_1 (or_1_out, program_active_memory_1_out_18, I4_1);
  or or_2 (or_2_out, program_active_memory_1_out_19, I4_2);
  or or_3 (or_3_out, program_active_memory_1_out_20, I4_3);
  or or_4 (or_4_out, program_active_memory_1_out_21, I4_4);
  or or_5 (or_5_out, program_active_memory_1_out_22, I4_5);
  or or_6 (or_6_out, program_active_memory_1_out_23, I4_6);
  or or_7 (or_7_out, program_active_memory_1_out_24, I4_7);
  or or_8 (or_8_out, program_active_memory_1_out_25, I4_8);
  or or_9 (or_9_out, program_active_memory_1_out_26, I4_9);
  or or_10 (or_10_out, program_active_memory_1_out_27, I4_10);
  or or_11 (or_11_out, program_active_memory_1_out_28, I4_11);
  or or_12 (or_12_out, program_active_memory_1_out_29, I4_12);
  or or_13 (or_13_out, program_active_memory_1_out_30, I4_13);
  or or_14 (or_14_out, program_active_memory_1_out_31, I4_14);
  or or_15 (or_15_out, program_active_memory_1_out_32, I4_15);
  or or_16 (or_16_out, program_active_memory_1_out_33, I4_16);
  Program_Active_Memory program_active_memory_2 (
    .in_1(or_1_out), .in_2(or_2_out), .in_3(or_3_out), .in_4(or_4_out), .in_5(or_5_out), .in_6(or_6_out),
    .in_7(or_7_out), .in_8(or_8_out), .in_9(or_9_out), .in_10(or_10_out), .in_11(or_11_out),
    .in_12(or_12_out), .in_13(or_13_out), .in_14(or_14_out), .in_15(or_15_out), .in_16(or_16_out),
    .INITIAL_LOAD(LOAD_I4), .out_18(program_active_memory_2_out_18), .out_19(program_active_memory_2_out_19),
    .out_20(program_active_memory_2_out_20), .out_21(program_active_memory_2_out_21),
    .out_22(program_active_memory_2_out_22), .out_23(program_active_memory_2_out_23),
    .out_24(program_active_memory_2_out_24), .out_25(program_active_memory_2_out_25),
    .out_26(program_active_memory_2_out_26), .out_27(program_active_memory_2_out_27),
    .out_28(program_active_memory_2_out_28), .out_29(program_active_memory_2_out_29),
    .out_30(program_active_memory_2_out_30), .out_31(program_active_memory_2_out_31),
    .out_32(program_active_memory_2_out_32), .out_33(program_active_memory_2_out_33));
  or or_17 (or_17_out, program_active_memory_2_out_18, I3_1);
  or or_18 (or_18_out, program_active_memory_2_out_19, I3_2);
  or or_19 (or_19_out, program_active_memory_2_out_20, I3_3);
  or or_20 (or_20_out, program_active_memory_2_out_21, I3_4);
  or or_21 (or_21_out, program_active_memory_2_out_22, I3_5);
  or or_22 (or_22_out, program_active_memory_2_out_23, I3_6);
  or or_23 (or_23_out, program_active_memory_2_out_24, I3_7);
  or or_24 (or_24_out, program_active_memory_2_out_25, I3_8);
  or or_25 (or_25_out, program_active_memory_2_out_26, I3_9);
  or or_26 (or_26_out, program_active_memory_2_out_27, I3_10);
  or or_27 (or_27_out, program_active_memory_2_out_28, I3_11);
  or or_28 (or_28_out, program_active_memory_2_out_29, I3_12);
  or or_29 (or_29_out, program_active_memory_2_out_30, I3_13);
  or or_30 (or_30_out, program_active_memory_2_out_31, I3_14);
  or or_31 (or_31_out, program_active_memory_2_out_32, I3_15);
  or or_32 (or_32_out, program_active_memory_2_out_33, I3_16);
  Program_Active_Memory program_active_memory_3 (
    .in_1(or_17_out), .in_2(or_18_out), .in_3(or_19_out), .in_4(or_20_out), .in_5(or_21_out),
    .in_6(or_22_out), .in_7(or_23_out), .in_8(or_24_out), .in_9(or_25_out), .in_10(or_26_out),
    .in_11(or_27_out), .in_12(or_28_out), .in_13(or_29_out), .in_14(or_30_out), .in_15(or_31_out),
    .in_16(or_32_out), .INITIAL_LOAD(LOAD_I3), .out_18(program_active_memory_3_out_18),
    .out_19(program_active_memory_3_out_19), .out_20(program_active_memory_3_out_20),
    .out_21(program_active_memory_3_out_21), .out_22(program_active_memory_3_out_22),
    .out_23(program_active_memory_3_out_23), .out_24(program_active_memory_3_out_24),
    .out_25(program_active_memory_3_out_25), .out_26(program_active_memory_3_out_26),
    .out_27(program_active_memory_3_out_27), .out_28(program_active_memory_3_out_28),
    .out_29(program_active_memory_3_out_29), .out_30(program_active_memory_3_out_30),
    .out_31(program_active_memory_3_out_31), .out_32(program_active_memory_3_out_32),
    .out_33(program_active_memory_3_out_33));
  or or_33 (or_33_out, program_active_memory_3_out_18, I2_1);
  or or_34 (or_34_out, program_active_memory_3_out_19, I2_2);
  or or_35 (or_35_out, program_active_memory_3_out_20, I2_3);
  or or_36 (or_36_out, program_active_memory_3_out_21, I2_4);
  or or_37 (or_37_out, program_active_memory_3_out_22, I2_5);
  or or_38 (or_38_out, program_active_memory_3_out_23, I2_6);
  or or_39 (or_39_out, program_active_memory_3_out_24, I2_7);
  or or_40 (or_40_out, program_active_memory_3_out_25, I2_8);
  or or_41 (or_41_out, program_active_memory_3_out_26, I2_9);
  or or_42 (or_42_out, program_active_memory_3_out_27, I2_10);
  or or_43 (or_43_out, program_active_memory_3_out_28, I2_11);
  or or_44 (or_44_out, program_active_memory_3_out_29, I2_12);
  or or_45 (or_45_out, program_active_memory_3_out_30, I2_13);
  or or_46 (or_46_out, program_active_memory_3_out_31, I2_14);
  or or_47 (or_47_out, program_active_memory_3_out_32, I2_15);
  or or_48 (or_48_out, program_active_memory_3_out_33, I2_16);
  Program_Active_Memory program_active_memory_4 (
    .in_1(or_33_out), .in_2(or_34_out), .in_3(or_35_out), .in_4(or_36_out), .in_5(or_37_out),
    .in_6(or_38_out), .in_7(or_39_out), .in_8(or_40_out), .in_9(or_41_out), .in_10(or_42_out),
    .in_11(or_43_out), .in_12(or_44_out), .in_13(or_45_out), .in_14(or_46_out), .in_15(or_47_out),
    .in_16(or_48_out), .INITIAL_LOAD(LOAD_I2), .out_18(program_active_memory_4_out_18),
    .out_19(program_active_memory_4_out_19), .out_20(program_active_memory_4_out_20),
    .out_21(program_active_memory_4_out_21), .out_22(program_active_memory_4_out_22),
    .out_23(program_active_memory_4_out_23), .out_24(program_active_memory_4_out_24),
    .out_25(program_active_memory_4_out_25), .out_26(program_active_memory_4_out_26),
    .out_27(program_active_memory_4_out_27), .out_28(program_active_memory_4_out_28),
    .out_29(program_active_memory_4_out_29), .out_30(program_active_memory_4_out_30),
    .out_31(program_active_memory_4_out_31), .out_32(program_active_memory_4_out_32),
    .out_33(program_active_memory_4_out_33));
  or or_49 (or_49_out, program_active_memory_4_out_18, I1_1);
  or or_50 (or_50_out, program_active_memory_4_out_19, I1_2);
  or or_51 (or_51_out, program_active_memory_4_out_20, I1_3);
  or or_52 (or_52_out, program_active_memory_4_out_21, I1_4);
  or or_53 (or_53_out, program_active_memory_4_out_22, I1_5);
  or or_54 (or_54_out, program_active_memory_4_out_23, I1_6);
  or or_55 (or_55_out, program_active_memory_4_out_24, I1_7);
  or or_56 (or_56_out, program_active_memory_4_out_25, I1_8);
  or or_57 (or_57_out, program_active_memory_4_out_26, I1_9);
  or or_58 (or_58_out, program_active_memory_4_out_27, I1_10);
  or or_59 (or_59_out, program_active_memory_4_out_28, I1_11);
  or or_60 (or_60_out, program_active_memory_4_out_29, I1_12);
  or or_61 (or_61_out, program_active_memory_4_out_30, I1_13);
  or or_62 (or_62_out, program_active_memory_4_out_31, I1_14);
  or or_63 (or_63_out, program_active_memory_4_out_32, I1_15);
  or or_64 (or_64_out, program_active_memory_4_out_33, I1_16);
  Program_Active_Memory program_active_memory_5 (
    .in_1(or_49_out), .in_2(or_50_out), .in_3(or_51_out), .in_4(or_52_out), .in_5(or_53_out),
    .in_6(or_54_out), .in_7(or_55_out), .in_8(or_56_out), .in_9(or_57_out), .in_10(or_58_out),
    .in_11(or_59_out), .in_12(or_60_out), .in_13(or_61_out), .in_14(or_62_out), .in_15(or_63_out),
    .in_16(or_64_out), .INITIAL_LOAD(LOAD_I1), .out_18(O1), .out_19(O2), .out_20(O3), .out_21(O4),
    .out_22(O5), .out_23(O6), .out_24(O7), .out_25(O8), .out_26(O9), .out_27(O10), .out_28(O11),
    .out_29(O12), .out_30(O13), .out_31(O14), .out_32(O15), .out_33(O16));
endmodule

module Data_Active_Memory (
  input  in_1,
  input  in_2,
  input  in_3,
  input  in_4,
  input  in_5,
  input  in_6,
  input  in_7,
  input  in_8,
  input  INITIAL_LOAD,
  output out_10,
  output out_11,
  output out_12,
  output out_13,
  output out_14,
  output out_15,
  output out_16,
  output out_17
);

  wire clock_1_out, or_1_out;

  Clock clock_1 (.out(clock_1_out));
  or or_1 (or_1_out, clock_1_out, INITIAL_LOAD);
  D_Flip_Flop d_ff_1 (.D(in_1), .clk(or_1_out), .Q(out_10));  // open: Qn, preset, reset
  D_Flip_Flop d_ff_2 (.D(in_2), .clk(or_1_out), .Q(out_11));  // open: Qn, preset, reset
  D_Flip_Flop d_ff_3 (.D(in_3), .clk(or_1_out), .Q(out_12));  // open: Qn, preset, reset
  D_Flip_Flop d_ff_4 (.D(in_4), .clk(or_1_out), .Q(out_13));  // open: Qn, preset, reset
  D_Flip_Flop d_ff_5 (.D(in_5), .clk(or_1_out), .Q(out_14));  // open: Qn, preset, reset
  D_Flip_Flop d_ff_6 (.D(in_6), .clk(or_1_out), .Q(out_15));  // open: Qn, preset, reset
  D_Flip_Flop d_ff_7 (.D(in_7), .clk(or_1_out), .Q(out_16));  // open: Qn, preset, reset
  D_Flip_Flop d_ff_8 (.D(in_8), .clk(or_1_out), .Q(out_17));  // open: Qn, preset, reset
endmodule

module Data_Flow_Memory (
  input  COM1,
  input  COM2,
  input  COM3,
  input  COM4,
  input  COM5,
  input  COM6,
  input  COM7,
  input  COM8,
  input  I1_1,
  input  I2_1,
  input  I3_1,
  input  I4_1,
  input  I1_2,
  input  I2_2,
  input  I3_2,
  input  I4_2,
  input  I1_3,
  input  I2_3,
  input  I3_3,
  input  I4_3,
  input  I1_4,
  input  I2_4,
  input  I3_4,
  input  I4_4,
  input  I1_5,
  input  I2_5,
  input  I3_5,
  input  I4_5,
  input  I1_6,
  input  I2_6,
  input  I3_6,
  input  I4_6,
  input  I1_7,
  input  I2_7,
  input  I3_7,
  input  I4_7,
  input  I1_8,
  input  I2_8,
  input  I3_8,
  input  I4_8,
  input  LOAD,
  output O1,
  output O2,
  output O3,
  output O4,
  output O5,
  output O6,
  output O7,
  output O8
);

  wire clock_1_out, data_active_memory_1_out_10, data_active_memory_1_out_11, data_active_memory_1_out_12,
       data_active_memory_1_out_13, data_active_memory_1_out_14, data_active_memory_1_out_15,
       data_active_memory_1_out_16, data_active_memory_1_out_17, data_active_memory_2_out_10,
       data_active_memory_2_out_11, data_active_memory_2_out_12, data_active_memory_2_out_13,
       data_active_memory_2_out_14, data_active_memory_2_out_15, data_active_memory_2_out_16,
       data_active_memory_2_out_17, data_active_memory_3_out_10, data_active_memory_3_out_11,
       data_active_memory_3_out_12, data_active_memory_3_out_13, data_active_memory_3_out_14,
       data_active_memory_3_out_15, data_active_memory_3_out_16, data_active_memory_3_out_17,
       data_active_memory_4_out_10, data_active_memory_4_out_11, data_active_memory_4_out_12,
       data_active_memory_4_out_13, data_active_memory_4_out_14, data_active_memory_4_out_15,
       data_active_memory_4_out_16, data_active_memory_4_out_17, or_1_out, or_2_out, or_3_out, or_4_out,
       or_5_out, or_6_out, or_7_out, or_8_out, or_9_out, or_10_out, or_11_out, or_12_out, or_13_out,
       or_14_out, or_15_out, or_16_out, or_17_out, or_18_out, or_19_out, or_20_out, or_21_out, or_22_out,
       or_23_out, or_24_out, or_25_out, or_26_out, or_27_out, or_28_out, or_29_out, or_30_out, or_31_out,
       or_32_out;

  Clock clock_1 (.out(clock_1_out));
  Data_Active_Memory data_active_memory_1 (
    .in_1(COM1), .in_2(COM2), .in_3(COM3), .in_4(COM4), .in_5(COM5), .in_6(COM6), .in_7(COM7), .in_8(COM8),
    .INITIAL_LOAD(clock_1_out), .out_10(data_active_memory_1_out_10), .out_11(data_active_memory_1_out_11),
    .out_12(data_active_memory_1_out_12), .out_13(data_active_memory_1_out_13),
    .out_14(data_active_memory_1_out_14), .out_15(data_active_memory_1_out_15),
    .out_16(data_active_memory_1_out_16), .out_17(data_active_memory_1_out_17));
  or or_1 (or_1_out, data_active_memory_1_out_10, I4_1);
  or or_2 (or_2_out, data_active_memory_1_out_11, I4_2);
  or or_3 (or_3_out, data_active_memory_1_out_12, I4_3);
  or or_4 (or_4_out, data_active_memory_1_out_13, I4_4);
  or or_5 (or_5_out, data_active_memory_1_out_14, I4_5);
  or or_6 (or_6_out, data_active_memory_1_out_15, I4_6);
  or or_7 (or_7_out, data_active_memory_1_out_16, I4_7);
  or or_8 (or_8_out, data_active_memory_1_out_17, I4_8);
  Data_Active_Memory data_active_memory_2 (
    .in_1(or_1_out), .in_2(or_2_out), .in_3(or_3_out), .in_4(or_4_out), .in_5(or_5_out), .in_6(or_6_out),
    .in_7(or_7_out), .in_8(or_8_out), .INITIAL_LOAD(LOAD), .out_10(data_active_memory_2_out_10),
    .out_11(data_active_memory_2_out_11), .out_12(data_active_memory_2_out_12),
    .out_13(data_active_memory_2_out_13), .out_14(data_active_memory_2_out_14),
    .out_15(data_active_memory_2_out_15), .out_16(data_active_memory_2_out_16),
    .out_17(data_active_memory_2_out_17));
  or or_9 (or_9_out, data_active_memory_2_out_10, I3_1);
  or or_10 (or_10_out, data_active_memory_2_out_11, I3_2);
  or or_11 (or_11_out, data_active_memory_2_out_12, I3_3);
  or or_12 (or_12_out, data_active_memory_2_out_13, I3_4);
  or or_13 (or_13_out, data_active_memory_2_out_14, I3_5);
  or or_14 (or_14_out, data_active_memory_2_out_15, I3_6);
  or or_15 (or_15_out, data_active_memory_2_out_16, I3_7);
  or or_16 (or_16_out, data_active_memory_2_out_17, I3_8);
  Data_Active_Memory data_active_memory_3 (
    .in_1(or_9_out), .in_2(or_10_out), .in_3(or_11_out), .in_4(or_12_out), .in_5(or_13_out),
    .in_6(or_14_out), .in_7(or_15_out), .in_8(or_16_out), .INITIAL_LOAD(LOAD),
    .out_10(data_active_memory_3_out_10), .out_11(data_active_memory_3_out_11),
    .out_12(data_active_memory_3_out_12), .out_13(data_active_memory_3_out_13),
    .out_14(data_active_memory_3_out_14), .out_15(data_active_memory_3_out_15),
    .out_16(data_active_memory_3_out_16), .out_17(data_active_memory_3_out_17));
  or or_17 (or_17_out, data_active_memory_3_out_10, I2_1);
  or or_18 (or_18_out, data_active_memory_3_out_11, I2_2);
  or or_19 (or_19_out, data_active_memory_3_out_12, I2_3);
  or or_20 (or_20_out, data_active_memory_3_out_13, I2_4);
  or or_21 (or_21_out, data_active_memory_3_out_14, I2_5);
  or or_22 (or_22_out, data_active_memory_3_out_15, I2_6);
  or or_23 (or_23_out, data_active_memory_3_out_16, I2_7);
  or or_24 (or_24_out, data_active_memory_3_out_17, I2_8);
  Data_Active_Memory data_active_memory_4 (
    .in_1(or_17_out), .in_2(or_18_out), .in_3(or_19_out), .in_4(or_20_out), .in_5(or_21_out),
    .in_6(or_22_out), .in_7(or_23_out), .in_8(or_24_out), .INITIAL_LOAD(LOAD),
    .out_10(data_active_memory_4_out_10), .out_11(data_active_memory_4_out_11),
    .out_12(data_active_memory_4_out_12), .out_13(data_active_memory_4_out_13),
    .out_14(data_active_memory_4_out_14), .out_15(data_active_memory_4_out_15),
    .out_16(data_active_memory_4_out_16), .out_17(data_active_memory_4_out_17));
  or or_25 (or_25_out, data_active_memory_4_out_10, I1_1);
  or or_26 (or_26_out, data_active_memory_4_out_11, I1_2);
  or or_27 (or_27_out, data_active_memory_4_out_12, I1_3);
  or or_28 (or_28_out, data_active_memory_4_out_13, I1_4);
  or or_29 (or_29_out, data_active_memory_4_out_14, I1_5);
  or or_30 (or_30_out, data_active_memory_4_out_15, I1_6);
  or or_31 (or_31_out, data_active_memory_4_out_16, I1_7);
  or or_32 (or_32_out, data_active_memory_4_out_17, I1_8);
  Data_Active_Memory data_active_memory_5 (
    .in_1(or_25_out), .in_2(or_26_out), .in_3(or_27_out), .in_4(or_28_out), .in_5(or_29_out),
    .in_6(or_30_out), .in_7(or_31_out), .in_8(or_32_out), .INITIAL_LOAD(LOAD), .out_10(O1), .out_11(O2),
    .out_12(O3), .out_13(O4), .out_14(O5), .out_15(O6), .out_16(O7), .out_17(O8));
endmodule
