// Logisim project DataBus.circ as structural Verilog: 1 circuit, main circuit main
module main (
  input  CLR,
  input  CLR_2,
  input  in_3,
  input  in_4,
  input  in_5,
  input  in_6,
  input  in_7,
  input  in_8,
  input  in_9,
  input  in_10,
  input  SOURCE_SINK,
  input  LOAD,
  input  LOAD_2,
  input  ENABLE,
  input  ENABLE_2,
  input  CLR_3,
  input  CLR_4,
  input  LOAD_3,
  input  LOAD_4,
  input  ENABLE_3,
  input  ENABLE_4
);

  wire and_1_out, and_2_out, and_3_out, and_4_out, clock_1_out, clock_2_out, clock_3_out, clock_4_out,
       controlled_buffer_1_out, controlled_buffer_2_out, controlled_buffer_3_out, controlled_buffer_4_out,
       controlled_buffer_5_out, controlled_buffer_6_out, controlled_buffer_7_out, controlled_buffer_8_out,
       n74175_1_pin2, n74175_1_pin7, n74175_1_pin10, n74175_1_pin15, n74175_2_pin2, n74175_2_pin7,
       n74175_2_pin11, n74175_2_pin15, n74175_3_pin2, n74175_3_pin7, n74175_3_pin10, n74175_3_pin15,
       n74175_4_pin2, n74175_4_pin7, n74175_4_pin11, n74175_4_pin15, n74175_5_pin2, n74175_5_pin7,
       n74175_5_pin10, n74175_5_pin15, n74175_6_pin2, n74175_6_pin7, n74175_6_pin11, n74175_6_pin15,
       n74175_7_pin2, n74175_7_pin7, n74175_7_pin10, n74175_7_pin15, n74175_8_pin2, n74175_8_pin7,
       n74175_8_pin11, n74175_8_pin15, n74245_1_pin1, n74245_2_pin1, n74245_3_pin1, n74245_4_pin1, not_1_out,
       not_2_out, not_3_out, not_4_out, not_5_out, not_6_out, not_7_out, not_8_out, not_9_out, not_10_out,
       not_11_out, not_12_out;

  not not_1 (not_1_out, CLR);
  assign controlled_buffer_1_out = SOURCE_SINK ? in_3 : 1'bz;  // Controlled_Buffer controlled_buffer_1
  assign controlled_buffer_2_out = SOURCE_SINK ? in_4 : 1'bz;  // Controlled_Buffer controlled_buffer_2
  assign controlled_buffer_3_out = SOURCE_SINK ? in_5 : 1'bz;  // Controlled_Buffer controlled_buffer_3
  assign controlled_buffer_4_out = SOURCE_SINK ? in_6 : 1'bz;  // Controlled_Buffer controlled_buffer_4
  assign controlled_buffer_5_out = SOURCE_SINK ? in_7 : 1'bz;  // Controlled_Buffer controlled_buffer_5
  assign controlled_buffer_6_out = SOURCE_SINK ? in_8 : 1'bz;  // Controlled_Buffer controlled_buffer_6
  assign controlled_buffer_7_out = SOURCE_SINK ? in_9 : 1'bz;  // Controlled_Buffer controlled_buffer_7
  assign controlled_buffer_8_out = SOURCE_SINK ? in_10 : 1'bz;  // Controlled_Buffer controlled_buffer_8
  Clock clock_1 (.out(clock_1_out));
  not not_2 (not_2_out, CLR_3);
  Clock clock_2 (.out(clock_2_out));
  and and_1 (and_1_out, clock_1_out, LOAD);
  and and_2 (and_2_out, clock_2_out, LOAD_3);
  LED led_1 (.in(n74175_1_pin2));
  LED led_2 (.in(n74175_3_pin2));
  LED led_3 (.in(n74175_1_pin7));
  LED led_4 (.in(n74175_1_pin10));
  LED led_5 (.in(n74175_1_pin15));
  _74175 u_74175_1 (
    .pin1(not_1_out), .pin2(n74175_1_pin2), .pin4(controlled_buffer_1_out), .pin5(controlled_buffer_2_out),
    .pin7(n74175_1_pin7), .pin15(n74175_1_pin15), .pin13(controlled_buffer_4_out),
    .pin12(controlled_buffer_3_out), .pin10(n74175_1_pin10), .pin9(and_1_out));  // open: pin3, pin6, pin14, pin11
  _74175 u_74175_2 (
    .pin1(not_1_out), .pin2(n74175_2_pin2), .pin4(controlled_buffer_5_out), .pin5(controlled_buffer_6_out),
    .pin7(n74175_2_pin7), .pin15(n74175_2_pin15), .pin13(controlled_buffer_8_out),
    .pin12(controlled_buffer_7_out), .pin11(n74175_2_pin11), .pin9(and_1_out));  // open: pin3, pin6, pin14, pin10
  LED led_6 (.in(n74175_3_pin7));
  LED led_7 (.in(n74175_3_pin10));
  LED led_8 (.in(n74175_3_pin15));
  _74175 u_74175_3 (
    .pin1(not_2_out), .pin2(n74175_3_pin2), .pin4(controlled_buffer_1_out), .pin5(controlled_buffer_2_out),
    .pin7(n74175_3_pin7), .pin15(n74175_3_pin15), .pin13(controlled_buffer_4_out),
    .pin12(controlled_buffer_3_out), .pin10(n74175_3_pin10), .pin9(and_2_out));  // open: pin3, pin6, pin14, pin11
  _74175 u_74175_4 (
    .pin1(not_2_out), .pin2(n74175_4_pin2), .pin4(controlled_buffer_5_out), .pin5(controlled_buffer_6_out),
    .pin7(n74175_4_pin7), .pin15(n74175_4_pin15), .pin13(controlled_buffer_8_out),
    .pin12(controlled_buffer_7_out), .pin11(n74175_4_pin11), .pin9(and_2_out));  // open: pin3, pin6, pin14, pin10
  LED led_9 (.in(n74175_2_pin2));
  LED led_10 (.in(n74175_2_pin7));
  LED led_11 (.in(n74175_4_pin2));
  LED led_12 (.in(n74175_4_pin7));
  LED led_13 (.in(not_3_out));
  LED led_14 (.in(n74175_2_pin15));
  not not_3 (not_3_out, n74175_2_pin11);
  LED led_15 (.in(not_4_out));
  LED led_16 (.in(n74175_4_pin15));
  not not_4 (not_4_out, n74175_4_pin11);
  not not_5 (not_5_out, ENABLE);
  not not_6 (not_6_out, ENABLE_3);
  _74245 u_74245_1 (
    .pin1(n74245_1_pin1), .pin2(n74175_1_pin2), .pin3(n74175_1_pin7), .pin4(n74175_1_pin10),
    .pin5(n74175_1_pin15), .pin6(n74175_2_pin2), .pin7(n74175_2_pin7), .pin8(not_3_out),
    .pin9(n74175_2_pin15), .pin19(not_5_out), .pin18(controlled_buffer_1_out),
    .pin17(controlled_buffer_2_out), .pin16(controlled_buffer_3_out), .pin15(controlled_buffer_4_out),
    .pin14(controlled_buffer_5_out), .pin13(controlled_buffer_6_out), .pin12(controlled_buffer_7_out),
    .pin11(controlled_buffer_8_out));
  _74245 u_74245_2 (
    .pin1(n74245_2_pin1), .pin2(n74175_3_pin2), .pin3(n74175_3_pin7), .pin4(n74175_3_pin10),
    .pin5(n74175_3_pin15), .pin6(n74175_4_pin2), .pin7(n74175_4_pin7), .pin8(not_4_out),
    .pin9(n74175_4_pin15), .pin19(not_6_out), .pin18(controlled_buffer_1_out),
    .pin17(controlled_buffer_2_out), .pin16(controlled_buffer_3_out), .pin15(controlled_buffer_4_out),
    .pin14(controlled_buffer_5_out), .pin13(controlled_buffer_6_out), .pin12(controlled_buffer_7_out),
    .pin11(controlled_buffer_8_out));
  not not_7 (not_7_out, CLR_2);
  Clock clock_3 (.out(clock_3_out));
  not not_8 (not_8_out, CLR_4);
  Clock clock_4 (.out(clock_4_out));
  and and_3 (and_3_out, clock_3_out, LOAD_2);
  and and_4 (and_4_out, clock_4_out, LOAD_4);
  LED led_17 (.in(n74175_5_pin2));
  LED led_18 (.in(n74175_7_pin2));
  LED led_19 (.in(n74175_5_pin7));
  LED led_20 (.in(n74175_5_pin10));
  LED led_21 (.in(n74175_5_pin15));
  _74175 u_74175_5 (
    .pin1(not_7_out), .pin2(n74175_5_pin2), .pin4(controlled_buffer_1_out), .pin5(controlled_buffer_2_out),
    .pin7(n74175_5_pin7), .pin15(n74175_5_pin15), .pin13(controlled_buffer_4_out),
    .pin12(controlled_buffer_3_out), .pin10(n74175_5_pin10), .pin9(and_3_out));  // open: pin3, pin6, pin14, pin11
  _74175 u_74175_6 (
    .pin1(not_7_out), .pin2(n74175_6_pin2), .pin4(controlled_buffer_5_out), .pin5(controlled_buffer_6_out),
    .pin7(n74175_6_pin7), .pin15(n74175_6_pin15), .pin13(controlled_buffer_8_out),
    .pin12(controlled_buffer_7_out), .pin11(n74175_6_pin11), .pin9(and_3_out));  // open: pin3, pin6, pin14, pin10
  LED led_22 (.in(n74175_7_pin7));
  LED led_23 (.in(n74175_7_pin10));
  LED led_24 (.in(n74175_7_pin15));
  _74175 u_74175_7 (
    .pin1(not_8_out), .pin2(n74175_7_pin2), .pin4(controlled_buffer_1_out), .pin5(controlled_buffer_2_out),
    .pin7(n74175_7_pin7), .pin15(n74175_7_pin15), .pin13(controlled_buffer_4_out),
    .pin12(controlled_buffer_3_out), .pin10(n74175_7_pin10), .pin9(and_4_out));  // open: pin3, pin6, pin14, pin11
  _74175 u_74175_8 (
    .pin1(not_8_out), .pin2(n74175_8_pin2), .pin4(controlled_buffer_5_out), .pin5(controlled_buffer_6_out),
    .pin7(n74175_8_pin7), .pin15(n74175_8_pin15), .pin13(controlled_buffer_8_out),
    .pin12(controlled_buffer_7_out), .pin11(n74175_8_pin11), .pin9(and_4_out));  // open: pin3, pin6, pin14, pin10
  LED led_25 (.in(n74175_6_pin2));
  LED led_26 (.in(n74175_6_pin7));
  LED led_27 (.in(not_9_out));
  not not_9 (not_9_out, n74175_6_pin11);
  LED led_28 (.in(n74175_8_pin2));
  LED led_29 (.in(n74175_8_pin7));
  LED led_30 (.in(not_10_out));
  not not_10 (not_10_out, n74175_8_pin11);
  LED led_31 (.in(n74175_6_pin15));
  LED led_32 (.in(n74175_8_pin15));
  not not_11 (not_11_out, ENABLE_2);
  not not_12 (not_12_out, ENABLE_4);
  _74245 u_74245_3 (
    .pin1(n74245_3_pin1), .pin2(n74175_5_pin2), .pin3(n74175_5_pin7), .pin4(n74175_5_pin10),
    .pin5(n74175_5_pin15), .pin6(n74175_6_pin2), .pin7(n74175_6_pin7), .pin8(not_9_out),
    .pin9(n74175_6_pin15), .pin19(not_11_out), .pin18(controlled_buffer_1_out),
    .pin17(controlled_buffer_2_out), .pin16(controlled_buffer_3_out), .pin15(controlled_buffer_4_out),
    .pin14(controlled_buffer_5_out), .pin13(controlled_buffer_6_out), .pin12(controlled_buffer_7_out),
    .pin11(controlled_buffer_8_out));
  _74245 u_74245_4 (
    .pin1(n74245_4_pin1), .pin2(n74175_7_pin2), .pin3(n74175_7_pin7), .pin4(n74175_7_pin10),
    .pin5(n74175_7_pin15), .pin6(n74175_8_pin2), .pin7(n74175_8_pin7), .pin8(not_10_out),
    .pin9(n74175_8_pin15), .pin19(not_12_out), .pin18(controlled_buffer_1_out),
    .pin17(controlled_buffer_2_out), .pin16(controlled_buffer_3_out), .pin15(controlled_buffer_4_out),
    .pin14(controlled_buffer_5_out), .pin13(controlled_buffer_6_out), .pin12(controlled_buffer_7_out),
    .pin11(controlled_buffer_8_out));
  // also tied to VCC on the sheet: {n74245_1_pin1, n74245_2_pin1, n74245_3_pin1, n74245_4_pin1}

  // Notes on the sheet:
  //   CHANNEL
  //   DATA
  //   Data Input Module
  //   Data Input Module
  //   MODCOM
  //   MODCOM
  //   Data Output Module
  //   Data Output Module
  //   Data Input Module
  //   Data Input Module
  //   MODCOM
  //   MODCOM
  //   Data Output Module
  //   Data Output Module
endmodule
